// Digital circuit Final_v2.0.dig as structural Verilog
module Final_v2_0 (
  input  start,
  input  reset,
  input  result,
  input  [7:0] M,
  input  [7:0] N,
  input  [12:0] progIN,
  input  progLoad,
  input  clk,
  output valid,
  output done,
  output [7:0] \output 
);

  wire _00000, _00001, _00010, _00011, _00100, _00101, _00110, _00111, _01000, _01001, _01010, _01011,
       _01100, _01101, _01110, _01111, _10000, _10001, _10010, _10011, _10100, _10101, _10110, _10111,
       _11000, _11001, _11010, _11011, _11100, _11101, _11110, _11111, and_2_out, and_3_out, and_4_out,
       and_5_out, Calculate, comparator_1_eq, comparator_1_gt, comparator_1_lt, Counter___Address,
       eq__eq__0x0F, equal_flag, Execute, FinalState, greater_flag, Initial_State, jump, lesser_flag,
       Load___accA, Load___accB, load___done, Load___flag, Load___regC, load___valid, multiplexer_4_out,
       multiplexer_8_out, multiplexer_9_out, multiplexer_10_out, not_2_out, not_3_out, not_4_out, not_5_out,
       not_6_out, or_2_out, or_3_out, Prime, PrintState, QA, QB, QC, Reset___Address, select___accB,
       select___pRam2Address, select___pRamAddress, select___rRamAddress, Transition, Waiting_State,
       WaitingResult;
  wire [1:0] select___regC;
  wire [3:0] Divide_r, select___accA;
  wire [4:0] opcode, pRam_d_2;
  wire [7:0] A___B, A___B_t, A___B_t_t, A___B_t_t_t, A___B_t_t_t_t, A__plus__B, A_and_B, A_or_B, A_shift_B,
       A_xor_B, accA, accB, add_2_s, Address, multiplexer_1_out, multiplexer_2_out, multiplexer_3_out,
       multiplexer_5_out, multiplexer_6_out, multiplexer_7_out, nA, operand, pRam, pRam_d, regC;
  wire [7:4] Divide_r_2;
  wire [12:8] pRam2_d;

  Add #(.Bits(8)) add_1 (.a(accA), .b(accB), .c_i(1'b0), .s(A__plus__B));  // open: c_o
  Sub #(.Bits(8)) sub_1 (.a(accA), .b(accB), .c_i(1'b0), .s(A___B_t_t));  // open: c_o
  Mul #(.Bits(4)) mul_1 (.a(accA[3:0]), .b(accB[3:0]), .mul(A___B_t));
  Div #(.Bits(8)) MainDivide (.a(accA), .b(accB), .q(A___B_t_t_t), .r(A___B));
  assign nA = ~accA;  // Not not_1, 8 bits wide
  assign A_and_B = accA & accB;  // And and_1, 8 bits wide
  assign A_or_B = accA | accB;  // Or or_1, 8 bits wide
  assign A_xor_B = accA ^ accB;  // XOr xor_1, 8 bits wide
  Div #(.Bits(8)) Divide (.a(accB), .b(8'h8), .r({Divide_r_2, Divide_r}));  // open: q
  Comparator #(.Signed("true"), .Bits(8)) comparator_1 (
    .a(accA), .b(accB), .gt(comparator_1_gt), .eq(comparator_1_eq), .lt(comparator_1_lt));
  LookUpTable #(.Bits(8)) lookuptable_1 (
    .in0(accB[0]), .in1(accB[1]), .in2(accB[2]), .in3(accA[0]), .in4(accA[1]), .in5(accA[2]),
    .out(A___B_t_t_t_t));
  LookUpTable lookuptable_2 (
    .in0(accA[0]), .in1(accA[1]), .in2(accA[2]), .in3(accA[3]), .in4(accA[4]), .in5(accA[5]), .in6(accA[6]),
    .in7(accA[7]), .out(Prime));
  BarrelShifter #(.Bits(8)) barrelshifter_1 (.in(accA), .shift(Divide_r), .out(A_shift_B));
  Multiplexer #(.Selector_Bits(4), .Bits(8)) multiplexer_1 (
    .sel(select___accA), .in_0(operand), .in_1(accB), .in_2(regC), .in_3(pRam), .in_4(\output ),
    .in_5(A__plus__B), .in_6(A___B_t_t), .in_7(A___B_t), .in_8(A___B_t_t_t), .in_9(A___B),
    .in_10(A___B_t_t_t_t), .in_11(nA), .in_12(A_and_B), .in_13(A_or_B), .in_14(A_xor_B), .in_15(A_shift_B),
    .out(multiplexer_1_out));
  Multiplexer #(.Bits(8)) multiplexer_2 (.sel(select___accB), .in_0(operand), .in_1(accA), .out(multiplexer_2_out));
  Multiplexer #(.Selector_Bits(2), .Bits(8)) multiplexer_3 (
    .sel(select___regC), .in_0(accA), .in_1(M), .in_2(N), .in_3(N), .out(multiplexer_3_out));
  Multiplexer multiplexer_4 (.sel(_11101), .in_0(comparator_1_eq), .in_1(Prime), .out(multiplexer_4_out));
  or or_2 (or_2_out, ~Initial_State, _11111, WaitingResult);  // Or
  or or_3 (or_3_out, ~Initial_State, FinalState);  // Or
  Register #(.Bits(8)) u_accA (.D(multiplexer_1_out), .C(clk), .en(Load___accA), .Q(accA));
  Register #(.Bits(8)) u_accB (.D(multiplexer_2_out), .C(clk), .en(Load___accB), .Q(accB));
  Register #(.Bits(8)) u_regC (.D(multiplexer_3_out), .C(clk), .en(Load___regC), .Q(regC));
  Register u_greater_flag (.D(comparator_1_gt), .C(clk), .en(Load___flag), .Q(greater_flag));
  Register u_equal_flag (.D(multiplexer_4_out), .C(clk), .en(Load___flag), .Q(equal_flag));
  Register u_lesser_flag (.D(comparator_1_lt), .C(clk), .en(Load___flag), .Q(lesser_flag));
  Register u_valid (.D(or_2_out), .C(clk), .en(load___valid), .Q(valid));
  Register u_done (.D(or_3_out), .C(clk), .en(load___done), .Q(done));
  Comparator #(.Bits(8)) u_eq__eq__0x0F (.a(Address), .b(8'hf), .eq(eq__eq__0x0F));  // open: gt, lt
  Multiplexer #(.Bits(8)) multiplexer_5 (
    .sel(select___pRamAddress), .in_0(Address), .in_1(operand), .out(multiplexer_5_out));
  Multiplexer #(.Bits(8)) multiplexer_6 (
    .sel(select___pRam2Address), .in_0(Address), .in_1(operand), .out(multiplexer_6_out));
  Multiplexer #(.Bits(8)) multiplexer_7 (
    .sel(select___rRamAddress), .in_0(Address), .in_1(operand), .out(multiplexer_7_out));
  Add #(.Bits(8)) add_2 (.a(operand), .b(8'h1), .c_i(1'b0), .s(add_2_s));  // open: c_o
  not not_2 (not_2_out, clk);
  not not_3 (not_3_out, clk);
  Seven_Seg_Hex seven_seg_hex_1 (.d(\output [3:0]), .dp(1'b0));
  RAMDualPort #(.AddrBits(8), .Bits(13)) u_pRam (
    .A(multiplexer_5_out), .Din(progIN), .str(progLoad), .C(not_2_out), .ld(1'b1), .D({pRam_d_2, pRam_d}));
  RAMDualPort #(.AddrBits(8), .Bits(13)) pRam2 (
    .A(multiplexer_6_out), .Din(progIN), .str(progLoad), .C(not_3_out), .ld(1'b1), .D({pRam2_d, pRam}));
  RAMDualPort #(.AddrBits(8), .Bits(8)) rRam (
    .A(multiplexer_7_out), .Din(accA), .str(_01011), .C(clk), .ld(1'b1), .D(\output ));
  CounterPreset #(.Bits(8)) AddressCount (
    .en(Counter___Address), .C(clk), .dir(1'b0), .in(add_2_s), .ld(jump), .clr(Reset___Address), .out(Address));  // open: ovf
  Seven_Seg_Hex seven_seg_hex_2 (.d(\output [7:4]), .dp(1'b0));
  Multiplexer #(.Selector_Bits(3)) multiplexer_8 (
    .sel({QA, QB, QC}), .in_0(1'b0), .in_1(1'b0), .in_2(1'b0), .in_3(valid), .in_4(1'b0), .in_5(1'b1),
    .in_6(1'b1), .in_7(1'b1), .out(multiplexer_8_out));
  Multiplexer #(.Selector_Bits(3)) multiplexer_9 (
    .sel({QA, QB, QC}), .in_0(1'b0), .in_1(start), .in_2(1'b1), .in_3(not_4_out), .in_4(1'b0), .in_5(result),
    .in_6(1'b1), .in_7(1'b1), .out(multiplexer_9_out));
  not not_4 (not_4_out, valid);
  Multiplexer #(.Selector_Bits(3)) multiplexer_10 (
    .sel({QA, QB, QC}), .in_0(1'b1), .in_1(not_5_out), .in_2(1'b1), .in_3(1'b1), .in_4(1'b0),
    .in_5(not_6_out), .in_6(eq__eq__0x0F), .in_7(1'b1), .out(multiplexer_10_out));
  not not_5 (not_5_out, start);
  not not_6 (not_6_out, result);
  Register #(.Bits(5)) u_Opcode (.D(pRam_d_2), .C(clk), .en(Execute), .Q(opcode));
  Register #(.Bits(8)) u_Operand (.D(pRam_d), .C(clk), .en(Execute), .Q(operand));
  D_FF_AS d_ff_as_1 (.Set(1'b0), .D(multiplexer_8_out), .C(clk), .Clr(reset), .Q(QA));  // open: nQ
  D_FF_AS d_ff_as_2 (.Set(1'b0), .D(multiplexer_9_out), .C(clk), .Clr(reset), .Q(QB));  // open: nQ
  D_FF_AS d_ff_as_3 (.Set(1'b0), .D(multiplexer_10_out), .C(clk), .Clr(reset), .Q(QC));  // open: nQ
  Demultiplexer #(.Selector_Bits(3)) demultiplexer_1 (
    .sel({QA, QB, QC}), .in(1'b1), .out_0(Initial_State), .out_1(Waiting_State), .out_2(Transition),
    .out_3(Execute), .out_4(Calculate), .out_5(WaitingResult), .out_6(PrintState), .out_7(FinalState));
  Demultiplexer #(.Selector_Bits(5)) demultiplexer_2 (
    .sel(opcode), .in(1'b1), .out_0(_00000), .out_1(_00001), .out_2(_00010), .out_3(_00011), .out_4(_00100),
    .out_5(_00101), .out_6(_00110), .out_7(_00111), .out_8(_01000), .out_9(_01001), .out_10(_01010),
    .out_11(_01011), .out_12(_01100), .out_13(_01101), .out_14(_01110), .out_15(_01111), .out_16(_10000),
    .out_17(_10001), .out_18(_10010), .out_19(_10011), .out_20(_10100), .out_21(_10101), .out_22(_10110),
    .out_23(_10111), .out_24(_11000), .out_25(_11001), .out_26(_11010), .out_27(_11011), .out_28(_11100),
    .out_29(_11101), .out_30(_11110), .out_31(_11111));
  LookUpTable #(.Bits(4)) lookuptable_3 (
    .in0(opcode[0]), .in1(opcode[1]), .in2(opcode[2]), .in3(opcode[3]), .in4(opcode[4]), .out(select___accA));
  LookUpTable lookuptable_4 (
    .in0(opcode[0]), .in1(opcode[1]), .in2(opcode[2]), .in3(opcode[3]), .in4(opcode[4]), .out(select___accB));
  LookUpTable #(.Bits(2)) lookuptable_5 (
    .in0(opcode[0]), .in1(opcode[1]), .in2(opcode[2]), .in3(opcode[3]), .in4(opcode[4]), .out(select___regC));
  LookUpTable u_select___pRamAddress (.in0(QC), .in1(QB), .in2(QA), .in3(jump), .out(select___pRamAddress));
  LookUpTable u_select___pRam2Address (.in0(QC), .in1(QB), .in2(QA), .in3(_01001), .out(select___pRam2Address));
  LookUpTable u_select___rRamAddress (.in0(QC), .in1(QB), .in2(QA), .in3(_01011), .out(select___rRamAddress));
  or or_4 (Counter___Address, progLoad, Execute, PrintState);
  or or_5 (Reset___Address, Initial_State, Transition, WaitingResult, reset);
  or or_6 (load___valid, Initial_State, _11111, WaitingResult);
  or or_7 (load___done, Initial_State, eq__eq__0x0F, FinalState);
  or or_8 (Load___accA, _00001, _00011, _00110, _01001, _01010, _10001, _10010, _10011, _10100, _10101, _10110, _11000, _11001, _11010, _11011, _11100);
  or or_9 (Load___accB, _00010, _00100);
  or or_10 (Load___regC, _00101, _00111, _01000);
  or or_11 (Load___flag, _10111, _11101);
  and and_2 (and_2_out, _01101, equal_flag);
  and and_3 (and_3_out, _01110, greater_flag);
  and and_4 (and_4_out, _01111, lesser_flag);
  and and_5 (and_5_out, _10000, ~lesser_flag);  // And
  or or_12 (jump, _01100, and_2_out, and_3_out, and_4_out, and_5_out);

  // Other names for the same wires on the sheet: Load___rRam = _01011; _1[3:0] = \output [3:0]; rRam[7:0] = \output ;
  //   _2[3:0] = \output [7:4]

  // Notes on the sheet:
  //   Execute
  //   contents of lookuptable_1 (hex, n*v repeats v):
  //   0,0,e00000,5*0,9*1,2,4,8,10,20,40,80,1,3,9,1b,51,f3,0,0,1,4,10
  //   ,40,100,0,0,0,1,5,19,7d,4*0,1,6,24,d8,4*0,1,7,31,8*0,1,0,0,0,1
  //   ,0,1,5*0,1,0,0,0,1,5*0,1,7*0,1,0,0,0,1,0,1,0,0,0,1,0,1,0,0,0,1
  //   ,13*0,1,0,0,0,1,5*0,1,0,1,9*0,1,0,1,5*0,1,5*0,1,0,0,0,1,5*0,1
  //   ,5*0,1,0,1,9*0,1,0,1,0,0,0,1,0,1,11*0,1,11*0,1,0,0,0,1,0,1,0,0,0
  //   ,1,5*0,1,0,1,9*0,1
  //   contents of lookuptable_2 (hex, n*v repeats v):
  //   0,0,1,1,0,1,0,1,0,0,0,1,0,1,0,0,0,1,0,1,0,0,0,1,5*0,1,0,1,5*0
  //   ,1,0,0,0,1,0,1,0,0,0,1,5*0,1,5*0,1,0,1,5*0,1,0,0,0,1,0,1,5*0,1
  //   ,0,0,0,1,5*0,1,7*0,1,0,0,0,1,0,1,0,0,0,1,0,1,0,0,0,1,13*0,1,0,0,0
  //   ,1,5*0,1,0,1,9*0,1,0,1,5*0,1,5*0,1,0,0,0,1,5*0,1,5*0,1,0,1,9*0
  //   ,1,0,1,0,0,0,1,0,1,11*0,1,11*0,1,0,0,0,1,0,1,0,0,0,1,5*0,1,0,1
  //   ,9*0,1
  //   Input / output
  //   Address Management
  //   MainStateTransition
  //   ControlUnit
  //   contents of lookuptable_3 (hex, n*v repeats v):
  //   0,0,0,1,0,0,2,0,0,3,4,6*0,5,6,7,8,9,a,0,b,c,d,e,f
  //   contents of lookuptable_4 (hex, n*v repeats v):
  //   4*0,1
  //   contents of lookuptable_5 (hex, n*v repeats v):
  //   7*0,1,2
  //   contents of select___pRamAddress (hex, n*v repeats v):
  //   8*0,8*1
  //   contents of select___pRam2Address (hex, n*v repeats v):
  //   8*0,8*1
  //   contents of select___rRamAddress (hex, n*v repeats v):
  //   7*0,9*1
endmodule

/* Test case 01_P01T01:
M N progIN reset progLoad start result clk valid done output
0 0 0 0 0 0 0 0 0 0 0
0 0 0 0 0 0 0 1 0 0 0
0 0 0 1 0 0 0 0 0 0 0
0 0 0 1 0 0 0 1 0 0 0
0 0 0 0 0 0 0 0 0 0 0
0 0 0 0 0 0 0 1 0 0 0
0 0 0 0 0 0 0 0 0 0 0
0 0 0 0 0 0 0 1 0 0 0
0 0 0 0 0 0 0 0 0 0 0
0 0 0 0 0 0 0 1 0 0 0
0 0 0 0 0 0 0 0 0 0 0
0 0 0 0 0 0 0 1 0 0 0
0 0 0 0 0 0 0 0 0 0 0
0 0 0 0 0 0 0 1 0 0 0
0 0 0 0 0 0 0 0 0 0 0
0 0 0 0 0 0 0 1 0 0 0
0 0 0 0 0 0 0 0 0 0 0
0 0 0 0 0 0 0 1 0 0 0
0 0 0 0 0 0 0 0 0 0 0
0 0 0 0 0 0 0 1 0 0 0
0 0 0 0 0 0 0 0 0 0 0
0 0 0 0 0 0 0 1 0 0 0
0 0 0 0 0 0 0 0 0 0 0
0 0 0 0 0 0 0 1 0 0 0
0 0 0 0 0 0 0 0 0 0 0
0 0 0 0 0 0 0 1 0 0 0
0 0 0 0 0 0 0 0 0 0 0
0 0 0 0 0 0 0 1 0 0 0
0 0 0 0 0 0 0 0 0 0 0
0 0 0 0 0 0 0 1 0 0 0
0 0 0 0 0 0 0 0 0 0 0
0 0 0 0 0 0 0 1 0 0 0
0 0 0 0 0 0 0 0 0 0 0
0 0 0 0 0 0 0 1 0 0 0
0 0 0 0 0 0 0 0 0 0 0
0 0 0 0 0 0 0 1 0 0 0
0 0 0 0 0 0 0 0 0 0 0
0 0 0 0 0 0 0 1 0 0 0
0 0 0 0 0 0 0 0 0 0 0
0 0 0 0 0 0 0 1 0 0 0
0 0 0 0 0 0 0 0 0 0 0
0 0 0 0 0 0 0 1 0 0 0
0 0 271 0 1 0 0 0 0 0 0
0 0 0 0 1 0 0 1 0 0 0
0 0 565 0 1 0 0 0 0 0 0
0 0 0 0 1 0 0 1 0 0 0
0 0 4352 0 1 0 0 0 0 0 0
0 0 0 0 1 0 0 1 0 0 0
0 0 2819 0 1 0 0 0 0 0 0
0 0 0 0 1 0 0 1 0 0 0
0 0 7936 0 1 0 0 0 0 0 0
0 0 0 0 1 0 0 1 0 0 0
0 0 0 0 0 1 0 0 0 0 0
0 0 0 0 0 1 0 1 0 0 0
0 0 0 0 0 0 0 0 x 0 0
0 0 0 0 0 0 0 1 x 0 0
0 0 0 0 0 0 0 0 x 0 0
0 0 0 0 0 0 0 1 x 0 0
0 0 0 0 0 0 0 0 x 0 0
0 0 0 0 0 0 0 1 x 0 0
0 0 0 0 0 0 0 0 x 0 0
0 0 0 0 0 0 0 1 x 0 0
0 0 0 0 0 0 0 0 x 0 0
0 0 0 0 0 0 0 1 x 0 0
0 0 0 0 0 0 0 0 x 0 0
0 0 0 0 0 0 0 1 x 0 0
0 0 0 0 0 0 0 0 x 0 0
0 0 0 0 0 0 0 1 x 0 0
0 0 0 0 0 0 0 0 x 0 0
0 0 0 0 0 0 0 1 x 0 0
0 0 0 0 0 0 0 0 x 0 0
0 0 0 0 0 0 0 1 x 0 0
0 0 0 0 0 0 0 0 x 0 0
0 0 0 0 0 0 0 1 x 0 0
0 0 0 0 0 0 0 0 x 0 0
0 0 0 0 0 0 0 1 x 0 0
0 0 0 0 0 0 0 0 x 0 0
0 0 0 0 0 0 0 1 x 0 0
0 0 0 0 0 0 0 0 x 0 0
0 0 0 0 0 0 0 1 x 0 0
0 0 0 0 0 0 0 0 x 0 0
0 0 0 0 0 0 0 1 x 0 0
0 0 0 0 0 0 0 0 x 0 0
0 0 0 0 0 0 0 1 x 0 0
0 0 0 0 0 0 0 0 x 0 0
0 0 0 0 0 0 0 1 x 0 0
0 0 0 0 0 0 0 0 x 0 0
0 0 0 0 0 0 0 1 x 0 0
0 0 0 0 0 0 0 0 x 0 0
0 0 0 0 0 0 0 1 x 0 0
0 0 0 0 0 0 0 0 x 0 0
0 0 0 0 0 0 0 1 x 0 0
0 0 0 0 0 0 0 0 x 0 0
0 0 0 0 0 0 0 1 x 0 0
0 0 0 0 0 0 0 0 x 0 0
0 0 0 0 0 0 0 1 x 0 0
0 0 0 0 0 0 0 0 x 0 0
0 0 0 0 0 0 0 1 x 0 0
0 0 0 0 0 0 0 0 x 0 0
0 0 0 0 0 0 0 1 x 0 0
0 0 0 0 0 0 0 0 x 0 0
0 0 0 0 0 0 0 1 x 0 0
0 0 0 0 0 0 0 0 x 0 0
0 0 0 0 0 0 0 1 x 0 0
0 0 0 0 0 0 0 0 x 0 0
0 0 0 0 0 0 0 1 1 0 0
0 0 0 0 0 0 1 0 1 0 0
0 0 0 0 0 0 1 1 1 0 0
0 0 0 0 0 0 0 0 1 0 0
0 0 0 0 0 0 0 1 1 0 0
0 0 0 0 0 0 0 0 1 0 0
0 0 0 0 0 0 0 1 1 0 0
0 0 0 0 0 0 0 0 1 0 0
0 0 0 0 0 0 0 1 1 0 68
0 0 0 0 0 0 0 0 1 0 68
0 0 0 0 0 0 0 1 1 0 0
0 0 0 0 0 0 0 0 1 0 0
0 0 0 0 0 0 0 1 1 0 0
0 0 0 0 0 0 0 0 1 0 0
0 0 0 0 0 0 0 1 1 0 0
0 0 0 0 0 0 0 0 1 0 0
0 0 0 0 0 0 0 1 1 0 0
0 0 0 0 0 0 0 0 1 0 0
0 0 0 0 0 0 0 1 1 0 0
0 0 0 0 0 0 0 0 1 0 0
0 0 0 0 0 0 0 1 1 0 0
0 0 0 0 0 0 0 0 1 0 0
0 0 0 0 0 0 0 1 1 0 0
0 0 0 0 0 0 0 0 1 0 0
0 0 0 0 0 0 0 1 1 0 0
0 0 0 0 0 0 0 0 1 0 0
0 0 0 0 0 0 0 1 1 0 0
0 0 0 0 0 0 0 0 1 0 0
0 0 0 0 0 0 0 1 1 0 0
0 0 0 0 0 0 0 0 1 0 0
0 0 0 0 0 0 0 1 1 0 0
0 0 0 0 0 0 0 0 1 0 0
0 0 0 0 0 0 0 1 1 0 0
0 0 0 0 0 0 0 0 1 0 0
0 0 0 0 0 0 0 1 1 1 0
0 0 0 0 0 0 0 0 1 1 0
0 0 0 0 0 0 0 1 1 1 0
0 0 0 0 0 0 0 0 1 1 0
*/
