// Digital circuit Final_v4.0.dig as structural Verilog
module Final_v4_0 (
  input  start,
  input  reset,
  input  result,
  input  [7:0] M,
  input  [7:0] N,
  input  [12:0] progIN,
  input  progLoad,
  input  clk,
  output valid,
  output done,
  output [7:0] \output ,
  output [7:0] out_12,
  output [7:0] out_13
);

  wire _00000, _00001, _00010, _00011, _00100, _00101, _00110, _00111, _01000, _01001, _01010, _01011,
       _01100, _01101, _01110, _01111, _10000, _10001, _10010, _10011, _10100, _10101, _10110, _10111,
       _11000, _11001, _11010, _11011, _11100, _11101, _11110, _11111, and_3_out, and_4_out, and_5_out,
       and_6_out, ClearState, comparator_1_eq, comparator_1_gt, comparator_1_lt, Counter___Address,
       d_ff_1_nq, eq__eq__0x0F, equal_flag, Execute, FinalState, Get____Not_Get, greater_flag, Initial_State,
       jump, lesser_flag, Load___accA, Load___accB, load___done, Load___equal, Load___flag, Load___regC,
       Load___rRam, load___valid, multiplexer_4_out, multiplexer_5_out, multiplexer_6_out,
       multiplexer_10_out, multiplexer_11_out, multiplexer_12_out, not_2_out, not_3_out, not_4_out,
       not_5_out, not_6_out, not_7_out, or_2_out, or_3_out, or_4_out, or_5_out, or_6_out, or_7_out, or_8_out,
       or_18_out, Prime, PrintState, QA, QB, QC, Reset___Address, select___accB, select___pRamAddress,
       select___rRamAddress, Transition, Waiting_State, WaitingResult;
  wire [1:0] select___equal_flag, select___regC;
  wire [3:0] select___accA;
  wire [4:0] multiplexer_9_out, opcode, pRam_d;
  wire [7:0] A___B, A___B_t, A___B_t_t, A___B_t_t_t, A___B_t_t_t_t, A__plus__B, A_and_B, A_or_B, A_shift_B,
       A_xor_B, add_2_s, Address, multiplexer_1_out, multiplexer_2_out, multiplexer_3_out, multiplexer_7_out,
       multiplexer_8_out, nA, operand, pRam, regC, rRam, value___rRam;

  Add #(.Bits(8)) add_1 (.a(out_12), .b(out_13), .c_i(1'b0), .s(A__plus__B));  // open: c_o
  Sub #(.Bits(8)) sub_1 (.a(out_12), .b(out_13), .c_i(1'b0), .s(A___B_t_t));  // open: c_o
  Mul #(.Bits(4)) mul_1 (.a(out_12[3:0]), .b(out_13[3:0]), .mul(A___B_t));
  Div #(.Bits(8)) MainDivide (.a(out_12), .b(out_13), .q(A___B_t_t_t), .r(A___B));
  assign nA = ~out_12;  // Not not_1, 8 bits wide
  assign A_and_B = out_12 & out_13;  // And and_1, 8 bits wide
  assign A_or_B = out_12 | out_13;  // Or or_1, 8 bits wide
  assign A_xor_B = out_12 ^ out_13;  // XOr xor_1, 8 bits wide
  Comparator #(.Signed("true"), .Bits(8)) comparator_1 (
    .a(out_12), .b(out_13), .gt(comparator_1_gt), .eq(comparator_1_eq), .lt(comparator_1_lt));
  LookUpTable #(.Bits(8)) lookuptable_1 (
    .in0(out_13[0]), .in1(out_13[1]), .in2(out_13[2]), .in3(out_12[0]), .in4(out_12[1]), .in5(out_12[2]),
    .out(A___B_t_t_t_t));
  LookUpTable lookuptable_2 (
    .in0(out_12[0]), .in1(out_12[1]), .in2(out_12[2]), .in3(out_12[3]), .in4(out_12[4]), .in5(out_12[5]),
    .in6(out_12[6]), .in7(out_12[7]), .out(Prime));
  BarrelShifter #(.Bits(8)) barrelshifter_1 (.in(out_12), .shift({1'b0, out_13[2:0]}), .out(A_shift_B));
  Multiplexer #(.Selector_Bits(4), .Bits(8)) multiplexer_1 (
    .sel(select___accA), .in_0(operand), .in_1(out_13), .in_2(regC), .in_3(pRam), .in_4(rRam),
    .in_5(A__plus__B), .in_6(A___B_t_t), .in_7(A___B_t), .in_8(A___B_t_t_t), .in_9(A___B),
    .in_10(A___B_t_t_t_t), .in_11(nA), .in_12(A_and_B), .in_13(A_or_B), .in_14(A_xor_B), .in_15(A_shift_B),
    .out(multiplexer_1_out));
  Multiplexer #(.Bits(8)) multiplexer_2 (.sel(select___accB), .in_0(operand), .in_1(out_12), .out(multiplexer_2_out));
  Multiplexer #(.Selector_Bits(2), .Bits(8)) multiplexer_3 (
    .sel(select___regC), .in_0(out_12), .in_1(M), .in_2(N), .in_3(N), .out(multiplexer_3_out));
  Multiplexer multiplexer_4 (.sel(Initial_State), .in_0(comparator_1_gt), .in_1(1'b0), .out(multiplexer_4_out));
  Multiplexer #(.Selector_Bits(2)) multiplexer_5 (
    .sel(select___equal_flag), .in_0(comparator_1_eq), .in_1(1'b0), .in_2(Prime), .in_3(1'b0),
    .out(multiplexer_5_out));
  Multiplexer multiplexer_6 (.sel(Initial_State), .in_0(comparator_1_lt), .in_1(1'b0), .out(multiplexer_6_out));
  or or_2 (or_2_out, ~Initial_State, _11111, WaitingResult);  // Or
  or or_3 (or_3_out, PrintState, FinalState);
  Register #(.Bits(8)) accA (.D(multiplexer_1_out), .C(clk), .en(Load___accA), .Q(out_12));
  Register #(.Bits(8)) accB (.D(multiplexer_2_out), .C(clk), .en(Load___accB), .Q(out_13));
  Register #(.Bits(8)) u_regC (.D(multiplexer_3_out), .C(clk), .en(Load___regC), .Q(regC));
  Register u_greater_flag (.D(multiplexer_4_out), .C(clk), .en(Load___flag), .Q(greater_flag));
  Register u_equal_flag (.D(multiplexer_5_out), .C(clk), .en(Load___equal), .Q(equal_flag));
  Register u_lesser_flag (.D(multiplexer_6_out), .C(clk), .en(Load___flag), .Q(lesser_flag));
  Register u_valid (.D(or_2_out), .C(clk), .en(load___valid), .Q(valid));
  Register u_done (.D(or_3_out), .C(clk), .en(load___done), .Q(done));
  Comparator #(.Bits(8)) u_eq__eq__0x0F (.a(Address), .b(8'hf), .eq(eq__eq__0x0F));  // open: gt, lt
  Multiplexer #(.Bits(8)) multiplexer_7 (
    .sel(select___pRamAddress), .in_0(Address), .in_1(operand), .out(multiplexer_7_out));
  Multiplexer #(.Bits(8)) multiplexer_8 (
    .sel(select___rRamAddress), .in_0(Address), .in_1(operand), .out(multiplexer_8_out));
  Add #(.Bits(8)) add_2 (.a(operand), .b(8'h1), .c_i(1'b0), .s(add_2_s));  // open: c_o
  or or_4 (or_4_out, ~eq__eq__0x0F, start);  // Or
  or or_5 (or_5_out, ~start, result);  // Or
  not not_2 (not_2_out, clk);
  RAMDualPort #(.AddrBits(8), .Bits(13)) u_pRam (
    .A(multiplexer_7_out), .Din(progIN), .str(progLoad), .C(not_2_out), .ld(1'b1), .D({pRam_d, pRam}));
  RAMDualPort #(.AddrBits(8), .Bits(8)) u_rRam (
    .A(multiplexer_8_out), .Din(value___rRam), .str(Load___rRam), .C(clk), .ld(1'b1), .D(rRam));
  CounterPreset #(.Bits(8)) AddressCount (
    .en(Counter___Address), .C(clk), .dir(1'b0), .in(add_2_s), .ld(jump), .clr(Reset___Address), .out(Address));  // open: ovf
  Seven_Seg_Hex seven_seg_hex_1 (.d(\output [3:0]), .dp(1'b0));
  not not_3 (not_3_out, eq__eq__0x0F);
  not not_4 (not_4_out, valid);
  not not_5 (not_5_out, valid);
  not not_6 (not_6_out, eq__eq__0x0F);
  not not_7 (not_7_out, eq__eq__0x0F);
  Seven_Seg_Hex seven_seg_hex_2 (.d(\output [7:4]), .dp(1'b0));
  Multiplexer #(.Bits(5)) multiplexer_9 (
    .sel(Get____Not_Get), .in_0(pRam_d), .in_1({5{1'b0}}), .out(multiplexer_9_out));
  Multiplexer #(.Selector_Bits(3)) multiplexer_10 (
    .sel({QA, QB, QC}), .in_0(1'b0), .in_1(result), .in_2(1'b0), .in_3(valid), .in_4(1'b1), .in_5(1'b1),
    .in_6(1'b0), .in_7(not_3_out), .out(multiplexer_10_out));
  Multiplexer #(.Selector_Bits(3)) multiplexer_11 (
    .sel({QA, QB, QC}), .in_0(1'b0), .in_1(start), .in_2(1'b1), .in_3(not_4_out), .in_4(1'b0),
    .in_5(eq__eq__0x0F), .in_6(1'b0), .in_7(or_4_out), .out(multiplexer_11_out));
  Multiplexer #(.Selector_Bits(3)) multiplexer_12 (
    .sel({QA, QB, QC}), .in_0(1'b1), .in_1(or_5_out), .in_2(1'b1), .in_3(not_5_out), .in_4(result),
    .in_5(not_6_out), .in_6(1'b1), .in_7(not_7_out), .out(multiplexer_12_out));
  Register #(.Bits(5)) u_Opcode (.D(multiplexer_9_out), .C(clk), .en(Execute), .Q(opcode));
  Register #(.Bits(8)) u_Operand (.D(pRam), .C(clk), .en(Execute), .Q(operand));
  Multiplexer #(.Bits(8)) multiplexer_13 (.sel(PrintState), .in_0({8{1'b0}}), .in_1(rRam), .out(\output ));
  D_FF_AS d_ff_as_1 (.Set(reset), .D(multiplexer_10_out), .C(clk), .Clr(1'b0), .Q(QA));  // open: nQ
  D_FF_AS d_ff_as_2 (.Set(reset), .D(multiplexer_11_out), .C(clk), .Clr(1'b0), .Q(QB));  // open: nQ
  D_FF_AS d_ff_as_3 (.Set(reset), .D(multiplexer_12_out), .C(clk), .Clr(1'b0), .Q(QC));  // open: nQ
  Demultiplexer #(.Selector_Bits(3)) demultiplexer_1 (
    .sel({QA, QB, QC}), .in(1'b1), .out_0(Initial_State), .out_1(Waiting_State), .out_2(Transition),
    .out_3(Execute), .out_4(WaitingResult), .out_5(PrintState), .out_6(FinalState), .out_7(ClearState));
  Demultiplexer #(.Selector_Bits(5)) demultiplexer_2 (
    .sel(opcode), .in(1'b1), .out_0(_00000), .out_1(_00001), .out_2(_00010), .out_3(_00011), .out_4(_00100),
    .out_5(_00101), .out_6(_00110), .out_7(_00111), .out_8(_01000), .out_9(_01001), .out_10(_01010),
    .out_11(_01011), .out_12(_01100), .out_13(_01101), .out_14(_01110), .out_15(_01111), .out_16(_10000),
    .out_17(_10001), .out_18(_10010), .out_19(_10011), .out_20(_10100), .out_21(_10101), .out_22(_10110),
    .out_23(_10111), .out_24(_11000), .out_25(_11001), .out_26(_11010), .out_27(_11011), .out_28(_11100),
    .out_29(_11101), .out_30(_11110), .out_31(_11111));
  or or_6 (or_6_out, jump, Get____Not_Get);
  or or_7 (or_7_out, _01010, _01011);
  LookUpTable u_select___pRamAddress (.in0(QC), .in1(QB), .in2(QA), .in3(or_6_out), .out(select___pRamAddress));
  LookUpTable u_select___rRamAddress (.in0(QC), .in1(QB), .in2(QA), .in3(or_7_out), .out(select___rRamAddress));
  LookUpTable #(.Bits(4)) lookuptable_3 (
    .in0(opcode[0]), .in1(opcode[1]), .in2(opcode[2]), .in3(opcode[3]), .in4(opcode[4]), .out(select___accA));
  LookUpTable lookuptable_4 (
    .in0(opcode[0]), .in1(opcode[1]), .in2(opcode[2]), .in3(opcode[3]), .in4(opcode[4]), .out(select___accB));
  LookUpTable #(.Bits(2)) lookuptable_5 (
    .in0(opcode[0]), .in1(opcode[1]), .in2(opcode[2]), .in3(opcode[3]), .in4(opcode[4]), .out(select___regC));
  or or_8 (or_8_out, ClearState, progLoad, Execute, PrintState);
  or or_9 (Reset___Address, Initial_State, Transition, WaitingResult, FinalState, reset);
  or or_10 (load___valid, Initial_State, _11111, WaitingResult);
  or or_11 (Load___accA, _00001, _00011, _00110, _01001, _01010, _10001, _10010, _10011, Initial_State, _10100, _10101, _10110, _11000, _11001, _11010, _11011, _11100);
  or or_12 (Load___accB, Initial_State, _00010, _00100);
  or or_13 (Load___regC, Initial_State, _00101, _00111, _01000);
  or or_14 (Load___flag, Initial_State, _10111);
  or or_15 (Load___equal, Initial_State, _10111, _11101);
  LookUpTable #(.Bits(2)) lookuptable_6 (.in0(Initial_State), .in1(_11101), .out(select___equal_flag));
  or or_16 (Load___rRam, ClearState, _01011);
  and and_2 (Counter___Address, or_8_out, ~jump, ~Get____Not_Get);  // And
  or or_17 (load___done, eq__eq__0x0F, FinalState, Initial_State);
  or or_18 (or_18_out, greater_flag, equal_flag);
  D_FF d_ff_1 (.D(_01001), .C(clk), .nQ(d_ff_1_nq));  // open: Q
  Multiplexer #(.Bits(8)) multiplexer_14 (.sel(ClearState), .in_0(out_12), .in_1({8{1'b0}}), .out(value___rRam));
  and and_3 (and_3_out, _01101, equal_flag);
  and and_4 (and_4_out, _01110, greater_flag);
  and and_5 (and_5_out, _01111, lesser_flag);
  and and_6 (and_6_out, _10000, or_18_out);
  and and_7 (Get____Not_Get, d_ff_1_nq, _01001);
  or or_19 (jump, and_3_out, and_4_out, _01100, and_5_out, and_6_out);

  // Other names for the same wires on the sheet: accA[7:0] = out_12; accB[7:0] = out_13; _1[3:0] = \output [3:0];
  //   out[7:0] = \output ; _2[3:0] = \output [7:4]

  // Notes on the sheet:
  //   Execute
  //   contents of lookuptable_1 (hex, n*v repeats v):
  //   0,0,e00000,5*0,9*1,2,4,8,10,20,40,80,1,3,9,1b,51,f3,0,0,1,4,10
  //   ,40,100,0,0,0,1,5,19,7d,4*0,1,6,24,d8,4*0,1,7,31,8*0,1,0,0,0,1
  //   ,0,1,5*0,1,0,0,0,1,5*0,1,7*0,1,0,0,0,1,0,1,0,0,0,1,0,1,0,0,0,1
  //   ,13*0,1,0,0,0,1,5*0,1,0,1,9*0,1,0,1,5*0,1,5*0,1,0,0,0,1,5*0,1
  //   ,5*0,1,0,1,9*0,1,0,1,0,0,0,1,0,1,11*0,1,11*0,1,0,0,0,1,0,1,0,0,0
  //   ,1,5*0,1,0,1,9*0,1
  //   contents of lookuptable_2 (hex, n*v repeats v):
  //   0,0,1,1,0,1,0,1,0,0,0,1,0,1,0,0,0,1,0,1,0,0,0,1,5*0,1,0,1,5*0
  //   ,1,0,0,0,1,0,1,0,0,0,1,5*0,1,5*0,1,0,1,5*0,1,0,0,0,1,0,1,5*0,1
  //   ,0,0,0,1,5*0,1,7*0,1,0,0,0,1,0,1,0,0,0,1,0,1,0,0,0,1,13*0,1,0,0,0
  //   ,1,5*0,1,0,1,9*0,1,0,1,5*0,1,5*0,1,0,0,0,1,5*0,1,5*0,1,0,1,9*0
  //   ,1,0,1,0,0,0,1,0,1,11*0,1,11*0,1,0,0,0,1,0,1,0,0,0,1,5*0,1,0,1
  //   ,9*0,1
  //   Input / output
  //   Address Management
  //   StateTransition
  //   Member
  //   673 30892 21 
  //   ธนกฤต แสงปานแก้ว
  //   673 31732 21 
  //   พัทธพล สุรินทร์วรางกูร
  //   673 32573 21
  //   ศิวกร แก้วสอาด
  //   ControlUnit
  //   contents of select___pRamAddress (hex, n*v repeats v):
  //   8*0,8*1
  //   contents of select___rRamAddress (hex, n*v repeats v):
  //   8*0,8*1
  //   contents of lookuptable_3 (hex, n*v repeats v):
  //   0,0,0,1,0,0,2,0,0,3,4,6*0,5,6,7,8,9,a,0,b,c,d,e,f
  //   contents of lookuptable_4 (hex, n*v repeats v):
  //   4*0,1
  //   contents of lookuptable_5 (hex, n*v repeats v):
  //   7*0,1,2
  //   contents of lookuptable_6 (hex, n*v repeats v):
  //   0,1,2
endmodule

/* Test case 01_P01T01:
M N progIN reset progLoad start result clk valid done output	
0 0 0 0 0 0 0 0 0 0 0	
0 0 0 0 0 0 0 1 0 0 0	
0 0 0 1 0 0 0 0 0 0 0	
0 0 0 1 0 0 0 1 0 0 0	
0 0 0 0 0 0 0 0 0 0 0	
0 0 0 0 0 0 0 1 0 0 0	
0 0 0 0 0 0 0 0 0 0 0	
0 0 0 0 0 0 0 1 0 0 0	
0 0 0 0 0 0 0 0 0 0 0	
0 0 0 0 0 0 0 1 0 0 0	
0 0 0 0 0 0 0 0 0 0 0	
0 0 0 0 0 0 0 1 0 0 0	
0 0 0 0 0 0 0 0 0 0 0	
0 0 0 0 0 0 0 1 0 0 0	
0 0 0 0 0 0 0 0 0 0 0	
0 0 0 0 0 0 0 1 0 0 0	
0 0 0 0 0 0 0 0 0 0 0	
0 0 0 0 0 0 0 1 0 0 0	
0 0 0 0 0 0 0 0 0 0 0	
0 0 0 0 0 0 0 1 0 0 0	
0 0 0 0 0 0 0 0 0 0 0	
0 0 0 0 0 0 0 1 0 0 0	
0 0 0 0 0 0 0 0 0 0 0	
0 0 0 0 0 0 0 1 0 0 0	
0 0 0 0 0 0 0 0 0 0 0	
0 0 0 0 0 0 0 1 0 0 0	
0 0 0 0 0 0 0 0 0 0 0	
0 0 0 0 0 0 0 1 0 0 0	
0 0 0 0 0 0 0 0 0 0 0	
0 0 0 0 0 0 0 1 0 0 0	
0 0 0 0 0 0 0 0 0 0 0	
0 0 0 0 0 0 0 1 0 0 0	
0 0 0 0 0 0 0 0 0 0 0	
0 0 0 0 0 0 0 1 0 0 0	
0 0 0 0 0 0 0 0 0 0 0	
0 0 0 0 0 0 0 1 0 0 0	
0 0 0 0 0 0 0 0 0 0 0	
0 0 0 0 0 0 0 1 0 0 0	
0 0 0 0 0 0 0 0 0 0 0	
0 0 0 0 0 0 0 1 0 0 0	
0 0 0 0 0 0 0 0 0 0 0	
0 0 0 0 0 0 0 1 0 0 0	
0 0 271 0 1 0 0 0 0 0 0	
0 0 271 0 1 0 0 1 0 0 0	
0 0 565 0 1 0 0 0 0 0 0	
0 0 565 0 1 0 0 1 0 0 0	
0 0 4352 0 1 0 0 0 0 0 0	
0 0 4352 0 1 0 0 1 0 0 0	
0 0 2819 0 1 0 0 0 0 0 0	
0 0 2819 0 1 0 0 1 0 0 0	
0 0 7936 0 1 0 0 0 0 0 0	
0 0 7936 0 1 0 0 1 0 0 0	
0 0 0 0 0 1 0 0 0 0 0	
0 0 0 0 0 1 0 1 0 0 0	
0 0 0 0 0 0 0 0 x 0 0	
0 0 0 0 0 0 0 1 x 0 0	
0 0 0 0 0 0 0 0 x 0 0	
0 0 0 0 0 0 0 1 x 0 0	
0 0 0 0 0 0 0 0 x 0 0	
0 0 0 0 0 0 0 1 x 0 0	
0 0 0 0 0 0 0 0 x 0 0	
0 0 0 0 0 0 0 1 x 0 0	
0 0 0 0 0 0 0 0 x 0 0	
0 0 0 0 0 0 0 1 x 0 0	
0 0 0 0 0 0 0 0 x 0 0	
0 0 0 0 0 0 0 1 x 0 0	
0 0 0 0 0 0 0 0 x 0 0	
0 0 0 0 0 0 0 1 x 0 0	
0 0 0 0 0 0 0 0 x 0 0	
0 0 0 0 0 0 0 1 x 0 0	
0 0 0 0 0 0 0 0 x 0 0	
0 0 0 0 0 0 0 1 x 0 0	
0 0 0 0 0 0 0 0 x 0 0	
0 0 0 0 0 0 0 1 x 0 0	
0 0 0 0 0 0 0 0 x 0 0	
0 0 0 0 0 0 0 1 x 0 0	
0 0 0 0 0 0 0 0 x 0 0	
0 0 0 0 0 0 0 1 x 0 0	
0 0 0 0 0 0 0 0 x 0 0	
0 0 0 0 0 0 0 1 x 0 0	
0 0 0 0 0 0 0 0 x 0 0	
0 0 0 0 0 0 0 1 x 0 0	
0 0 0 0 0 0 0 0 x 0 0	
0 0 0 0 0 0 0 1 x 0 0	
0 0 0 0 0 0 0 0 x 0 0	
0 0 0 0 0 0 0 1 x 0 0	
0 0 0 0 0 0 0 0 x 0 0	
0 0 0 0 0 0 0 1 x 0 0	
0 0 0 0 0 0 0 0 x 0 0	
0 0 0 0 0 0 0 1 x 0 0	
0 0 0 0 0 0 0 0 x 0 0	
0 0 0 0 0 0 0 1 x 0 0	
0 0 0 0 0 0 0 0 x 0 0	
0 0 0 0 0 0 0 1 x 0 0	
0 0 0 0 0 0 0 0 x 0 0	
0 0 0 0 0 0 0 1 x 0 0	
0 0 0 0 0 0 0 0 x 0 0	
0 0 0 0 0 0 0 1 x 0 0	
0 0 0 0 0 0 0 0 x 0 0	
0 0 0 0 0 0 0 1 x 0 0	
0 0 0 0 0 0 0 0 x 0 0	
0 0 0 0 0 0 0 1 x 0 0	
0 0 0 0 0 0 0 0 x 0 0	
0 0 0 0 0 0 0 1 x 0 0	
0 0 0 0 0 0 0 0 x 0 0	
0 0 0 0 0 0 0 1 1 0 0	
0 0 0 0 0 0 1 0 1 0 0	
0 0 0 0 0 0 1 1 1 0 0	
0 0 0 0 0 0 0 0 1 0 0	
0 0 0 0 0 0 0 1 1 0 0	
0 0 0 0 0 0 0 0 1 0 0	
0 0 0 0 0 0 0 1 1 0 0	
0 0 0 0 0 0 0 0 1 0 0	
0 0 0 0 0 0 0 1 1 0 68	
0 0 0 0 0 0 0 0 1 0 68	
0 0 0 0 0 0 0 1 1 0 0	
0 0 0 0 0 0 0 0 1 0 0	
0 0 0 0 0 0 0 1 1 0 0	
0 0 0 0 0 0 0 0 1 0 0	
0 0 0 0 0 0 0 1 1 0 0	
0 0 0 0 0 0 0 0 1 0 0	
0 0 0 0 0 0 0 1 1 0 0	
0 0 0 0 0 0 0 0 1 0 0	
0 0 0 0 0 0 0 1 1 0 0	
0 0 0 0 0 0 0 0 1 0 0	
0 0 0 0 0 0 0 1 1 0 0	
0 0 0 0 0 0 0 0 1 0 0	
0 0 0 0 0 0 0 1 1 0 0	
0 0 0 0 0 0 0 0 1 0 0	
0 0 0 0 0 0 0 1 1 0 0	
0 0 0 0 0 0 0 0 1 0 0	
0 0 0 0 0 0 0 1 1 0 0	
0 0 0 0 0 0 0 0 1 0 0	
0 0 0 0 0 0 0 1 1 0 0	
0 0 0 0 0 0 0 0 1 0 0	
0 0 0 0 0 0 0 1 1 0 0	
0 0 0 0 0 0 0 0 1 0 0	
0 0 0 0 0 0 0 1 1 0 0	
0 0 0 0 0 0 0 0 1 0 0	
0 0 0 0 0 0 0 1 1 1 0	
0 0 0 0 0 0 0 0 1 1 0	
0 0 0 0 0 0 0 1 1 1 0	
0 0 0 0 0 0 0 0 1 1 0	
*/

/* Test case Jump_Test:
M N progIN reset progLoad start result clk valid done output	
0 0 0 0 0 0 0 0 x x x	
0 0 0 0 0 0 0 1 x x x	
0 0 0 1 0 0 0 0 x x x	
0 0 0 1 0 0 0 1 0 0 0	
0 0 0 0 0 0 0 0 0 0 0	
0 0 0 0 0 0 0 1 0 0 0	
0 0 0 0 0 0 0 0 0 0 0	
0 0 0 0 0 0 0 1 0 0 0	
0 0 0 0 0 0 0 0 0 0 0	
0 0 0 0 0 0 0 1 0 0 0	
0 0 0 0 0 0 0 0 0 0 0	
0 0 0 0 0 0 0 1 0 0 0	
0 0 0 0 0 0 0 0 0 0 0	
0 0 0 0 0 0 0 1 0 0 0	
0 0 0 0 0 0 0 0 0 0 0	
0 0 0 0 0 0 0 1 0 0 0	
0 0 0 0 0 0 0 0 0 0 0	
0 0 0 0 0 0 0 1 0 0 0	
0 0 0 0 0 0 0 0 0 0 0	
0 0 0 0 0 0 0 1 0 0 0	
0 0 0 0 0 0 0 0 0 0 0	
0 0 0 0 0 0 0 1 0 0 0	
0 0 0 0 0 0 0 0 0 0 0	
0 0 0 0 0 0 0 1 0 0 0	
0 0 0 0 0 0 0 0 0 0 0	
0 0 0 0 0 0 0 1 0 0 0	
0 0 0 0 0 0 0 0 0 0 0	
0 0 0 0 0 0 0 1 0 0 0	
0 0 0 0 0 0 0 0 0 0 0	
0 0 0 0 0 0 0 1 0 0 0	
0 0 0 0 0 0 0 0 0 0 0	
0 0 0 0 0 0 0 1 0 0 0	
0 0 0 0 0 0 0 0 0 0 0	
0 0 0 0 0 0 0 1 0 0 0	
0 0 0 0 0 0 0 0 0 0 0	
0 0 0 0 0 0 0 1 0 0 0	
0 0 0 0 0 0 0 0 0 0 0	
0 0 0 0 0 0 0 1 0 0 0	
0 0 0 0 0 0 0 0 0 0 0	
0 0 0 0 0 0 0 1 0 0 0	
0 0 0 0 0 0 0 0 0 0 0	
0 0 0 0 0 0 0 1 0 0 0	
0 0 271 0 1 0 0 0 0 0 0	
0 0 271 0 1 0 0 1 0 0 0	
0 0 566 0 1 0 0 0 0 0 0	
0 0 566 0 1 0 0 1 0 0 0	
0 0 5888 0 1 0 0 0 0 0 0	
0 0 5888 0 1 0 0 1 0 0 0	
0 0 3599 0 1 0 0 0 0 0 0	
0 0 3599 0 1 0 0 1 0 0 0	
0 0 4110 0 1 0 0 0 0 0 0	
0 0 4110 0 1 0 0 1 0 0 0	
0 0 3856 0 1 0 0 0 0 0 0	
0 0 3856 0 1 0 0 1 0 0 0	
0 0 0 0 1 0 0 0 0 0 0	
0 0 0 0 1 0 0 1 0 0 0	
0 0 0 0 1 0 0 0 0 0 0	
0 0 0 0 1 0 0 1 0 0 0	
0 0 0 0 1 0 0 0 0 0 0	
0 0 0 0 1 0 0 1 0 0 0	
0 0 0 0 1 0 0 0 0 0 0	
0 0 0 0 1 0 0 1 0 0 0	
0 0 0 0 1 0 0 0 0 0 0	
0 0 0 0 1 0 0 1 0 0 0	
0 0 0 0 1 0 0 0 0 0 0	
0 0 0 0 1 0 0 1 0 0 0	
0 0 0 0 1 0 0 0 0 0 0	
0 0 0 0 1 0 0 1 0 0 0	
0 0 0 0 1 0 0 0 0 0 0	
0 0 0 0 1 0 0 1 0 0 0	
0 0 0 0 1 0 0 0 0 0 0	
0 0 0 0 1 0 0 1 0 0 0	
0 0 0 0 1 0 0 0 0 0 0	
0 0 0 0 1 0 0 1 0 0 0	
0 0 4352 0 1 0 0 0 0 0 0	
0 0 4352 0 1 0 0 1 0 0 0	
0 0 2819 0 1 0 0 0 0 0 0	
0 0 2819 0 1 0 0 1 0 0 0	
0 0 7936 0 1 0 0 0 0 0 0	
0 0 7936 0 1 0 0 1 0 0 0	
0 0 0 0 1 0 0 0 0 0 0	
0 0 0 0 1 0 0 1 0 0 0	
0 0 0 0 0 0 0 0 0 0 0	
0 0 0 0 0 0 0 1 0 0 0	
0 0 0 0 0 0 0 0 0 0 0	
0 0 0 0 0 0 0 1 0 0 0	
0 0 0 0 0 0 0 0 0 0 0	
0 0 0 0 0 0 0 1 0 0 0	
0 0 0 0 0 1 0 0 0 0 0	
0 0 0 0 0 1 0 1 0 0 0	
0 0 0 0 0 0 0 0 x 0 0	
0 0 0 0 0 0 0 1 x 0 0	
0 0 0 0 0 0 0 0 x 0 0	
0 0 0 0 0 0 0 1 x 0 0	
0 0 0 0 0 0 0 0 x 0 0	
0 0 0 0 0 0 0 1 x 0 0	
0 0 0 0 0 0 0 0 x 0 0	
0 0 0 0 0 0 0 1 x 0 0	
0 0 0 0 0 0 0 0 x 0 0	
0 0 0 0 0 0 0 1 x 0 0	
0 0 0 0 0 0 0 0 x 0 0	
0 0 0 0 0 0 0 1 x 0 0	
0 0 0 0 0 0 0 0 x 0 0	
0 0 0 0 0 0 0 1 x 0 0	
0 0 0 0 0 0 0 0 x 0 0	
0 0 0 0 0 0 0 1 x 0 0	
0 0 0 0 0 0 0 0 x 0 0	
0 0 0 0 0 0 0 1 x 0 0	
0 0 0 0 0 0 0 0 x 0 0	
0 0 0 0 0 0 0 1 x 0 0	
0 0 0 0 0 0 0 0 x 0 0	
0 0 0 0 0 0 0 1 x 0 0	
0 0 0 0 0 0 0 0 x 0 0	
0 0 0 0 0 0 0 1 x 0 0	
0 0 0 0 0 0 0 0 x 0 0	
0 0 0 0 0 0 0 1 x 0 0	
0 0 0 0 0 0 0 0 x 0 0	
0 0 0 0 0 0 0 1 x 0 0	
0 0 0 0 0 0 0 0 x 0 0	
0 0 0 0 0 0 0 1 x 0 0	
0 0 0 0 0 0 0 0 x 0 0	
0 0 0 0 0 0 0 1 x 0 0	
0 0 0 0 0 0 0 0 x 0 0	
0 0 0 0 0 0 0 1 x 0 0	
0 0 0 0 0 0 0 0 x 0 0	
0 0 0 0 0 0 0 1 x 0 0	
0 0 0 0 0 0 0 0 x 0 0	
0 0 0 0 0 0 0 1 x 0 0	
0 0 0 0 0 0 0 0 x 0 0	
0 0 0 0 0 0 0 1 x 0 0	
0 0 0 0 0 0 0 0 x 0 0	
0 0 0 0 0 0 0 1 x 0 0	
0 0 0 0 0 0 0 0 x 0 0	
0 0 0 0 0 0 0 1 x 0 0	
0 0 0 0 0 0 0 0 x 0 0	
0 0 0 0 0 0 0 1 x 0 0	
0 0 0 0 0 0 0 0 x 0 0	
0 0 0 0 0 0 0 1 x 0 0	
0 0 0 0 0 0 0 0 x 0 0	
0 0 0 0 0 0 0 1 x 0 0	
0 0 0 0 0 0 0 0 x 0 0	
0 0 0 0 0 0 0 1 1 0 0	
0 0 0 0 0 0 1 0 1 0 0	
0 0 0 0 0 0 1 1 1 0 0	
0 0 0 0 0 0 0 0 1 0 0	
0 0 0 0 0 0 0 1 1 0 0	
0 0 0 0 0 0 0 0 1 0 0	
0 0 0 0 0 0 0 1 1 0 0	
0 0 0 0 0 0 0 0 1 0 0	
0 0 0 0 0 0 0 1 1 0 69	
0 0 0 0 0 0 0 0 1 0 69	
0 0 0 0 0 0 0 1 1 0 0	
0 0 0 0 0 0 0 0 1 0 0	
0 0 0 0 0 0 0 1 1 0 0	
0 0 0 0 0 0 0 0 1 0 0	
0 0 0 0 0 0 0 1 1 0 0	
0 0 0 0 0 0 0 0 1 0 0	
0 0 0 0 0 0 0 1 1 0 0	
0 0 0 0 0 0 0 0 1 0 0	
0 0 0 0 0 0 0 1 1 0 0	
0 0 0 0 0 0 0 0 1 0 0	
0 0 0 0 0 0 0 1 1 0 0	
0 0 0 0 0 0 0 0 1 0 0	
0 0 0 0 0 0 0 1 1 0 0	
0 0 0 0 0 0 0 0 1 0 0	
0 0 0 0 0 0 0 1 1 0 0	
0 0 0 0 0 0 0 0 1 0 0	
0 0 0 0 0 0 0 1 1 0 0	
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*/

/* Test case rRam_Test:
M N progIN reset progLoad start result clk valid done output
0 0 0 0 0 0 0 0 0 0 0
0 0 0 0 0 0 0 1 0 0 0
0 0 0 1 0 0 0 0 0 0 0
0 0 0 1 0 0 0 1 0 0 0
0 0 0 0 0 0 0 0 0 0 0
0 0 0 0 0 0 0 1 0 0 0
0 0 0 0 0 0 0 0 0 0 0
0 0 0 0 0 0 0 1 0 0 0
0 0 0 0 0 0 0 0 0 0 0
0 0 0 0 0 0 0 1 0 0 0
0 0 0 0 0 0 0 0 0 0 0
0 0 0 0 0 0 0 1 0 0 0
0 0 0 0 0 0 0 0 0 0 0
0 0 0 0 0 0 0 1 0 0 0
0 0 0 0 0 0 0 0 0 0 0
0 0 0 0 0 0 0 1 0 0 0
0 0 0 0 0 0 0 0 0 0 0
0 0 0 0 0 0 0 1 0 0 0
0 0 0 0 0 0 0 0 0 0 0
0 0 0 0 0 0 0 1 0 0 0
0 0 0 0 0 0 0 0 0 0 0
0 0 0 0 0 0 0 1 0 0 0
0 0 0 0 0 0 0 0 0 0 0
0 0 0 0 0 0 0 1 0 0 0
0 0 0 0 0 0 0 0 0 0 0
0 0 0 0 0 0 0 1 0 0 0
0 0 0 0 0 0 0 0 0 0 0
0 0 0 0 0 0 0 1 0 0 0
0 0 0 0 0 0 0 0 0 0 0
0 0 0 0 0 0 0 1 0 0 0
0 0 0 0 0 0 0 0 0 0 0
0 0 0 0 0 0 0 1 0 0 0
0 0 0 0 0 0 0 0 0 0 0
0 0 0 0 0 0 0 1 0 0 0
0 0 0 0 0 0 0 0 0 0 0
0 0 0 0 0 0 0 1 0 0 0
0 0 0 0 0 0 0 0 0 0 0
0 0 0 0 0 0 0 1 0 0 0
0 0 0 0 0 0 0 0 0 0 0
0 0 0 0 0 0 0 1 0 0 0
0 0 0 0 0 0 0 0 0 0 0
0 0 0 0 0 0 0 1 0 0 0
0 0 0 0 0 0 0 0 0 0 0
0 0 0 0 0 0 0 1 0 0 0
0 0 259 0 1 0 0 0 0 0 0
0 0 259 0 1 0 0 1 0 0 0
0 0 2816 0 1 0 0 0 0 0 0
0 0 2816 0 1 0 0 1 0 0 0
0 0 1024 0 1 0 0 0 0 0 0
0 0 1024 0 1 0 0 1 0 0 0
0 0 7168 0 1 0 0 0 0 0 0
0 0 7168 0 1 0 0 1 0 0 0
0 0 2817 0 1 0 0 0 0 0 0
0 0 2817 0 1 0 0 1 0 0 0
0 0 2560 0 1 0 0 0 0 0 0
0 0 2560 0 1 0 0 1 0 0 0
0 0 2831 0 1 0 0 0 0 0 0
0 0 2831 0 1 0 0 1 0 0 0
0 0 7936 0 1 0 0 0 0 0 0
0 0 7936 0 1 0 0 1 0 0 0
0 0 0 0 0 0 0 0 0 0 0
0 0 0 0 0 0 0 1 0 0 0
0 0 0 0 0 0 0 0 0 0 0
0 0 0 0 0 0 0 1 0 0 0
0 0 0 0 0 0 0 0 0 0 0
0 0 0 0 0 0 0 1 0 0 0
0 0 0 0 0 0 0 0 0 0 0
0 0 0 0 0 0 0 1 0 0 0
0 0 0 0 0 0 0 0 0 0 0
0 0 0 0 0 0 0 1 0 0 0
0 0 0 0 0 0 0 0 0 0 0
0 0 0 0 0 0 0 1 0 0 0
0 0 0 0 0 0 0 0 0 0 0
0 0 0 0 0 0 0 1 0 0 0
0 0 0 0 0 0 0 0 0 0 0
0 0 0 0 0 0 0 1 0 0 0
0 0 0 0 0 0 0 0 0 0 0
0 0 0 0 0 0 0 1 0 0 0
0 0 0 0 0 0 0 0 0 0 0
0 0 0 0 0 0 0 1 0 0 0
0 0 0 0 0 0 0 0 0 0 0
0 0 0 0 0 0 0 1 0 0 0
0 0 0 0 0 0 0 0 0 0 0
0 0 0 0 0 0 0 1 0 0 0
0 0 0 0 0 0 0 0 0 0 0
0 0 0 0 0 0 0 1 0 0 0
0 0 0 0 0 0 0 0 0 0 0
0 0 0 0 0 0 0 1 0 0 0
0 0 0 0 0 0 0 0 0 0 0
0 0 0 0 0 0 0 1 0 0 0
0 0 0 0 0 1 0 0 0 0 0
0 0 0 0 0 1 0 1 0 0 0
0 0 0 0 0 0 0 0 x 0 0
0 0 0 0 0 0 0 1 x 0 0
0 0 0 0 0 0 0 0 x 0 0
0 0 0 0 0 0 0 1 x 0 0
0 0 0 0 0 0 0 0 x 0 0
0 0 0 0 0 0 0 1 x 0 0
0 0 0 0 0 0 0 0 x 0 0
0 0 0 0 0 0 0 1 x 0 0
0 0 0 0 0 0 0 0 x 0 0
0 0 0 0 0 0 0 1 x 0 0
0 0 0 0 0 0 0 0 x 0 0
0 0 0 0 0 0 0 1 x 0 0
0 0 0 0 0 0 0 0 x 0 0
0 0 0 0 0 0 0 1 x 0 0
0 0 0 0 0 0 0 0 x 0 0
0 0 0 0 0 0 0 1 x 0 0
0 0 0 0 0 0 0 0 x 0 0
0 0 0 0 0 0 0 1 x 0 0
0 0 0 0 0 0 0 0 x 0 0
0 0 0 0 0 0 0 1 x 0 0
0 0 0 0 0 0 0 0 x 0 0
0 0 0 0 0 0 0 1 x 0 0
0 0 0 0 0 0 0 0 x 0 0
0 0 0 0 0 0 0 1 x 0 0
0 0 0 0 0 0 0 0 x 0 0
0 0 0 0 0 0 0 1 x 0 0
0 0 0 0 0 0 0 0 x 0 0
0 0 0 0 0 0 0 1 x 0 0
0 0 0 0 0 0 0 0 x 0 0
0 0 0 0 0 0 0 1 x 0 0
0 0 0 0 0 0 0 0 x 0 0
0 0 0 0 0 0 0 1 x 0 0
0 0 0 0 0 0 0 0 x 0 0
0 0 0 0 0 0 0 1 x 0 0
0 0 0 0 0 0 0 0 x 0 0
0 0 0 0 0 0 0 1 x 0 0
0 0 0 0 0 0 0 0 x 0 0
0 0 0 0 0 0 0 1 x 0 0
0 0 0 0 0 0 0 0 x 0 0
0 0 0 0 0 0 0 1 x 0 0
0 0 0 0 0 0 0 0 x 0 0
0 0 0 0 0 0 0 1 x 0 0
0 0 0 0 0 0 0 0 x 0 0
0 0 0 0 0 0 0 1 x 0 0
0 0 0 0 0 0 0 0 x 0 0
0 0 0 0 0 0 0 1 x 0 0
0 0 0 0 0 0 0 0 x 0 0
0 0 0 0 0 0 0 1 x 0 0
0 0 0 0 0 0 0 0 x 0 0
0 0 0 0 0 0 0 1 x 0 0
0 0 0 0 0 0 0 0 x 0 0
0 0 0 0 0 0 0 1 x 0 0
0 0 0 0 0 0 0 0 x 0 0
0 0 0 0 0 0 0 1 x 0 0
0 0 0 0 0 0 0 0 x 0 0
0 0 0 0 0 0 0 1 x 0 0
0 0 0 0 0 0 0 0 x 0 0
0 0 0 0 0 0 0 1 x 0 0
0 0 0 0 0 0 0 0 x 0 0
0 0 0 0 0 0 0 1 x 0 0
0 0 0 0 0 0 0 0 x 0 0
0 0 0 0 0 0 0 1 x 0 0
0 0 0 0 0 0 0 0 x 0 0
0 0 0 0 0 0 0 1 x 0 0
0 0 0 0 0 0 0 0 x 0 0
0 0 0 0 0 0 0 1 x 0 0
0 0 0 0 0 0 0 0 x 0 0
0 0 0 0 0 0 0 1 x 0 0
0 0 0 0 0 0 0 0 x 0 0
0 0 0 0 0 0 0 1 x 0 0
0 0 0 0 0 0 0 0 x 0 0
0 0 0 0 0 0 0 1 x 0 0
0 0 0 0 0 0 0 0 x 0 0
0 0 0 0 0 0 0 1 x 0 0
0 0 0 0 0 0 0 0 x 0 0
0 0 0 0 0 0 0 1 x 0 0
0 0 0 0 0 0 0 0 x 0 0
0 0 0 0 0 0 0 1 x 0 0
0 0 0 0 0 0 0 0 x 0 0
0 0 0 0 0 0 0 1 x 0 0
0 0 0 0 0 0 0 0 x 0 0
0 0 0 0 0 0 0 1 x 0 0
0 0 0 0 0 0 0 0 x 0 0
0 0 0 0 0 0 0 1 x 0 0
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*/

/* Test case TripleJump_Test:
M N progIN reset progLoad start result clk valid done output
0 0 0 0 0 0 0 0 x x x
0 0 0 0 0 0 0 1 x x x
0 0 0 1 0 0 0 0 x x x
0 0 0 1 0 0 0 1 0 0 0
0 0 0 0 0 0 0 0 0 0 0
0 0 0 0 0 0 0 1 0 0 0
0 0 0 0 0 0 0 0 0 0 0
0 0 0 0 0 0 0 1 0 0 0
0 0 0 0 0 0 0 0 0 0 0
0 0 0 0 0 0 0 1 0 0 0
0 0 0 0 0 0 0 0 0 0 0
0 0 0 0 0 0 0 1 0 0 0
0 0 0 0 0 0 0 0 0 0 0
0 0 0 0 0 0 0 1 0 0 0
0 0 0 0 0 0 0 0 0 0 0
0 0 0 0 0 0 0 1 0 0 0
0 0 0 0 0 0 0 0 0 0 0
0 0 0 0 0 0 0 1 0 0 0
0 0 0 0 0 0 0 0 0 0 0
0 0 0 0 0 0 0 1 0 0 0
0 0 0 0 0 0 0 0 0 0 0
0 0 0 0 0 0 0 1 0 0 0
0 0 0 0 0 0 0 0 0 0 0
0 0 0 0 0 0 0 1 0 0 0
0 0 0 0 0 0 0 0 0 0 0
0 0 0 0 0 0 0 1 0 0 0
0 0 0 0 0 0 0 0 0 0 0
0 0 0 0 0 0 0 1 0 0 0
0 0 0 0 0 0 0 0 0 0 0
0 0 0 0 0 0 0 1 0 0 0
0 0 0 0 0 0 0 0 0 0 0
0 0 0 0 0 0 0 1 0 0 0
0 0 0 0 0 0 0 0 0 0 0
0 0 0 0 0 0 0 1 0 0 0
0 0 0 0 0 0 0 0 0 0 0
0 0 0 0 0 0 0 1 0 0 0
0 0 0 0 0 0 0 0 0 0 0
0 0 0 0 0 0 0 1 0 0 0
0 0 0 0 0 0 0 0 0 0 0
0 0 0 0 0 0 0 1 0 0 0
0 0 0 0 0 0 0 0 0 0 0
0 0 0 0 0 0 0 1 0 0 0
0 0 0 0 0 0 0 0 0 0 0
0 0 0 0 0 0 0 1 0 0 0
0 0 271 0 1 0 0 0 0 0 0
0 0 271 0 1 0 0 1 0 0 0
0 0 565 0 1 0 0 0 0 0 0
0 0 565 0 1 0 0 1 0 0 0
0 0 5888 0 1 0 0 0 0 0 0
0 0 5888 0 1 0 0 1 0 0 0
0 0 3845 0 1 0 0 0 0 0 0
0 0 3845 0 1 0 0 1 0 0 0
0 0 4352 0 1 0 0 0 0 0 0
0 0 4352 0 1 0 0 1 0 0 0
0 0 3847 0 1 0 0 0 0 0 0
0 0 3847 0 1 0 0 1 0 0 0
0 0 4352 0 1 0 0 0 0 0 0
0 0 4352 0 1 0 0 1 0 0 0
0 0 4107 0 1 0 0 0 0 0 0
0 0 4107 0 1 0 0 1 0 0 0
0 0 1024 0 1 0 0 0 0 0 0
0 0 1024 0 1 0 0 1 0 0 0
0 0 5888 0 1 0 0 0 0 0 0
0 0 5888 0 1 0 0 1 0 0 0
0 0 3331 0 1 0 0 0 0 0 0
0 0 3331 0 1 0 0 1 0 0 0
0 0 2819 0 1 0 0 0 0 0 0
0 0 2819 0 1 0 0 1 0 0 0
0 0 7936 0 1 0 0 0 0 0 0
0 0 7936 0 1 0 0 1 0 0 0
0 0 0 0 0 0 0 0 0 0 0
0 0 0 0 0 0 0 1 0 0 0
0 0 0 0 0 1 0 0 0 0 0
0 0 0 0 0 1 0 1 0 0 0
0 0 0 0 0 0 0 0 x 0 0
0 0 0 0 0 0 0 1 x 0 0
0 0 0 0 0 0 0 0 x 0 0
0 0 0 0 0 0 0 1 x 0 0
0 0 0 0 0 0 0 0 x 0 0
0 0 0 0 0 0 0 1 x 0 0
0 0 0 0 0 0 0 0 x 0 0
0 0 0 0 0 0 0 1 x 0 0
0 0 0 0 0 0 0 0 x 0 0
0 0 0 0 0 0 0 1 x 0 0
0 0 0 0 0 0 0 0 x 0 0
0 0 0 0 0 0 0 1 x 0 0
0 0 0 0 0 0 0 0 x 0 0
0 0 0 0 0 0 0 1 x 0 0
0 0 0 0 0 0 0 0 x 0 0
0 0 0 0 0 0 0 1 x 0 0
0 0 0 0 0 0 0 0 x 0 0
0 0 0 0 0 0 0 1 x 0 0
0 0 0 0 0 0 0 0 x 0 0
0 0 0 0 0 0 0 1 x 0 0
0 0 0 0 0 0 0 0 x 0 0
0 0 0 0 0 0 0 1 x 0 0
0 0 0 0 0 0 0 0 x 0 0
0 0 0 0 0 0 0 1 x 0 0
0 0 0 0 0 0 0 0 x 0 0
0 0 0 0 0 0 0 1 x 0 0
0 0 0 0 0 0 0 0 x 0 0
0 0 0 0 0 0 0 1 x 0 0
0 0 0 0 0 0 0 0 x 0 0
0 0 0 0 0 0 0 1 x 0 0
0 0 0 0 0 0 0 0 x 0 0
0 0 0 0 0 0 0 1 x 0 0
0 0 0 0 0 0 0 0 x 0 0
0 0 0 0 0 0 0 1 x 0 0
0 0 0 0 0 0 0 0 x 0 0
0 0 0 0 0 0 0 1 x 0 0
0 0 0 0 0 0 0 0 x 0 0
0 0 0 0 0 0 0 1 x 0 0
0 0 0 0 0 0 0 0 x 0 0
0 0 0 0 0 0 0 1 x 0 0
0 0 0 0 0 0 0 0 x 0 0
0 0 0 0 0 0 0 1 x 0 0
0 0 0 0 0 0 0 0 x 0 0
0 0 0 0 0 0 0 1 x 0 0
0 0 0 0 0 0 0 0 x 0 0
0 0 0 0 0 0 0 1 x 0 0
0 0 0 0 0 0 0 0 x 0 0
0 0 0 0 0 0 0 1 x 0 0
0 0 0 0 0 0 0 0 x 0 0
0 0 0 0 0 0 0 1 x 0 0
0 0 0 0 0 0 0 0 x 0 0
0 0 0 0 0 0 0 1 x 0 0
0 0 0 0 0 0 0 0 x 0 0
0 0 0 0 0 0 0 1 x 0 0
0 0 0 0 0 0 0 0 x 0 0
0 0 0 0 0 0 0 1 x 0 0
0 0 0 0 0 0 0 0 x 0 0
0 0 0 0 0 0 0 1 x 0 0
0 0 0 0 0 0 0 0 x 0 0
0 0 0 0 0 0 0 1 x 0 0
0 0 0 0 0 0 0 0 x 0 0
0 0 0 0 0 0 0 1 x 0 0
0 0 0 0 0 0 0 0 x 0 0
0 0 0 0 0 0 0 1 x 0 0
0 0 0 0 0 0 0 0 x 0 0
0 0 0 0 0 0 0 1 x 0 0
0 0 0 0 0 0 0 0 x 0 0
0 0 0 0 0 0 0 1 x 0 0
0 0 0 0 0 0 0 0 x 0 0
0 0 0 0 0 0 0 1 x 0 0
0 0 0 0 0 0 0 0 x 0 0
0 0 0 0 0 0 0 1 x 0 0
0 0 0 0 0 0 0 0 x 0 0
0 0 0 0 0 0 0 1 x 0 0
0 0 0 0 0 0 0 0 x 0 0
0 0 0 0 0 0 0 1 x 0 0
0 0 0 0 0 0 0 0 x 0 0
0 0 0 0 0 0 0 1 x 0 0
0 0 0 0 0 0 0 0 x 0 0
0 0 0 0 0 0 0 1 x 0 0
0 0 0 0 0 0 0 0 x 0 0
0 0 0 0 0 0 0 1 x 0 0
0 0 0 0 0 0 0 0 x 0 0
0 0 0 0 0 0 0 1 x 0 0
0 0 0 0 0 0 0 0 x 0 0
0 0 0 0 0 0 0 1 x 0 0
0 0 0 0 0 0 0 0 x 0 0
0 0 0 0 0 0 0 1 x 0 0
0 0 0 0 0 0 0 0 x 0 0
0 0 0 0 0 0 0 1 x 0 0
0 0 0 0 0 0 0 0 x 0 0
0 0 0 0 0 0 0 1 x 0 0
0 0 0 0 0 0 0 0 x 0 0
0 0 0 0 0 0 0 1 x 0 0
0 0 0 0 0 0 0 0 x 0 0
0 0 0 0 0 0 0 1 x 0 0
0 0 0 0 0 0 0 0 x 0 0
0 0 0 0 0 0 0 1 x 0 0
0 0 0 0 0 0 0 0 x 0 0
0 0 0 0 0 0 0 1 x 0 0
0 0 0 0 0 0 0 0 x 0 0
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*/

/* Test case Arithmatic_Test:
M N progIN reset progLoad start result clk valid done output
0 0 0 0 0 0 0 0 0 0 0
0 0 0 0 0 0 0 1 0 0 0
0 0 0 1 0 0 0 0 0 0 0
0 0 0 1 0 0 0 1 0 0 0
0 0 0 0 0 0 0 0 0 0 0
0 0 0 0 0 0 0 1 0 0 0
0 0 0 0 0 0 0 0 0 0 0
0 0 0 0 0 0 0 1 0 0 0
0 0 0 0 0 0 0 0 0 0 0
0 0 0 0 0 0 0 1 0 0 0
0 0 0 0 0 0 0 0 0 0 0
0 0 0 0 0 0 0 1 0 0 0
0 0 0 0 0 0 0 0 0 0 0
0 0 0 0 0 0 0 1 0 0 0
0 0 0 0 0 0 0 0 0 0 0
0 0 0 0 0 0 0 1 0 0 0
0 0 0 0 0 0 0 0 0 0 0
0 0 0 0 0 0 0 1 0 0 0
0 0 0 0 0 0 0 0 0 0 0
0 0 0 0 0 0 0 1 0 0 0
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*/

/* Test case pRam_Test:
M N progIN reset progLoad start result clk valid done output	
0 0 0 0 0 0 0 0 x x x	
0 0 0 0 0 0 0 1 x x x	
0 0 0 1 0 0 0 0 x x x	
0 0 0 1 0 0 0 1 0 0 0	
0 0 0 0 0 0 0 0 0 0 0	
0 0 0 0 0 0 0 1 0 0 0	
0 0 0 0 0 0 0 0 0 0 0	
0 0 0 0 0 0 0 1 0 0 0	
0 0 0 0 0 0 0 0 0 0 0	
0 0 0 0 0 0 0 1 0 0 0	
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*/

/* Test case Super_Test:
M N progIN reset progLoad start result clk valid done output
0 0 0 0 0 0 0 0 0 0 0
0 0 0 0 0 0 0 1 0 0 0
0 0 0 1 0 0 0 0 0 0 0
0 0 0 1 0 0 0 1 0 0 0
0 0 0 0 0 0 0 0 0 0 0
0 0 0 0 0 0 0 1 0 0 0
0 0 0 0 0 0 0 0 0 0 0
0 0 0 0 0 0 0 1 0 0 0
0 0 0 0 0 0 0 0 0 0 0
0 0 0 0 0 0 0 1 0 0 0
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*/

/* Test case Prime_Test:
M N progIN reset progLoad start result clk valid done output
0 0 0 0 0 0 0 0 x x x
0 0 0 0 0 0 0 1 x x x
0 0 0 1 0 0 0 0 x x x
0 0 0 1 0 0 0 1 0 0 0
0 0 0 0 0 0 0 0 0 0 0
0 0 0 0 0 0 0 1 0 0 0
0 0 0 0 0 0 0 0 0 0 0
0 0 0 0 0 0 0 1 0 0 0
0 0 0 0 0 0 0 0 0 0 0
0 0 0 0 0 0 0 1 0 0 0
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*/

/* Test case Comment19_Test:
M N progIN reset progLoad start result clk valid done output
0 0 0 0 0 0 0 0 0 0 0
0 0 0 0 0 0 0 1 0 0 0
0 0 0 1 0 0 0 0 0 0 0
0 0 0 1 0 0 0 1 0 0 0
0 0 0 0 0 0 0 0 0 0 0
0 0 0 0 0 0 0 1 0 0 0
0 0 0 0 0 0 0 0 0 0 0
0 0 0 0 0 0 0 1 0 0 0
0 0 0 0 0 0 0 0 0 0 0
0 0 0 0 0 0 0 1 0 0 0
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*/
