// Digital circuit Final_v6.dig as structural Verilog
module Final_v6 (
  input  start,
  input  reset,
  input  result,
  input  [7:0] M,
  input  [7:0] N,
  input  [12:0] progIN,
  input  progLoad,
  input  clk,
  output valid,
  output done,
  output [7:0] \output ,
  output [15:0] out_12
);

  wire _00000, _00001, _00010, _00011, _00100, _00101, _00110, _00111, _01000, _01001, _01010, _01011,
       _01100, _01101, _01110, _01111, _10000, _10001, _10010, _10011, _10100, _10101, _10110, _10111,
       _11000, _11001, _11010, _11011, _11100, _11101, _11110, _11111, and_2_out, and_3_out, and_7_out,
       and_8_out, and_9_out, and_10_out, and_11_out, bitselector_1_out, busy, Calculate, ClearState,
       comparator_1_eq, comparator_1_gt, comparator_1_lt, Counter___Address, eq__eq__0x0F, equal_flag,
       Execute, FinalState, greater_flag, Initial_State, jump, lesser_flag, Load___accA, Load___accB,
       load___busy, load___done, Load___equal, Load___flag, load___Ops, Load___regC, Load___rRam,
       load___valid, load_m___n, m__eq__n, m__gt__n, m__lt__n, multiplexer_5_out, multiplexer_6_out,
       multiplexer_7_out, multiplexer_8_out, multiplexer_14_out, multiplexer_15_out, multiplexer_16_out,
       multiplexer_22_out, multiplexer_23_out, multiplexer_24_out, not_3_out, not_4_out, not_5_out,
       not_6_out, not_7_out, not_8_out, or_2_out, or_3_out, or_5_out, or_14_out, Prime, PrintState, q0, q1,
       q2, q3, q4, q5, q6, q7, QA, qA_t, QB, qB_t, QC, qC_t, Reset___Address, select___accB, select___ops,
       select___rRamAddress, subCal, subFinish, subLCM, subload_M_N, subLoadE, subLoadF, subWait,
       Waiting_State, WaitingResult;
  wire [1:0] lookuptable_1_out, lookuptable_2_out, lookuptable_3_out, select___equal_flag, select___regC;
  wire [3:0] op__0_3, op__4_7, select___accA;
  wire [4:0] opcode, Opcode_q, pRam_d1_2;
  wire [7:0] A___B, A___B_t, A___B_t_t, A___B_t_t_t, A___B_t_t_t_t, A__plus__B, A_and_B, A_or_B, A_shift_B,
       A_xor_B, accA, accB, add_2_s, add_3_s, add_4_s, add_5_s, add_6_s, add_7_s, add_8_s, add_9_s, add_10_s,
       add_11_s, Address, and_12_out, and_13_out, and_14_out, and_15_out, bitextender_1_out,
       bitextender_2_out, bitextender_3_out, bitextender_4_out, m_t, multiplexer_2_out, multiplexer_3_out,
       multiplexer_4_out, multiplexer_10_out, multiplexer_11_out, multiplexer_12_out, multiplexer_17_out,
       multiplexer_21_out, multiplexer_25_out, multiplexer_27_out, multiplexer_28_out, multiplexer_29_out,
       multiplexer_30_out, n_t, nA, New_m, New_n, operand, Operand_q, pRam, pRam_d1, regC, rRam, rRam_d1,
       startm, startn, sub_2_s, sub_3_s, sub_4_s, sub_5_s, sub_6_s, sub_7_s, sub_8_s, sub_9_s, sub_10_s,
       sub_11_s, value___rRam;
  wire [7:1] multiplexer_9_out, multiplexer_13_out, multiplexer_26_out;
  wire [7:7] multiplexer_9_out_2, multiplexer_13_out_2, multiplexer_26_out_2;
  wire [12:8] pRam_d2;
  wire [15:0] div_1_q, mul, mul_2_mul;

  Add #(.Bits(8)) add_1 (.a(accA), .b(accB), .c_i(1'b0), .s(A__plus__B));  // open: c_o
  Sub #(.Bits(8)) sub_1 (.a(accA), .b(accB), .c_i(1'b0), .s(A___B_t_t));  // open: c_o
  Mul #(.Bits(4)) mul_1 (.a(accA[3:0]), .b(accB[3:0]), .mul(A___B_t));
  assign nA = ~accA;  // Not not_1, 8 bits wide
  assign A_and_B = accA & accB;  // And and_1, 8 bits wide
  assign A_or_B = accA | accB;  // Or or_1, 8 bits wide
  assign A_xor_B = accA ^ accB;  // XOr xor_1, 8 bits wide
  LookUpTable #(.Bits(8)) Power (
    .in0(accB[0]), .in1(accB[1]), .in2(accB[2]), .in3(accA[0]), .in4(accA[1]), .in5(accA[2]),
    .out(A___B_t_t_t_t));
  LookUpTable u_Prime (
    .in0(accA[0]), .in1(accA[1]), .in2(accA[2]), .in3(accA[3]), .in4(accA[4]), .in5(accA[5]), .in6(accA[6]),
    .in7(accA[7]), .out(Prime));
  ROM #(.AddrBits(8), .Bits(8)) sqrt (.A(accA), .sel(1'b1));  // open: D
  Multiplexer #(.Selector_Bits(3), .Bits(8)) multiplexer_1 (
    .sel(accB[2:0]), .in_0(accA), .in_1({accA[6:0], 1'b0}), .in_2({accA[5:0], 2'b00}),
    .in_3({accA[4:0], 3'b000}), .in_4({accA[3:0], 4'b0000}), .in_5({accA[2:0], {5{1'b0}}}),
    .in_6({accA[1:0], {6{1'b0}}}), .in_7({accA[0], {7{1'b0}}}), .out(A_shift_B));
  BitSelector #(.Selector_Bits(3)) bitselector_1 (.in({8{1'b0}}), .sel(3'b111), .out(bitselector_1_out));
  Comparator #(.Signed("true"), .Bits(8)) comparator_1 (
    .a(accA), .b(accB), .gt(comparator_1_gt), .eq(comparator_1_eq), .lt(comparator_1_lt));
  Multiplexer #(.Selector_Bits(4), .Bits(8)) multiplexer_2 (
    .sel(select___accA), .in_0(operand), .in_1(accB), .in_2(regC), .in_3(pRam), .in_4(rRam),
    .in_5(A__plus__B), .in_6(A___B_t_t), .in_7(A___B_t), .in_8(A___B_t_t_t), .in_9(A___B),
    .in_10(A___B_t_t_t_t), .in_11(nA), .in_12(A_and_B), .in_13(A_or_B), .in_14(A_xor_B), .in_15(A_shift_B),
    .out(multiplexer_2_out));
  Multiplexer #(.Bits(8)) multiplexer_3 (.sel(select___accB), .in_0(operand), .in_1(accA), .out(multiplexer_3_out));
  Multiplexer #(.Selector_Bits(2), .Bits(8)) multiplexer_4 (
    .sel(select___regC), .in_0(accA), .in_1(M), .in_2(N), .in_3(N), .out(multiplexer_4_out));
  Sub #(.Bits(8)) sub_2 (.a({{7{1'b0}}, accA[7]}), .b(accB), .c_i(1'b0), .s(sub_2_s));  // open: c_o
  Add #(.Bits(8)) add_2 (.a({{7{1'b0}}, accA[7]}), .b(accB), .c_i(1'b0), .s(add_2_s));  // open: c_o
  Multiplexer multiplexer_5 (.sel(Initial_State), .in_0(comparator_1_gt), .in_1(1'b0), .out(multiplexer_5_out));
  Multiplexer #(.Selector_Bits(2)) multiplexer_6 (
    .sel(select___equal_flag), .in_0(comparator_1_eq), .in_1(1'b0), .in_2(Prime), .in_3(1'b0),
    .out(multiplexer_6_out));
  Multiplexer multiplexer_7 (.sel(Initial_State), .in_0(comparator_1_lt), .in_1(1'b0), .out(multiplexer_7_out));
  or or_2 (or_2_out, _11111, WaitingResult);
  Multiplexer multiplexer_8 (.sel(PrintState), .in_0(1'b0), .in_1(eq__eq__0x0F), .out(multiplexer_8_out));
  Multiplexer #(.Bits(8)) multiplexer_9 (
    .sel(bitselector_1_out), .in_0(sub_2_s), .in_1(add_2_s), .out({multiplexer_9_out_2[7], multiplexer_9_out}));
  BitSelector #(.Selector_Bits(3)) bitselector_2 (
    .in({multiplexer_9_out_2[7], multiplexer_9_out}), .sel(3'b111), .out(q7));
  Register #(.Bits(8)) u_accA (.D(multiplexer_2_out), .C(clk), .en(Load___accA), .Q(accA));
  Register #(.Bits(8)) u_accB (.D(multiplexer_3_out), .C(clk), .en(Load___accB), .Q(accB));
  Register #(.Bits(8)) u_regC (.D(multiplexer_4_out), .C(clk), .en(Load___regC), .Q(regC));
  Register GreaterFlag (.D(multiplexer_5_out), .C(clk), .en(Load___flag), .Q(greater_flag));
  Register EqualFlag (.D(multiplexer_6_out), .C(clk), .en(Load___equal), .Q(equal_flag));
  Register LesserFlag (.D(multiplexer_7_out), .C(clk), .en(Load___flag), .Q(lesser_flag));
  Register u_valid (.D(or_2_out), .C(clk), .en(load___valid), .Q(valid));
  Register u_done (.D(multiplexer_8_out), .C(clk), .en(load___done), .Q(done));
  Comparator #(.Bits(8)) u_eq__eq__0x0F (.a(Address), .b(8'hf), .eq(eq__eq__0x0F));  // open: gt, lt
  assign A___B_t_t_t = ~{q7, q6, q5, q4, q3, q2, q1, q0};  // Not not_2, 8 bits wide
  Sub #(.Bits(8)) sub_3 (.a({multiplexer_9_out, accA[6]}), .b(accB), .c_i(1'b0), .s(sub_3_s));  // open: c_o
  Add #(.Bits(8)) add_3 (.a({multiplexer_9_out, accA[6]}), .b(accB), .c_i(1'b0), .s(add_3_s));  // open: c_o
  Multiplexer #(.Bits(8)) multiplexer_10 (.sel(q7), .in_0(sub_3_s), .in_1(add_3_s), .out(multiplexer_10_out));
  BitSelector #(.Selector_Bits(3)) bitselector_3 (.in(multiplexer_10_out), .sel(3'b111), .out(q6));
  Sub #(.Bits(8)) sub_4 (.a({multiplexer_10_out[6:0], accA[5]}), .b(accB), .c_i(1'b0), .s(sub_4_s));  // open: c_o
  Add #(.Bits(8)) add_4 (.a({multiplexer_10_out[6:0], accA[5]}), .b(accB), .c_i(1'b0), .s(add_4_s));  // open: c_o
  Multiplexer #(.Bits(8)) multiplexer_11 (.sel(jump), .in_0(Address), .in_1(operand), .out(multiplexer_11_out));
  Multiplexer #(.Selector_Bits(2), .Bits(8)) multiplexer_12 (
    .sel(lookuptable_1_out), .in_0(Address), .in_1(operand), .in_2(8'hf), .in_3(8'he),
    .out(multiplexer_12_out));
  Add #(.Bits(8)) add_5 (.a(operand), .b(8'h1), .c_i(1'b0), .s(add_5_s));  // open: c_o
  or or_3 (or_3_out, ~start, result);  // Or
  and and_2 (and_2_out, ~load___valid, busy);  // And
  Multiplexer #(.Bits(8)) multiplexer_13 (
    .sel(q6), .in_0(sub_4_s), .in_1(add_4_s), .out({multiplexer_13_out_2[7], multiplexer_13_out}));
  LookUpTable #(.Bits(2)) lookuptable_1 (.in0(subLoadE), .in1(subLoadF), .in2(_01011), .out(lookuptable_1_out));
  BitSelector #(.Selector_Bits(3)) bitselector_4 (
    .in({multiplexer_13_out_2[7], multiplexer_13_out}), .sel(3'b111), .out(q5));
  RAMDualAccess #(.AddrBits(8), .Bits(13)) u_pRam (
    .str(progLoad), .C(clk), .ld(1'b1), .A1(multiplexer_11_out), .Din1(progIN), .A2(operand),
    .D1({pRam_d1_2, pRam_d1}), .D2({pRam_d2, pRam}));
  RAMDualAccess #(.AddrBits(8), .Bits(8)) u_rRam (
    .str(Load___rRam), .C(clk), .ld(1'b1), .A1(multiplexer_12_out), .Din1(value___rRam), .A2(operand),
    .D1(rRam_d1), .D2(rRam));
  CounterPreset #(.Bits(8)) AddressCount (
    .en(Counter___Address), .C(clk), .dir(1'b0), .in(add_5_s), .ld(jump), .clr(Reset___Address), .out(Address));  // open: ovf
  Multiplexer #(.Selector_Bits(3)) multiplexer_14 (
    .sel({QA, QB, QC}), .in_0(1'b0), .in_1(result), .in_2(load___valid), .in_3(1'b0), .in_4(1'b1),
    .in_5(1'b1), .in_6(1'b0), .in_7(not_3_out), .out(multiplexer_14_out));
  not not_3 (not_3_out, eq__eq__0x0F);
  Multiplexer #(.Selector_Bits(3)) multiplexer_15 (
    .sel({QA, QB, QC}), .in_0(1'b0), .in_1(start), .in_2(not_4_out), .in_3(1'b1), .in_4(1'b0),
    .in_5(eq__eq__0x0F), .in_6(1'b0), .in_7(not_5_out), .out(multiplexer_15_out));
  not not_4 (not_4_out, load___valid);
  not not_5 (not_5_out, eq__eq__0x0F);
  Multiplexer #(.Selector_Bits(3)) multiplexer_16 (
    .sel({QA, QB, QC}), .in_0(1'b1), .in_1(or_3_out), .in_2(and_2_out), .in_3(busy), .in_4(result),
    .in_5(not_6_out), .in_6(1'b1), .in_7(not_7_out), .out(multiplexer_16_out));
  not not_6 (not_6_out, eq__eq__0x0F);
  not not_7 (not_7_out, eq__eq__0x0F);
  Sub #(.Bits(8)) sub_5 (.a({multiplexer_13_out, accA[4]}), .b(accB), .c_i(1'b0), .s(sub_5_s));  // open: c_o
  Add #(.Bits(8)) add_6 (.a({multiplexer_13_out, accA[4]}), .b(accB), .c_i(1'b0), .s(add_6_s));  // open: c_o
  Register #(.Bits(5)) u_Opcode (.D(pRam_d1_2), .C(clk), .en(load___Ops), .Q(Opcode_q));
  Register #(.Bits(8)) u_Operand (.D(pRam_d1), .C(clk), .en(load___Ops), .Q(Operand_q));
  D_FF_AS d_ff_as_1 (.Set(reset), .D(multiplexer_14_out), .C(clk), .Clr(1'b0), .Q(QA));  // open: nQ
  D_FF_AS d_ff_as_2 (.Set(reset), .D(multiplexer_15_out), .C(clk), .Clr(1'b0), .Q(QB));  // open: nQ
  D_FF_AS d_ff_as_3 (.Set(reset), .D(multiplexer_16_out), .C(clk), .Clr(1'b0), .Q(QC));  // open: nQ
  Multiplexer #(.Bits(8)) multiplexer_17 (.sel(q5), .in_0(sub_5_s), .in_1(add_6_s), .out(multiplexer_17_out));
  Multiplexer #(.Bits(5)) multiplexer_18 (.sel(select___ops), .in_0({5{1'b0}}), .in_1(Opcode_q), .out(opcode));
  Multiplexer #(.Bits(8)) multiplexer_19 (.sel(select___ops), .in_0({8{1'b0}}), .in_1(Operand_q), .out(operand));
  Multiplexer #(.Bits(8)) multiplexer_20 (.sel(PrintState), .in_0({8{1'b0}}), .in_1(rRam_d1), .out(\output ));
  BitSelector #(.Selector_Bits(3)) bitselector_5 (.in(multiplexer_17_out), .sel(3'b111), .out(q4));
  Sub #(.Bits(8)) sub_6 (.a({multiplexer_17_out[6:0], accA[3]}), .b(accB), .c_i(1'b0), .s(sub_6_s));  // open: c_o
  Add #(.Bits(8)) add_7 (.a({multiplexer_17_out[6:0], accA[3]}), .b(accB), .c_i(1'b0), .s(add_7_s));  // open: c_o
  Multiplexer #(.Bits(8)) multiplexer_21 (.sel(q4), .in_0(sub_6_s), .in_1(add_7_s), .out(multiplexer_21_out));
  Decoder #(.Selector_Bits(3)) decoder_1 (
    .sel({QA, QB, QC}), .out_0(Initial_State), .out_1(Waiting_State), .out_2(Execute), .out_3(Calculate),
    .out_4(WaitingResult), .out_5(PrintState), .out_6(FinalState), .out_7(ClearState));
  Decoder #(.Selector_Bits(5)) decoder_2 (
    .sel(opcode), .out_0(_00000), .out_1(_00001), .out_2(_00010), .out_3(_00011), .out_4(_00100),
    .out_5(_00101), .out_6(_00110), .out_7(_00111), .out_8(_01000), .out_9(_01001), .out_10(_01010),
    .out_11(_01011), .out_12(_01100), .out_13(_01101), .out_14(_01110), .out_15(_01111), .out_16(_10000),
    .out_17(_10001), .out_18(_10010), .out_19(_10011), .out_20(_10100), .out_21(_10101), .out_22(_10110),
    .out_23(_10111), .out_24(_11000), .out_25(_11001), .out_26(_11010), .out_27(_11011), .out_28(_11100),
    .out_29(_11101), .out_30(_11110), .out_31(_11111));
  BitSelector #(.Selector_Bits(3)) bitselector_6 (.in(multiplexer_21_out), .sel(3'b111), .out(q3));
  Multiplexer #(.Selector_Bits(3)) multiplexer_22 (
    .sel({qA_t, qB_t, qC_t}), .in_0(1'b0), .in_1(1'b0), .in_2(1'b0), .in_3(1'b1), .in_4(1'b1), .in_5(1'b1),
    .in_6(1'b0), .in_7(1'b0), .out(multiplexer_22_out));
  Multiplexer #(.Selector_Bits(3)) multiplexer_23 (
    .sel({qA_t, qB_t, qC_t}), .in_0(1'b0), .in_1(m__eq__n), .in_2(1'b1), .in_3(1'b0), .in_4(1'b0),
    .in_5(1'b1), .in_6(1'b0), .in_7(1'b0), .out(multiplexer_23_out));
  Multiplexer #(.Selector_Bits(3)) multiplexer_24 (
    .sel({qA_t, qB_t, qC_t}), .in_0(busy), .in_1(not_8_out), .in_2(m__eq__n), .in_3(1'b0), .in_4(1'b1),
    .in_5(1'b1), .in_6(1'b0), .in_7(1'b0), .out(multiplexer_24_out));
  not not_8 (not_8_out, m__eq__n);
  Sub #(.Bits(8)) sub_7 (.a({multiplexer_21_out[6:0], accA[2]}), .b(accB), .c_i(1'b0), .s(sub_7_s));  // open: c_o
  Add #(.Bits(8)) add_8 (.a({multiplexer_21_out[6:0], accA[2]}), .b(accB), .c_i(1'b0), .s(add_8_s));  // open: c_o
  ROM #(.AddrBits(5), .Bits(4)) select_accA (.A(opcode), .sel(1'b1), .D(select___accA));
  ROM #(.AddrBits(5)) select_accB (.A(opcode), .sel(1'b1), .D(select___accB));
  ROM #(.AddrBits(5), .Bits(2)) select_regC (.A(opcode), .sel(1'b1), .D(select___regC));
  Multiplexer #(.Selector_Bits(2), .Bits(8)) multiplexer_25 (
    .sel(lookuptable_2_out), .in_0(Address), .in_1(operand), .in_2({4'b0000, op__4_7}),
    .in_3({4'b0000, op__4_7}), .out(multiplexer_25_out));
  Multiplexer #(.Bits(8)) multiplexer_26 (
    .sel(q3), .in_0(sub_7_s), .in_1(add_8_s), .out({multiplexer_26_out_2[7], multiplexer_26_out}));
  D_FF_AS d_ff_as_4 (.Set(1'b0), .D(multiplexer_22_out), .C(clk), .Clr(reset), .Q(qA_t));  // open: nQ
  D_FF_AS d_ff_as_5 (.Set(1'b0), .D(multiplexer_23_out), .C(clk), .Clr(reset), .Q(qB_t));  // open: nQ
  D_FF_AS d_ff_as_6 (.Set(1'b0), .D(multiplexer_24_out), .C(clk), .Clr(reset), .Q(qC_t));  // open: nQ
  and and_3 (and_3_out, start, Waiting_State);
  LookUpTable #(.Bits(2)) lookuptable_2 (.in0(subload_M_N), .in1(_01011), .out(lookuptable_2_out));
  BitSelector #(.Selector_Bits(3)) bitselector_7 (
    .in({multiplexer_26_out_2[7], multiplexer_26_out}), .sel(3'b111), .out(q2));
  RAMDualAccess #(.AddrBits(8), .Bits(8)) rRam_2 (
    .str(Load___rRam), .C(clk), .ld(1'b1), .A1(multiplexer_25_out), .Din1(value___rRam),
    .A2({4'b0000, op__0_3}), .D1(startm), .D2(startn));
  Decoder #(.Selector_Bits(3)) decoder_3 (
    .sel({qA_t, qB_t, qC_t}), .out_0(subWait), .out_1(subload_M_N), .out_2(subCal), .out_3(subLCM),
    .out_4(subLoadF), .out_5(subLoadE), .out_7(subFinish));  // open: out_6
  or or_4 (load___busy, _11110, subFinish);
  or or_5 (or_5_out, ClearState, progLoad, Execute, PrintState);
  or or_6 (Reset___Address, Initial_State, and_3_out, WaitingResult, FinalState, reset);
  and and_4 (load___Ops, Execute, ~busy);  // And
  and and_5 (select___ops, Execute, ~busy);  // And
  or or_7 (Load___rRam, ClearState, _01011, subLoadE, subLoadF);
  or or_8 (Load___accA, _00001, _00011, _00110, _01001, _01010, _10001, _10010, _10011, Initial_State, _10100, _10101, _10110, _11000, _11001, _11010, _11011, _11100);
  or or_9 (Load___accB, Initial_State, _00010, _00100);
  or or_10 (Load___regC, Initial_State, _00101, _00111, _01000);
  or or_11 (Load___flag, Initial_State, _10111);
  or or_12 (Load___equal, Initial_State, _10111, _11101);
  LookUpTable #(.Bits(2)) Select_EqualFlag (.in0(Initial_State), .in1(_11101), .out(select___equal_flag));
  Div #(.Bits(16)) div_1 (.a(mul), .b({{8{1'b0}}, m_t}), .q(div_1_q));  // open: r
  Sub #(.Bits(8)) sub_8 (.a({multiplexer_26_out, accA[1]}), .b(accB), .c_i(1'b0), .s(sub_8_s));  // open: c_o
  Add #(.Bits(8)) add_9 (.a({multiplexer_26_out, accA[1]}), .b(accB), .c_i(1'b0), .s(add_9_s));  // open: c_o
  Multiplexer #(.Bits(8)) multiplexer_27 (.sel(q2), .in_0(sub_8_s), .in_1(add_9_s), .out(multiplexer_27_out));
  and and_6 (Counter___Address, or_5_out, ~busy);  // And
  Register #(.Bits(16)) register_1 (.D(div_1_q), .C(clk), .en(m__eq__n), .Q(out_12));
  or or_13 (load_m___n, subload_M_N, m__lt__n, m__gt__n);
  BitSelector #(.Selector_Bits(3)) bitselector_8 (.in(multiplexer_27_out), .sel(3'b111), .out(q1));
  Sub #(.Bits(8)) sub_9 (.a({multiplexer_27_out[6:0], accA[0]}), .b(accB), .c_i(1'b0), .s(sub_9_s));  // open: c_o
  Add #(.Bits(8)) add_10 (.a({multiplexer_27_out[6:0], accA[0]}), .b(accB), .c_i(1'b0), .s(add_10_s));  // open: c_o
  Mul #(.Bits(8)) mul_2 (.a(startm), .b(startn), .mul(mul_2_mul));
  Multiplexer #(.Bits(8)) multiplexer_28 (.sel(subload_M_N), .in_0(New_m), .in_1(startm), .out(multiplexer_28_out));
  Multiplexer #(.Bits(8)) multiplexer_29 (.sel(subload_M_N), .in_0(New_n), .in_1(startn), .out(multiplexer_29_out));
  Comparator #(.Bits(8)) comparator_2 (.a(m_t), .b(n_t), .gt(m__gt__n), .eq(m__eq__n), .lt(m__lt__n));
  Sub #(.Bits(8)) sub_10 (.a(m_t), .b(n_t), .c_i(1'b0), .s(sub_10_s));  // open: c_o
  Sub #(.Bits(8)) sub_11 (.a(n_t), .b(m_t), .c_i(1'b0), .s(sub_11_s));  // open: c_o
  Multiplexer #(.Bits(8)) multiplexer_30 (.sel(q1), .in_0(sub_9_s), .in_1(add_10_s), .out(multiplexer_30_out));
  or or_14 (or_14_out, greater_flag, equal_flag);
  Multiplexer #(.Selector_Bits(2), .Bits(8)) multiplexer_31 (
    .sel(lookuptable_3_out), .in_0(accA), .in_1({8{1'b0}}), .in_2(out_12[7:0]), .in_3(out_12[15:8]),
    .out(value___rRam));
  or or_15 (select___rRamAddress, _01010, _01011);
  and and_7 (and_7_out, start, Waiting_State);
  or or_16 (load___done, Initial_State, PrintState, start, result, reset);
  and and_8 (and_8_out, _01101, equal_flag);
  and and_9 (and_9_out, _01110, greater_flag);
  and and_10 (and_10_out, _01111, lesser_flag);
  and and_11 (and_11_out, _10000, or_14_out);
  BitSelector #(.Selector_Bits(3)) bitselector_9 (.in(multiplexer_30_out), .sel(3'b111), .out(q0));
  BitExtender #(.inputBits(1), .outputBits(8)) bitextender_1 (.in(m__gt__n), .out(bitextender_1_out));
  BitExtender #(.inputBits(1), .outputBits(8)) bitextender_2 (.in(m__lt__n), .out(bitextender_2_out));
  BitExtender #(.inputBits(1), .outputBits(8)) bitextender_3 (.in(m__gt__n), .out(bitextender_3_out));
  BitExtender #(.inputBits(1), .outputBits(8)) bitextender_4 (.in(m__lt__n), .out(bitextender_4_out));
  Add #(.Bits(8)) add_11 (.a(multiplexer_30_out), .b(accB), .c_i(1'b0), .s(add_11_s));  // open: c_o
  Register #(.Bits(16)) register_2 (.D(mul_2_mul), .C(clk), .en(subload_M_N), .Q(mul));
  Register #(.Bits(8)) register_3 (.D(multiplexer_28_out), .C(clk), .en(load_m___n), .Q(m_t));
  Register #(.Bits(8)) register_4 (.D(multiplexer_29_out), .C(clk), .en(load_m___n), .Q(n_t));
  assign and_12_out = sub_10_s & bitextender_1_out;  // And and_12, 8 bits wide
  assign and_13_out = sub_11_s & bitextender_2_out;  // And and_13, 8 bits wide
  assign and_14_out = n_t & bitextender_3_out;  // And and_14, 8 bits wide
  assign and_15_out = m_t & bitextender_4_out;  // And and_15, 8 bits wide
  LookUpTable #(.Bits(2)) lookuptable_3 (.in0(subLoadE), .in1(subLoadF), .in2(ClearState), .out(lookuptable_3_out));
  or or_17 (load___valid, Initial_State, WaitingResult, _11111, and_7_out, reset);
  or or_18 (jump, and_8_out, and_9_out, _01100, and_10_out, and_11_out);
  Register u_busy (.D(_11110), .C(clk), .en(load___busy), .Q(busy));
  Register #(.Bits(8)) oplc (.D(operand), .C(clk), .en(_11110), .Q({op__4_7, op__0_3}));
  Multiplexer #(.Bits(8)) multiplexer_32 (.sel(q0), .in_0(multiplexer_30_out), .in_1(add_11_s), .out(A___B));
  assign New_m = and_12_out | and_13_out;  // Or or_19, 8 bits wide
  assign New_n = and_14_out | and_15_out;  // Or or_20, 8 bits wide

  // Other names for the same wires on the sheet: sign0 = accA[0]; sign1 = accA[1]; sign2 = accA[2]; sign3 = accA[3];
  //   sign4 = accA[4]; sign5 = accA[5]; sign6 = accA[6]; sign7 = accA[7]; LCM[15:0] = out_12;
  //   OP_FOR_LCM[7:0] = {op__4_7, op__0_3}; _1[3:0] = \output [3:0]; out[7:0] = \output ; _2[3:0] = \output [7:4];
  //   remainder[7:0] = A___B; Select___done = PrintState

  // Notes on the sheet:
  //   Divide && Shifter
  //   Execute
  //   contents of Power (hex, n*v repeats v):
  //   1,7*0,9*1,2,4,8,10,20,40,80,1,3,9,1b,51,f3,d9,8b,1,4,10,40,4*0
  //   ,1,5,19,7d,71,35,9,2d,1,6,24,d8,10,60,40,80,1,7,31,57,61,a7,91
  //   ,f7,0,0,0,1,0,0,0,1,0,1,5*0,1,0,0,0,1,5*0,1,7*0,1,0,0,0,1,0,1
  //   ,0,0,0,1,0,1,0,0,0,1,13*0,1,0,0,0,1,5*0,1,0,1,9*0,1,0,1,5*0,1
  //   ,5*0,1,0,0,0,1,5*0,1,5*0,1,0,1,9*0,1,0,1,0,0,0,1,0,1,11*0,1,11*0
  //   ,1,0,0,0,1,0,1,0,0,0,1,5*0,1,0,1,9*0,1
  //   contents of Prime (hex, n*v repeats v):
  //   0,0,1,1,0,1,0,1,0,0,0,1,0,1,0,0,0,1,0,1,0,0,0,1,5*0,1,0,1,5*0
  //   ,1,0,0,0,1,0,1,0,0,0,1,5*0,1,5*0,1,0,1,5*0,1,0,0,0,1,0,1,5*0,1
  //   ,0,0,0,1,5*0,1,7*0,1,0,0,0,1,0,1,0,0,0,1,0,1,0,0,0,1,13*0,1,0,0,0
  //   ,1,5*0,1,0,1,9*0,1,0,1,5*0,1,5*0,1,0,0,0,1,5*0,1,5*0,1,0,1,9*0
  //   ,1,0,1,0,0,0,1,0,1,11*0,1,11*0,1,0,0,0,1,0,1,0,0,0,1,5*0,1,0,1
  //   ,9*0,1
  //   contents of sqrt (hex, n*v repeats v):
  //   0,1,1,1,5*2,7*3,9*4,11*5,13*6,15*7,17*8,19*9,21*a,23*b,25*c,27*d
  //   ,29*e,31*f
  //   Input / output
  //   Address Management
  //   StateTransition
  //   contents of lookuptable_1 (hex, n*v repeats v):
  //   0,3,2,0,4*1
  //   Member Group SSS
  //   673 30892 21 
  //   ธนกฤต แสงปานแก้ว ( พัฒนาหลักคนที่ 1 และ 2  )
  //   673 31732 21 
  //   พัทธพล สุรินทร์วรางกูร ( ทำสไลด์ )
  //   673 32573 21
  //   ศิวกร แก้วสอาด (  ทำเอกสาร )
  //   ControlUnit
  //   CalculationState
  //   contents of select_accA (hex, n*v repeats v):
  //   0,0,0,1,0,0,2,0,0,3,4,6*0,5,6,7,8,9,a,0,b,c,d,e,f,0,0,0,3
  //   contents of select_accB (hex, n*v repeats v):
  //   4*0,1,27*0,3
  //   contents of select_regC (hex, n*v repeats v):
  //   7*0,1,2,23*0,3
  //   contents of lookuptable_2 (hex, n*v repeats v):
  //   0,2,6*1
  //   contents of Select_EqualFlag (hex, n*v repeats v):
  //   0,1,2
  //   contents of lookuptable_3 (hex, n*v repeats v):
  //   0,3,2,0,12*1
endmodule

/* Test case Jump_Test:
M N progIN reset progLoad start result clk valid done output	
0 0 0 0 0 0 0 0 x x x	
0 0 0 0 0 0 0 1 x x x	
0 0 0 1 0 0 0 0 x x x	
0 0 0 1 0 0 0 1 0 0 0	
0 0 0 0 0 0 0 0 0 0 0	
0 0 0 0 0 0 0 1 0 0 0	
0 0 0 0 0 0 0 0 0 0 0	
0 0 0 0 0 0 0 1 0 0 0	
0 0 0 0 0 0 0 0 0 0 0	
0 0 0 0 0 0 0 1 0 0 0	
0 0 0 0 0 0 0 0 0 0 0	
0 0 0 0 0 0 0 1 0 0 0	
0 0 0 0 0 0 0 0 0 0 0	
0 0 0 0 0 0 0 1 0 0 0	
0 0 0 0 0 0 0 0 0 0 0	
0 0 0 0 0 0 0 1 0 0 0	
0 0 0 0 0 0 0 0 0 0 0	
0 0 0 0 0 0 0 1 0 0 0	
0 0 0 0 0 0 0 0 0 0 0	
0 0 0 0 0 0 0 1 0 0 0	
0 0 0 0 0 0 0 0 0 0 0	
0 0 0 0 0 0 0 1 0 0 0	
0 0 0 0 0 0 0 0 0 0 0	
0 0 0 0 0 0 0 1 0 0 0	
0 0 0 0 0 0 0 0 0 0 0	
0 0 0 0 0 0 0 1 0 0 0	
0 0 0 0 0 0 0 0 0 0 0	
0 0 0 0 0 0 0 1 0 0 0	
0 0 0 0 0 0 0 0 0 0 0	
0 0 0 0 0 0 0 1 0 0 0	
0 0 0 0 0 0 0 0 0 0 0	
0 0 0 0 0 0 0 1 0 0 0	
0 0 0 0 0 0 0 0 0 0 0	
0 0 0 0 0 0 0 1 0 0 0	
0 0 0 0 0 0 0 0 0 0 0	
0 0 0 0 0 0 0 1 0 0 0	
0 0 0 0 0 0 0 0 0 0 0	
0 0 0 0 0 0 0 1 0 0 0	
0 0 0 0 0 0 0 0 0 0 0	
0 0 0 0 0 0 0 1 0 0 0	
0 0 0 0 0 0 0 0 0 0 0	
0 0 0 0 0 0 0 1 0 0 0	
0 0 271 0 1 0 0 0 0 0 0	
0 0 271 0 1 0 0 1 0 0 0	
0 0 566 0 1 0 0 0 0 0 0	
0 0 566 0 1 0 0 1 0 0 0	
0 0 5888 0 1 0 0 0 0 0 0	
0 0 5888 0 1 0 0 1 0 0 0	
0 0 3599 0 1 0 0 0 0 0 0	
0 0 3599 0 1 0 0 1 0 0 0	
0 0 4110 0 1 0 0 0 0 0 0	
0 0 4110 0 1 0 0 1 0 0 0	
0 0 3856 0 1 0 0 0 0 0 0	
0 0 3856 0 1 0 0 1 0 0 0	
0 0 0 0 1 0 0 0 0 0 0	
0 0 0 0 1 0 0 1 0 0 0	
0 0 0 0 1 0 0 0 0 0 0	
0 0 0 0 1 0 0 1 0 0 0	
0 0 0 0 1 0 0 0 0 0 0	
0 0 0 0 1 0 0 1 0 0 0	
0 0 0 0 1 0 0 0 0 0 0	
0 0 0 0 1 0 0 1 0 0 0	
0 0 0 0 1 0 0 0 0 0 0	
0 0 0 0 1 0 0 1 0 0 0	
0 0 0 0 1 0 0 0 0 0 0	
0 0 0 0 1 0 0 1 0 0 0	
0 0 0 0 1 0 0 0 0 0 0	
0 0 0 0 1 0 0 1 0 0 0	
0 0 0 0 1 0 0 0 0 0 0	
0 0 0 0 1 0 0 1 0 0 0	
0 0 0 0 1 0 0 0 0 0 0	
0 0 0 0 1 0 0 1 0 0 0	
0 0 0 0 1 0 0 0 0 0 0	
0 0 0 0 1 0 0 1 0 0 0	
0 0 4352 0 1 0 0 0 0 0 0	
0 0 4352 0 1 0 0 1 0 0 0	
0 0 2819 0 1 0 0 0 0 0 0	
0 0 2819 0 1 0 0 1 0 0 0	
0 0 7936 0 1 0 0 0 0 0 0	
0 0 7936 0 1 0 0 1 0 0 0	
0 0 0 0 1 0 0 0 0 0 0	
0 0 0 0 1 0 0 1 0 0 0	
0 0 0 0 0 0 0 0 0 0 0	
0 0 0 0 0 0 0 1 0 0 0	
0 0 0 0 0 0 0 0 0 0 0	
0 0 0 0 0 0 0 1 0 0 0	
0 0 0 0 0 0 0 0 0 0 0	
0 0 0 0 0 0 0 1 0 0 0	
0 0 0 0 0 1 0 0 0 0 0	
0 0 0 0 0 1 0 1 0 0 0	
0 0 0 0 0 0 0 0 x 0 0	
0 0 0 0 0 0 0 1 x 0 0	
0 0 0 0 0 0 0 0 x 0 0	
0 0 0 0 0 0 0 1 x 0 0	
0 0 0 0 0 0 0 0 x 0 0	
0 0 0 0 0 0 0 1 x 0 0	
0 0 0 0 0 0 0 0 x 0 0	
0 0 0 0 0 0 0 1 x 0 0	
0 0 0 0 0 0 0 0 x 0 0	
0 0 0 0 0 0 0 1 x 0 0	
0 0 0 0 0 0 0 0 x 0 0	
0 0 0 0 0 0 0 1 x 0 0	
0 0 0 0 0 0 0 0 x 0 0	
0 0 0 0 0 0 0 1 x 0 0	
0 0 0 0 0 0 0 0 x 0 0	
0 0 0 0 0 0 0 1 x 0 0	
0 0 0 0 0 0 0 0 x 0 0	
0 0 0 0 0 0 0 1 x 0 0	
0 0 0 0 0 0 0 0 x 0 0	
0 0 0 0 0 0 0 1 x 0 0	
0 0 0 0 0 0 0 0 x 0 0	
0 0 0 0 0 0 0 1 x 0 0	
0 0 0 0 0 0 0 0 x 0 0	
0 0 0 0 0 0 0 1 x 0 0	
0 0 0 0 0 0 0 0 x 0 0	
0 0 0 0 0 0 0 1 x 0 0	
0 0 0 0 0 0 0 0 x 0 0	
0 0 0 0 0 0 0 1 x 0 0	
0 0 0 0 0 0 0 0 x 0 0	
0 0 0 0 0 0 0 1 x 0 0	
0 0 0 0 0 0 0 0 x 0 0	
0 0 0 0 0 0 0 1 x 0 0	
0 0 0 0 0 0 0 0 x 0 0	
0 0 0 0 0 0 0 1 x 0 0	
0 0 0 0 0 0 0 0 x 0 0	
0 0 0 0 0 0 0 1 x 0 0	
0 0 0 0 0 0 0 0 x 0 0	
0 0 0 0 0 0 0 1 x 0 0	
0 0 0 0 0 0 0 0 x 0 0	
0 0 0 0 0 0 0 1 x 0 0	
0 0 0 0 0 0 0 0 x 0 0	
0 0 0 0 0 0 0 1 x 0 0	
0 0 0 0 0 0 0 0 x 0 0	
0 0 0 0 0 0 0 1 x 0 0	
0 0 0 0 0 0 0 0 x 0 0	
0 0 0 0 0 0 0 1 x 0 0	
0 0 0 0 0 0 0 0 x 0 0	
0 0 0 0 0 0 0 1 x 0 0	
0 0 0 0 0 0 0 0 x 0 0	
0 0 0 0 0 0 0 1 x 0 0	
0 0 0 0 0 0 0 0 x 0 0	
0 0 0 0 0 0 0 1 1 0 0	
0 0 0 0 0 0 1 0 1 0 0	
0 0 0 0 0 0 1 1 1 0 0	
0 0 0 0 0 0 0 0 1 0 0	
0 0 0 0 0 0 0 1 1 0 0	
0 0 0 0 0 0 0 0 1 0 0	
0 0 0 0 0 0 0 1 1 0 0	
0 0 0 0 0 0 0 0 1 0 0	
0 0 0 0 0 0 0 1 1 0 69	
0 0 0 0 0 0 0 0 1 0 69	
0 0 0 0 0 0 0 1 1 0 0	
0 0 0 0 0 0 0 0 1 0 0	
0 0 0 0 0 0 0 1 1 0 0	
0 0 0 0 0 0 0 0 1 0 0	
0 0 0 0 0 0 0 1 1 0 0	
0 0 0 0 0 0 0 0 1 0 0	
0 0 0 0 0 0 0 1 1 0 0	
0 0 0 0 0 0 0 0 1 0 0	
0 0 0 0 0 0 0 1 1 0 0	
0 0 0 0 0 0 0 0 1 0 0	
0 0 0 0 0 0 0 1 1 0 0	
0 0 0 0 0 0 0 0 1 0 0	
0 0 0 0 0 0 0 1 1 0 0	
0 0 0 0 0 0 0 0 1 0 0	
0 0 0 0 0 0 0 1 1 0 0	
0 0 0 0 0 0 0 0 1 0 0	
0 0 0 0 0 0 0 1 1 0 0	
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*/

/* Test case rRam_Test:
M N progIN reset progLoad start result clk valid done output
0 0 0 0 0 0 0 0 x x x
0 0 0 0 0 0 0 1 x x x
0 0 0 1 0 0 0 0 x x x
0 0 0 1 0 0 0 1 0 0 0
0 0 0 0 0 0 0 0 0 0 0
0 0 0 0 0 0 0 1 0 0 0
0 0 0 0 0 0 0 0 0 0 0
0 0 0 0 0 0 0 1 0 0 0
0 0 0 0 0 0 0 0 0 0 0
0 0 0 0 0 0 0 1 0 0 0
0 0 0 0 0 0 0 0 0 0 0
0 0 0 0 0 0 0 1 0 0 0
0 0 0 0 0 0 0 0 0 0 0
0 0 0 0 0 0 0 1 0 0 0
0 0 0 0 0 0 0 0 0 0 0
0 0 0 0 0 0 0 1 0 0 0
0 0 0 0 0 0 0 0 0 0 0
0 0 0 0 0 0 0 1 0 0 0
0 0 0 0 0 0 0 0 0 0 0
0 0 0 0 0 0 0 1 0 0 0
0 0 0 0 0 0 0 0 0 0 0
0 0 0 0 0 0 0 1 0 0 0
0 0 0 0 0 0 0 0 0 0 0
0 0 0 0 0 0 0 1 0 0 0
0 0 0 0 0 0 0 0 0 0 0
0 0 0 0 0 0 0 1 0 0 0
0 0 0 0 0 0 0 0 0 0 0
0 0 0 0 0 0 0 1 0 0 0
0 0 0 0 0 0 0 0 0 0 0
0 0 0 0 0 0 0 1 0 0 0
0 0 0 0 0 0 0 0 0 0 0
0 0 0 0 0 0 0 1 0 0 0
0 0 0 0 0 0 0 0 0 0 0
0 0 0 0 0 0 0 1 0 0 0
0 0 0 0 0 0 0 0 0 0 0
0 0 0 0 0 0 0 1 0 0 0
0 0 0 0 0 0 0 0 0 0 0
0 0 0 0 0 0 0 1 0 0 0
0 0 0 0 0 0 0 0 0 0 0
0 0 0 0 0 0 0 1 0 0 0
0 0 0 0 0 0 0 0 0 0 0
0 0 0 0 0 0 0 1 0 0 0
0 0 0 0 0 0 0 0 0 0 0
0 0 0 0 0 0 0 1 0 0 0
0 0 259 0 1 0 0 0 0 0 0
0 0 259 0 1 0 0 1 0 0 0
0 0 2816 0 1 0 0 0 0 0 0
0 0 2816 0 1 0 0 1 0 0 0
0 0 1024 0 1 0 0 0 0 0 0
0 0 1024 0 1 0 0 1 0 0 0
0 0 7168 0 1 0 0 0 0 0 0
0 0 7168 0 1 0 0 1 0 0 0
0 0 2817 0 1 0 0 0 0 0 0
0 0 2817 0 1 0 0 1 0 0 0
0 0 2560 0 1 0 0 0 0 0 0
0 0 2560 0 1 0 0 1 0 0 0
0 0 2831 0 1 0 0 0 0 0 0
0 0 2831 0 1 0 0 1 0 0 0
0 0 7936 0 1 0 0 0 0 0 0
0 0 7936 0 1 0 0 1 0 0 0
0 0 0 0 0 0 0 0 0 0 0
0 0 0 0 0 0 0 1 0 0 0
0 0 0 0 0 1 0 0 0 0 0
0 0 0 0 0 1 0 1 0 0 0
0 0 0 0 0 0 0 0 x 0 0
0 0 0 0 0 0 0 1 x 0 0
0 0 0 0 0 0 0 0 x 0 0
0 0 0 0 0 0 0 1 x 0 0
0 0 0 0 0 0 0 0 x 0 0
0 0 0 0 0 0 0 1 x 0 0
0 0 0 0 0 0 0 0 x 0 0
0 0 0 0 0 0 0 1 x 0 0
0 0 0 0 0 0 0 0 x 0 0
0 0 0 0 0 0 0 1 x 0 0
0 0 0 0 0 0 0 0 x 0 0
0 0 0 0 0 0 0 1 x 0 0
0 0 0 0 0 0 0 0 x 0 0
0 0 0 0 0 0 0 1 x 0 0
0 0 0 0 0 0 0 0 x 0 0
0 0 0 0 0 0 0 1 x 0 0
0 0 0 0 0 0 0 0 x 0 0
0 0 0 0 0 0 0 1 x 0 0
0 0 0 0 0 0 0 0 x 0 0
0 0 0 0 0 0 0 1 x 0 0
0 0 0 0 0 0 0 0 x 0 0
0 0 0 0 0 0 0 1 x 0 0
0 0 0 0 0 0 0 0 x 0 0
0 0 0 0 0 0 0 1 x 0 0
0 0 0 0 0 0 0 0 x 0 0
0 0 0 0 0 0 0 1 x 0 0
0 0 0 0 0 0 0 0 x 0 0
0 0 0 0 0 0 0 1 x 0 0
0 0 0 0 0 0 0 0 x 0 0
0 0 0 0 0 0 0 1 x 0 0
0 0 0 0 0 0 0 0 x 0 0
0 0 0 0 0 0 0 1 x 0 0
0 0 0 0 0 0 0 0 x 0 0
0 0 0 0 0 0 0 1 x 0 0
0 0 0 0 0 0 0 0 x 0 0
0 0 0 0 0 0 0 1 x 0 0
0 0 0 0 0 0 0 0 x 0 0
0 0 0 0 0 0 0 1 x 0 0
0 0 0 0 0 0 0 0 x 0 0
0 0 0 0 0 0 0 1 x 0 0
0 0 0 0 0 0 0 0 x 0 0
0 0 0 0 0 0 0 1 x 0 0
0 0 0 0 0 0 0 0 x 0 0
0 0 0 0 0 0 0 1 x 0 0
0 0 0 0 0 0 0 0 x 0 0
0 0 0 0 0 0 0 1 x 0 0
0 0 0 0 0 0 0 0 x 0 0
0 0 0 0 0 0 0 1 x 0 0
0 0 0 0 0 0 0 0 x 0 0
0 0 0 0 0 0 0 1 x 0 0
0 0 0 0 0 0 0 0 x 0 0
0 0 0 0 0 0 0 1 x 0 0
0 0 0 0 0 0 0 0 x 0 0
0 0 0 0 0 0 0 1 x 0 0
0 0 0 0 0 0 0 0 x 0 0
0 0 0 0 0 0 0 1 x 0 0
0 0 0 0 0 0 0 0 x 0 0
0 0 0 0 0 0 0 1 x 0 0
0 0 0 0 0 0 0 0 x 0 0
0 0 0 0 0 0 0 1 x 0 0
0 0 0 0 0 0 0 0 x 0 0
0 0 0 0 0 0 0 1 x 0 0
0 0 0 0 0 0 0 0 x 0 0
0 0 0 0 0 0 0 1 x 0 0
0 0 0 0 0 0 0 0 x 0 0
0 0 0 0 0 0 0 1 x 0 0
0 0 0 0 0 0 0 0 x 0 0
0 0 0 0 0 0 0 1 x 0 0
0 0 0 0 0 0 0 0 x 0 0
0 0 0 0 0 0 0 1 x 0 0
0 0 0 0 0 0 0 0 x 0 0
0 0 0 0 0 0 0 1 x 0 0
0 0 0 0 0 0 0 0 x 0 0
0 0 0 0 0 0 0 1 x 0 0
0 0 0 0 0 0 0 0 x 0 0
0 0 0 0 0 0 0 1 x 0 0
0 0 0 0 0 0 0 0 x 0 0
0 0 0 0 0 0 0 1 x 0 0
0 0 0 0 0 0 0 0 x 0 0
0 0 0 0 0 0 0 1 x 0 0
0 0 0 0 0 0 0 0 x 0 0
0 0 0 0 0 0 0 1 x 0 0
0 0 0 0 0 0 0 0 x 0 0
0 0 0 0 0 0 0 1 x 0 0
0 0 0 0 0 0 0 0 x 0 0
0 0 0 0 0 0 0 1 x 0 0
0 0 0 0 0 0 0 0 x 0 0
0 0 0 0 0 0 0 1 x 0 0
0 0 0 0 0 0 0 0 x 0 0
0 0 0 0 0 0 0 1 x 0 0
0 0 0 0 0 0 0 0 x 0 0
0 0 0 0 0 0 0 1 x 0 0
0 0 0 0 0 0 0 0 x 0 0
0 0 0 0 0 0 0 1 x 0 0
0 0 0 0 0 0 0 0 x 0 0
0 0 0 0 0 0 0 1 x 0 0
0 0 0 0 0 0 0 0 x 0 0
0 0 0 0 0 0 0 1 x 0 0
0 0 0 0 0 0 0 0 x 0 0
0 0 0 0 0 0 0 1 x 0 0
0 0 0 0 0 0 0 0 x 0 0
0 0 0 0 0 0 0 1 x 0 0
0 0 0 0 0 0 0 0 x 0 0
0 0 0 0 0 0 0 1 x 0 0
0 0 0 0 0 0 0 0 x 0 0
0 0 0 0 0 0 0 1 x 0 0
0 0 0 0 0 0 0 0 x 0 0
0 0 0 0 0 0 0 1 1 0 0
0 0 0 0 0 0 1 0 1 0 0
0 0 0 0 0 0 1 1 1 0 3
0 0 0 0 0 0 0 0 1 0 3
0 0 0 0 0 0 0 1 1 0 24
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*/

/* Test case 01_P01T01:
M N progIN reset progLoad start result clk valid done output	
0 0 0 0 0 0 0 0 0 0 0	
0 0 0 0 0 0 0 1 0 0 0	
0 0 0 1 0 0 0 0 0 0 0	
0 0 0 1 0 0 0 1 0 0 0	
0 0 0 0 0 0 0 0 0 0 0	
0 0 0 0 0 0 0 1 0 0 0	
0 0 0 0 0 0 0 0 0 0 0	
0 0 0 0 0 0 0 1 0 0 0	
0 0 0 0 0 0 0 0 0 0 0	
0 0 0 0 0 0 0 1 0 0 0	
0 0 0 0 0 0 0 0 0 0 0	
0 0 0 0 0 0 0 1 0 0 0	
0 0 0 0 0 0 0 0 0 0 0	
0 0 0 0 0 0 0 1 0 0 0	
0 0 0 0 0 0 0 0 0 0 0	
0 0 0 0 0 0 0 1 0 0 0	
0 0 0 0 0 0 0 0 0 0 0	
0 0 0 0 0 0 0 1 0 0 0	
0 0 0 0 0 0 0 0 0 0 0	
0 0 0 0 0 0 0 1 0 0 0	
0 0 0 0 0 0 0 0 0 0 0	
0 0 0 0 0 0 0 1 0 0 0	
0 0 0 0 0 0 0 0 0 0 0	
0 0 0 0 0 0 0 1 0 0 0	
0 0 0 0 0 0 0 0 0 0 0	
0 0 0 0 0 0 0 1 0 0 0	
0 0 0 0 0 0 0 0 0 0 0	
0 0 0 0 0 0 0 1 0 0 0	
0 0 0 0 0 0 0 0 0 0 0	
0 0 0 0 0 0 0 1 0 0 0	
0 0 0 0 0 0 0 0 0 0 0	
0 0 0 0 0 0 0 1 0 0 0	
0 0 0 0 0 0 0 0 0 0 0	
0 0 0 0 0 0 0 1 0 0 0	
0 0 0 0 0 0 0 0 0 0 0	
0 0 0 0 0 0 0 1 0 0 0	
0 0 0 0 0 0 0 0 0 0 0	
0 0 0 0 0 0 0 1 0 0 0	
0 0 0 0 0 0 0 0 0 0 0	
0 0 0 0 0 0 0 1 0 0 0	
0 0 0 0 0 0 0 0 0 0 0	
0 0 0 0 0 0 0 1 0 0 0	
0 0 271 0 1 0 0 0 0 0 0	
0 0 271 0 1 0 0 1 0 0 0	
0 0 565 0 1 0 0 0 0 0 0	
0 0 565 0 1 0 0 1 0 0 0	
0 0 4352 0 1 0 0 0 0 0 0	
0 0 4352 0 1 0 0 1 0 0 0	
0 0 2819 0 1 0 0 0 0 0 0	
0 0 2819 0 1 0 0 1 0 0 0	
0 0 7936 0 1 0 0 0 0 0 0	
0 0 7936 0 1 0 0 1 0 0 0	
0 0 0 0 0 1 0 0 0 0 0	
0 0 0 0 0 1 0 1 0 0 0	
0 0 0 0 0 0 0 0 x 0 0	
0 0 0 0 0 0 0 1 x 0 0	
0 0 0 0 0 0 0 0 x 0 0	
0 0 0 0 0 0 0 1 x 0 0	
0 0 0 0 0 0 0 0 x 0 0	
0 0 0 0 0 0 0 1 x 0 0	
0 0 0 0 0 0 0 0 x 0 0	
0 0 0 0 0 0 0 1 x 0 0	
0 0 0 0 0 0 0 0 x 0 0	
0 0 0 0 0 0 0 1 x 0 0	
0 0 0 0 0 0 0 0 x 0 0	
0 0 0 0 0 0 0 1 x 0 0	
0 0 0 0 0 0 0 0 x 0 0	
0 0 0 0 0 0 0 1 x 0 0	
0 0 0 0 0 0 0 0 x 0 0	
0 0 0 0 0 0 0 1 x 0 0	
0 0 0 0 0 0 0 0 x 0 0	
0 0 0 0 0 0 0 1 x 0 0	
0 0 0 0 0 0 0 0 x 0 0	
0 0 0 0 0 0 0 1 x 0 0	
0 0 0 0 0 0 0 0 x 0 0	
0 0 0 0 0 0 0 1 x 0 0	
0 0 0 0 0 0 0 0 x 0 0	
0 0 0 0 0 0 0 1 x 0 0	
0 0 0 0 0 0 0 0 x 0 0	
0 0 0 0 0 0 0 1 x 0 0	
0 0 0 0 0 0 0 0 x 0 0	
0 0 0 0 0 0 0 1 x 0 0	
0 0 0 0 0 0 0 0 x 0 0	
0 0 0 0 0 0 0 1 x 0 0	
0 0 0 0 0 0 0 0 x 0 0	
0 0 0 0 0 0 0 1 x 0 0	
0 0 0 0 0 0 0 0 x 0 0	
0 0 0 0 0 0 0 1 x 0 0	
0 0 0 0 0 0 0 0 x 0 0	
0 0 0 0 0 0 0 1 x 0 0	
0 0 0 0 0 0 0 0 x 0 0	
0 0 0 0 0 0 0 1 x 0 0	
0 0 0 0 0 0 0 0 x 0 0	
0 0 0 0 0 0 0 1 x 0 0	
0 0 0 0 0 0 0 0 x 0 0	
0 0 0 0 0 0 0 1 x 0 0	
0 0 0 0 0 0 0 0 x 0 0	
0 0 0 0 0 0 0 1 x 0 0	
0 0 0 0 0 0 0 0 x 0 0	
0 0 0 0 0 0 0 1 x 0 0	
0 0 0 0 0 0 0 0 x 0 0	
0 0 0 0 0 0 0 1 x 0 0	
0 0 0 0 0 0 0 0 x 0 0	
0 0 0 0 0 0 0 1 x 0 0	
0 0 0 0 0 0 0 0 x 0 0	
0 0 0 0 0 0 0 1 1 0 0	
0 0 0 0 0 0 1 0 1 0 0	
0 0 0 0 0 0 1 1 1 0 0	
0 0 0 0 0 0 0 0 1 0 0	
0 0 0 0 0 0 0 1 1 0 0	
0 0 0 0 0 0 0 0 1 0 0	
0 0 0 0 0 0 0 1 1 0 0	
0 0 0 0 0 0 0 0 1 0 0	
0 0 0 0 0 0 0 1 1 0 68	
0 0 0 0 0 0 0 0 1 0 68	
0 0 0 0 0 0 0 1 1 0 0	
0 0 0 0 0 0 0 0 1 0 0	
0 0 0 0 0 0 0 1 1 0 0	
0 0 0 0 0 0 0 0 1 0 0	
0 0 0 0 0 0 0 1 1 0 0	
0 0 0 0 0 0 0 0 1 0 0	
0 0 0 0 0 0 0 1 1 0 0	
0 0 0 0 0 0 0 0 1 0 0	
0 0 0 0 0 0 0 1 1 0 0	
0 0 0 0 0 0 0 0 1 0 0	
0 0 0 0 0 0 0 1 1 0 0	
0 0 0 0 0 0 0 0 1 0 0	
0 0 0 0 0 0 0 1 1 0 0	
0 0 0 0 0 0 0 0 1 0 0	
0 0 0 0 0 0 0 1 1 0 0	
0 0 0 0 0 0 0 0 1 0 0	
0 0 0 0 0 0 0 1 1 0 0	
0 0 0 0 0 0 0 0 1 0 0	
0 0 0 0 0 0 0 1 1 0 0	
0 0 0 0 0 0 0 0 1 0 0	
0 0 0 0 0 0 0 1 1 0 0	
0 0 0 0 0 0 0 0 1 0 0	
0 0 0 0 0 0 0 1 1 0 0	
0 0 0 0 0 0 0 0 1 0 0	
0 0 0 0 0 0 0 1 1 1 0	
0 0 0 0 0 0 0 0 1 1 0	
0 0 0 0 0 0 0 1 1 1 0	
0 0 0 0 0 0 0 0 1 1 0	
*/

/* Test case TripleJump_Test:
M N progIN reset progLoad start result clk valid done output
0 0 0 0 0 0 0 0 x x x
0 0 0 0 0 0 0 1 x x x
0 0 0 1 0 0 0 0 x x x
0 0 0 1 0 0 0 1 0 0 0
0 0 0 0 0 0 0 0 0 0 0
0 0 0 0 0 0 0 1 0 0 0
0 0 0 0 0 0 0 0 0 0 0
0 0 0 0 0 0 0 1 0 0 0
0 0 0 0 0 0 0 0 0 0 0
0 0 0 0 0 0 0 1 0 0 0
0 0 0 0 0 0 0 0 0 0 0
0 0 0 0 0 0 0 1 0 0 0
0 0 0 0 0 0 0 0 0 0 0
0 0 0 0 0 0 0 1 0 0 0
0 0 0 0 0 0 0 0 0 0 0
0 0 0 0 0 0 0 1 0 0 0
0 0 0 0 0 0 0 0 0 0 0
0 0 0 0 0 0 0 1 0 0 0
0 0 0 0 0 0 0 0 0 0 0
0 0 0 0 0 0 0 1 0 0 0
0 0 0 0 0 0 0 0 0 0 0
0 0 0 0 0 0 0 1 0 0 0
0 0 0 0 0 0 0 0 0 0 0
0 0 0 0 0 0 0 1 0 0 0
0 0 0 0 0 0 0 0 0 0 0
0 0 0 0 0 0 0 1 0 0 0
0 0 0 0 0 0 0 0 0 0 0
0 0 0 0 0 0 0 1 0 0 0
0 0 0 0 0 0 0 0 0 0 0
0 0 0 0 0 0 0 1 0 0 0
0 0 0 0 0 0 0 0 0 0 0
0 0 0 0 0 0 0 1 0 0 0
0 0 0 0 0 0 0 0 0 0 0
0 0 0 0 0 0 0 1 0 0 0
0 0 0 0 0 0 0 0 0 0 0
0 0 0 0 0 0 0 1 0 0 0
0 0 0 0 0 0 0 0 0 0 0
0 0 0 0 0 0 0 1 0 0 0
0 0 0 0 0 0 0 0 0 0 0
0 0 0 0 0 0 0 1 0 0 0
0 0 0 0 0 0 0 0 0 0 0
0 0 0 0 0 0 0 1 0 0 0
0 0 0 0 0 0 0 0 0 0 0
0 0 0 0 0 0 0 1 0 0 0
0 0 271 0 1 0 0 0 0 0 0
0 0 271 0 1 0 0 1 0 0 0
0 0 565 0 1 0 0 0 0 0 0
0 0 565 0 1 0 0 1 0 0 0
0 0 5888 0 1 0 0 0 0 0 0
0 0 5888 0 1 0 0 1 0 0 0
0 0 3845 0 1 0 0 0 0 0 0
0 0 3845 0 1 0 0 1 0 0 0
0 0 4352 0 1 0 0 0 0 0 0
0 0 4352 0 1 0 0 1 0 0 0
0 0 3847 0 1 0 0 0 0 0 0
0 0 3847 0 1 0 0 1 0 0 0
0 0 4352 0 1 0 0 0 0 0 0
0 0 4352 0 1 0 0 1 0 0 0
0 0 4107 0 1 0 0 0 0 0 0
0 0 4107 0 1 0 0 1 0 0 0
0 0 1024 0 1 0 0 0 0 0 0
0 0 1024 0 1 0 0 1 0 0 0
0 0 5888 0 1 0 0 0 0 0 0
0 0 5888 0 1 0 0 1 0 0 0
0 0 3331 0 1 0 0 0 0 0 0
0 0 3331 0 1 0 0 1 0 0 0
0 0 2819 0 1 0 0 0 0 0 0
0 0 2819 0 1 0 0 1 0 0 0
0 0 7936 0 1 0 0 0 0 0 0
0 0 7936 0 1 0 0 1 0 0 0
0 0 0 0 0 0 0 0 0 0 0
0 0 0 0 0 0 0 1 0 0 0
0 0 0 0 0 1 0 0 0 0 0
0 0 0 0 0 1 0 1 0 0 0
0 0 0 0 0 0 0 0 x 0 0
0 0 0 0 0 0 0 1 x 0 0
0 0 0 0 0 0 0 0 x 0 0
0 0 0 0 0 0 0 1 x 0 0
0 0 0 0 0 0 0 0 x 0 0
0 0 0 0 0 0 0 1 x 0 0
0 0 0 0 0 0 0 0 x 0 0
0 0 0 0 0 0 0 1 x 0 0
0 0 0 0 0 0 0 0 x 0 0
0 0 0 0 0 0 0 1 x 0 0
0 0 0 0 0 0 0 0 x 0 0
0 0 0 0 0 0 0 1 x 0 0
0 0 0 0 0 0 0 0 x 0 0
0 0 0 0 0 0 0 1 x 0 0
0 0 0 0 0 0 0 0 x 0 0
0 0 0 0 0 0 0 1 x 0 0
0 0 0 0 0 0 0 0 x 0 0
0 0 0 0 0 0 0 1 x 0 0
0 0 0 0 0 0 0 0 x 0 0
0 0 0 0 0 0 0 1 x 0 0
0 0 0 0 0 0 0 0 x 0 0
0 0 0 0 0 0 0 1 x 0 0
0 0 0 0 0 0 0 0 x 0 0
0 0 0 0 0 0 0 1 x 0 0
0 0 0 0 0 0 0 0 x 0 0
0 0 0 0 0 0 0 1 x 0 0
0 0 0 0 0 0 0 0 x 0 0
0 0 0 0 0 0 0 1 x 0 0
0 0 0 0 0 0 0 0 x 0 0
0 0 0 0 0 0 0 1 x 0 0
0 0 0 0 0 0 0 0 x 0 0
0 0 0 0 0 0 0 1 x 0 0
0 0 0 0 0 0 0 0 x 0 0
0 0 0 0 0 0 0 1 x 0 0
0 0 0 0 0 0 0 0 x 0 0
0 0 0 0 0 0 0 1 x 0 0
0 0 0 0 0 0 0 0 x 0 0
0 0 0 0 0 0 0 1 x 0 0
0 0 0 0 0 0 0 0 x 0 0
0 0 0 0 0 0 0 1 x 0 0
0 0 0 0 0 0 0 0 x 0 0
0 0 0 0 0 0 0 1 x 0 0
0 0 0 0 0 0 0 0 x 0 0
0 0 0 0 0 0 0 1 x 0 0
0 0 0 0 0 0 0 0 x 0 0
0 0 0 0 0 0 0 1 x 0 0
0 0 0 0 0 0 0 0 x 0 0
0 0 0 0 0 0 0 1 x 0 0
0 0 0 0 0 0 0 0 x 0 0
0 0 0 0 0 0 0 1 x 0 0
0 0 0 0 0 0 0 0 x 0 0
0 0 0 0 0 0 0 1 x 0 0
0 0 0 0 0 0 0 0 x 0 0
0 0 0 0 0 0 0 1 x 0 0
0 0 0 0 0 0 0 0 x 0 0
0 0 0 0 0 0 0 1 x 0 0
0 0 0 0 0 0 0 0 x 0 0
0 0 0 0 0 0 0 1 x 0 0
0 0 0 0 0 0 0 0 x 0 0
0 0 0 0 0 0 0 1 x 0 0
0 0 0 0 0 0 0 0 x 0 0
0 0 0 0 0 0 0 1 x 0 0
0 0 0 0 0 0 0 0 x 0 0
0 0 0 0 0 0 0 1 x 0 0
0 0 0 0 0 0 0 0 x 0 0
0 0 0 0 0 0 0 1 x 0 0
0 0 0 0 0 0 0 0 x 0 0
0 0 0 0 0 0 0 1 x 0 0
0 0 0 0 0 0 0 0 x 0 0
0 0 0 0 0 0 0 1 x 0 0
0 0 0 0 0 0 0 0 x 0 0
0 0 0 0 0 0 0 1 x 0 0
0 0 0 0 0 0 0 0 x 0 0
0 0 0 0 0 0 0 1 x 0 0
0 0 0 0 0 0 0 0 x 0 0
0 0 0 0 0 0 0 1 x 0 0
0 0 0 0 0 0 0 0 x 0 0
0 0 0 0 0 0 0 1 x 0 0
0 0 0 0 0 0 0 0 x 0 0
0 0 0 0 0 0 0 1 x 0 0
0 0 0 0 0 0 0 0 x 0 0
0 0 0 0 0 0 0 1 x 0 0
0 0 0 0 0 0 0 0 x 0 0
0 0 0 0 0 0 0 1 x 0 0
0 0 0 0 0 0 0 0 x 0 0
0 0 0 0 0 0 0 1 x 0 0
0 0 0 0 0 0 0 0 x 0 0
0 0 0 0 0 0 0 1 x 0 0
0 0 0 0 0 0 0 0 x 0 0
0 0 0 0 0 0 0 1 x 0 0
0 0 0 0 0 0 0 0 x 0 0
0 0 0 0 0 0 0 1 x 0 0
0 0 0 0 0 0 0 0 x 0 0
0 0 0 0 0 0 0 1 x 0 0
0 0 0 0 0 0 0 0 x 0 0
0 0 0 0 0 0 0 1 x 0 0
0 0 0 0 0 0 0 0 x 0 0
0 0 0 0 0 0 0 1 x 0 0
0 0 0 0 0 0 0 0 x 0 0
0 0 0 0 0 0 0 1 x 0 0
0 0 0 0 0 0 0 0 x 0 0
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*/

/* Test case Arithmatic_Test:
M N progIN reset progLoad start result clk valid done output
0 0 0 0 0 0 0 0 x x x
0 0 0 0 0 0 0 1 x x x
0 0 0 1 0 0 0 0 x x x
0 0 0 1 0 0 0 1 0 0 0
0 0 0 0 0 0 0 0 0 0 0
0 0 0 0 0 0 0 1 0 0 0
0 0 0 0 0 0 0 0 0 0 0
0 0 0 0 0 0 0 1 0 0 0
0 0 0 0 0 0 0 0 0 0 0
0 0 0 0 0 0 0 1 0 0 0
0 0 0 0 0 0 0 0 0 0 0
0 0 0 0 0 0 0 1 0 0 0
0 0 0 0 0 0 0 0 0 0 0
0 0 0 0 0 0 0 1 0 0 0
0 0 0 0 0 0 0 0 0 0 0
0 0 0 0 0 0 0 1 0 0 0
0 0 0 0 0 0 0 0 0 0 0
0 0 0 0 0 0 0 1 0 0 0
0 0 0 0 0 0 0 0 0 0 0
0 0 0 0 0 0 0 1 0 0 0
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*/

/* Test case 02_P01T2:
M N progIN reset progLoad start result clk valid done output
0 0 0 0 0 0 0 0 x x x
0 0 0 0 0 0 0 1 x x x
0 0 0 1 0 0 0 0 x x x
0 0 0 1 0 0 0 1 0 0 0
0 0 0 0 0 0 0 0 0 0 0
0 0 0 0 0 0 0 1 0 0 0
0 0 0 0 0 0 0 0 0 0 0
0 0 0 0 0 0 0 1 0 0 0
0 0 0 0 0 0 0 0 0 0 0
0 0 0 0 0 0 0 1 0 0 0
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*/

/* Test case pRam_Test:
M N progIN reset progLoad start result clk valid done output	
0 0 0 0 0 0 0 0 x x x	
0 0 0 0 0 0 0 1 x x x	
0 0 0 1 0 0 0 0 x x x	
0 0 0 1 0 0 0 1 0 0 0	
0 0 0 0 0 0 0 0 0 0 0	
0 0 0 0 0 0 0 1 0 0 0	
0 0 0 0 0 0 0 0 0 0 0	
0 0 0 0 0 0 0 1 0 0 0	
0 0 0 0 0 0 0 0 0 0 0	
0 0 0 0 0 0 0 1 0 0 0	
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*/

/* Test case Super_Test:
M N progIN reset progLoad start result clk valid done output
0 0 0 0 0 0 0 0 x x x
0 0 0 0 0 0 0 1 x x x
0 0 0 1 0 0 0 0 x x x
0 0 0 1 0 0 0 1 0 0 0
0 0 0 0 0 0 0 0 0 0 0
0 0 0 0 0 0 0 1 0 0 0
0 0 0 0 0 0 0 0 0 0 0
0 0 0 0 0 0 0 1 0 0 0
0 0 0 0 0 0 0 0 0 0 0
0 0 0 0 0 0 0 1 0 0 0
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*/

/* Test case 03_P02T1:
M N progIN reset progLoad start result clk valid done output
0 0 0 0 0 0 0 0 x x x
0 0 0 0 0 0 0 1 x x x
0 0 0 1 0 0 0 0 x x x
0 0 0 1 0 0 0 1 0 0 0
0 0 0 0 0 0 0 0 0 0 0
0 0 0 0 0 0 0 1 0 0 0
0 0 0 0 0 0 0 0 0 0 0
0 0 0 0 0 0 0 1 0 0 0
0 0 0 0 0 0 0 0 0 0 0
0 0 0 0 0 0 0 1 0 0 0
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*/

/* Test case Prime_Test:
M N progIN reset progLoad start result clk valid done output
0 0 0 0 0 0 0 0 x x x
0 0 0 0 0 0 0 1 x x x
0 0 0 1 0 0 0 0 x x x
0 0 0 1 0 0 0 1 0 0 0
0 0 0 0 0 0 0 0 0 0 0
0 0 0 0 0 0 0 1 0 0 0
0 0 0 0 0 0 0 0 0 0 0
0 0 0 0 0 0 0 1 0 0 0
0 0 0 0 0 0 0 0 0 0 0
0 0 0 0 0 0 0 1 0 0 0
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*/

/* Test case ResultAgain_Test:
M N progIN reset progLoad start result clk valid done output
0 0 0 0 0 0 0 0 x x x
0 0 0 0 0 0 0 1 x x x
0 0 0 1 0 0 0 0 x x x
0 0 0 1 0 0 0 1 0 0 0
0 0 0 0 0 0 0 0 0 0 0
0 0 0 0 0 0 0 1 0 0 0
0 0 0 0 0 0 0 0 0 0 0
0 0 0 0 0 0 0 1 0 0 0
0 0 0 0 0 0 0 0 0 0 0
0 0 0 0 0 0 0 1 0 0 0
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*/

/* Test case 04_P03T1:
M N progIN reset progLoad start result clk valid done output
0 0 0 0 0 0 0 0 x x x
0 0 0 0 0 0 0 1 x x x
0 0 0 1 0 0 0 0 x x x
0 0 0 1 0 0 0 1 0 0 0
0 0 0 0 0 0 0 0 0 0 0
0 0 0 0 0 0 0 1 0 0 0
0 0 0 0 0 0 0 0 0 0 0
0 0 0 0 0 0 0 1 0 0 0
0 0 0 0 0 0 0 0 0 0 0
0 0 0 0 0 0 0 1 0 0 0
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*/

/* Test case Comment19_Test:
M N progIN reset progLoad start result clk valid done output
0 0 0 0 0 0 0 0 x x x
0 0 0 0 0 0 0 1 x x x
0 0 0 1 0 0 0 0 x x x
0 0 0 1 0 0 0 1 0 0 0
0 0 0 0 0 0 0 0 0 0 0
0 0 0 0 0 0 0 1 0 0 0
0 0 0 0 0 0 0 0 0 0 0
0 0 0 0 0 0 0 1 0 0 0
0 0 0 0 0 0 0 0 0 0 0
0 0 0 0 0 0 0 1 0 0 0
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*/

/* Test case StartAgain_Test:
M N progIN reset progLoad start result clk valid done output
0 0 0 0 0 0 0 0 x x x
0 0 0 0 0 0 0 1 x x x
0 0 0 1 0 0 0 0 x x x
0 0 0 1 0 0 0 1 0 0 0
0 0 0 0 0 0 0 0 0 0 0
0 0 0 0 0 0 0 1 0 0 0
0 0 0 0 0 0 0 0 0 0 0
0 0 0 0 0 0 0 1 0 0 0
0 0 0 0 0 0 0 0 0 0 0
0 0 0 0 0 0 0 1 0 0 0
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*/

/* Test case 05_P04T01:
M N progIN reset progLoad start result clk valid done output
0 0 0 0 0 0 0 0 x x x
0 0 0 0 0 0 0 1 x x x
0 0 0 1 0 0 0 0 x x x
0 0 0 1 0 0 0 1 0 0 x
0 0 0 0 0 0 0 0 0 0 x
0 0 0 0 0 0 0 1 0 0 x
0 0 0 0 0 0 0 0 0 0 x
0 0 0 0 0 0 0 1 0 0 x
0 0 0 0 0 0 0 0 0 0 x
0 0 0 0 0 0 0 1 0 0 x
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*/

/* Test case NewWorld_Test:
M N progIN reset progLoad start result clk valid done output
0 0 0 0 0 0 0 0 x x x
0 0 0 0 0 0 0 1 x x x
0 0 0 1 0 0 0 0 x x x
0 0 0 1 0 0 0 1 0 0 0
0 0 0 0 0 0 0 0 0 0 0
0 0 0 0 0 0 0 1 0 0 0
0 0 0 0 0 0 0 0 0 0 0
0 0 0 0 0 0 0 1 0 0 0
0 0 0 0 0 0 0 0 0 0 0
0 0 0 0 0 0 0 1 0 0 0
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*/

/* Test case 06_P05T1:
M N progIN reset progLoad start result clk valid done output
0 0 0 0 0 0 0 0 x x x
0 0 0 0 0 0 0 1 x x x
0 0 0 1 0 0 0 0 x x x
0 0 0 1 0 0 0 1 0 0 x
0 0 0 0 0 0 0 0 0 0 x
0 0 0 0 0 0 0 1 0 0 x
0 0 0 0 0 0 0 0 0 0 x
0 0 0 0 0 0 0 1 0 0 x
0 0 0 0 0 0 0 0 0 0 x
0 0 0 0 0 0 0 1 0 0 x
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*/

/* Test case 07_P06T1:
M N progIN reset progLoad start result clk valid done output
0 0 0 0 0 0 0 0 x x x
0 0 0 0 0 0 0 1 x x x
0 0 0 1 0 0 0 0 x x x
0 0 0 1 0 0 0 1 0 0 x
0 0 0 0 0 0 0 0 0 0 x
0 0 0 0 0 0 0 1 0 0 x
0 0 0 0 0 0 0 0 0 0 x
0 0 0 0 0 0 0 1 0 0 x
0 0 0 0 0 0 0 0 0 0 x
0 0 0 0 0 0 0 1 0 0 x
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*/

/* Test case LCM:
M N progIN reset progLoad start result clk valid done output
0 0 0 0 0 0 0 0 x x x
0 0 0 0 0 0 0 1 x x x
0 0 0 1 0 0 0 0 x x x
0 0 0 1 0 0 0 1 0 0 x
0 0 0 0 0 0 0 0 0 0 x
0 0 0 0 0 0 0 1 0 0 x
0 0 0 0 0 0 0 0 0 0 x
0 0 0 0 0 0 0 1 0 0 x
0 0 0 0 0 0 0 0 0 0 x
0 0 0 0 0 0 0 1 0 0 x
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*/

/* Test case LCM 2:
M N progIN reset progLoad start result clk valid done output
0 0 0 0 0 0 0 0 x x x
0 0 0 0 0 0 0 1 x x x
0 0 0 1 0 0 0 0 x x x
0 0 0 1 0 0 0 1 0 0 x
0 0 0 0 0 0 0 0 0 0 x
0 0 0 0 0 0 0 1 0 0 x
0 0 0 0 0 0 0 0 0 0 x
0 0 0 0 0 0 0 1 0 0 x
0 0 0 0 0 0 0 0 0 0 x
0 0 0 0 0 0 0 1 0 0 x
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*/
