// Digital circuit DateToDay_NoSimplify.dig as structural Verilog
module DateToDay_NoSimplify (
  input  _8,
  input  Leap,
  input  _4,
  input  _2,
  input  _1,
  input  in_10,
  output D29,
  output D28,
  output D30,
  output D31
);

  wire and_3_out, and_4_out, and_5_out, and_6_out, and_7_out, and_8_out, and_9_out, and_10_out, and_11_out,
       and_12_out, and_13_out, not_1_out, not_2_out, not_3_out, not_4_out, not_5_out, not_6_out, not_7_out,
       not_8_out, not_9_out, not_10_out, not_11_out, not_12_out, not_13_out, not_14_out, not_15_out;

  not not_1 (not_1_out, _8);
  not not_2 (not_2_out, _4);
  not not_3 (not_3_out, _1);
  not not_4 (not_4_out, Leap);
  not not_5 (not_5_out, _8);
  not not_6 (not_6_out, _4);
  not not_7 (not_7_out, _1);
  and and_1 (D28, not_1_out, not_2_out, _2, not_3_out, not_4_out);
  and and_2 (D29, not_5_out, not_6_out, _2, not_7_out, Leap);
  and and_3 (and_3_out, _8, not_9_out, _2, _1);
  and and_4 (and_4_out, _8, not_9_out, not_10_out, _1);
  or or_1 (D30, and_6_out, and_5_out, and_4_out, and_3_out);
  and and_5 (and_5_out, not_8_out, _4, _2, not_11_out);
  and and_6 (and_6_out, not_8_out, _4, not_10_out, not_11_out);
  or or_2 (D31, and_13_out, and_12_out, and_11_out, and_10_out, and_9_out, and_8_out, and_7_out);
  not not_8 (not_8_out, _8);
  not not_9 (not_9_out, _4);
  not not_10 (not_10_out, _2);
  not not_11 (not_11_out, _1);
  and and_7 (and_7_out, _1, not_13_out, not_14_out, not_15_out);
  and and_8 (and_8_out, _1, _2, not_14_out, not_15_out);
  and and_9 (and_9_out, _1, not_13_out, _4, not_15_out);
  and and_10 (and_10_out, _1, _2, _4, not_15_out);
  and and_11 (and_11_out, not_14_out, not_13_out, not_12_out, _8);
  and and_12 (and_12_out, not_12_out, _2, not_14_out, _8);
  and and_13 (and_13_out, not_12_out, not_13_out, _4, _8);
  not not_12 (not_12_out, _1);
  not not_13 (not_13_out, _2);
  not not_14 (not_14_out, _4);
  not not_15 (not_15_out, _8);

  // Other names for the same wires on the sheet: t1 = _1; t2 = _2; t4 = _4; t8 = _8; tLeap = Leap
endmodule
