// Digital circuit Register.dig as structural Verilog
module Register (
  input  clk,
  input  in_2,
  output out_3,
  output out_4,
  output out_5,
  output out_6
);

  D_FF d_ff_1 (.D(in_2), .C(clk), .Q(out_3));  // open: nQ
  D_FF d_ff_2 (.D(out_3), .C(clk), .Q(out_4));  // open: nQ
  D_FF d_ff_3 (.D(out_4), .C(clk), .Q(out_5));  // open: nQ
  D_FF d_ff_4 (.D(out_5), .C(clk));  // open: Q, nQ

  assign out_6 = in_2;
endmodule
