// Digital circuit Shifter.dig as structural Verilog
module Shifter (
  input  [7:0] in_1,
  input  [7:0] in_2,
  output [7:0] out_3,
  output [7:0] out_4
);

  BarrelShifter #(.Bits(8)) barrelshifter_1 (.in(in_1), .shift({1'b0, in_2[2:0]}), .out(out_3));
  Multiplexer #(.Bits(8), .Selector_Bits(3)) multiplexer_1 (
    .sel(in_2[2:0]), .in_0(in_1), .in_1({in_1[6:0], 1'b0}), .in_2({in_1[5:0], 2'b00}),
    .in_3({in_1[4:0], 3'b000}), .in_4({in_1[3:0], 4'b0000}), .in_5({in_1[2:0], {5{1'b0}}}),
    .in_6({in_1[1:0], {6{1'b0}}}), .in_7({in_1[0], {7{1'b0}}}), .out(out_4));
endmodule
