// Digital circuit addsubtract.dig as structural Verilog
module addsubtract (
  input  [7:0] in_1,
  input  [7:0] in_2,
  output [7:0] out_3
);

  Mul #(.Bits(3)) mul_1 (.a(in_1[2:0]), .b(in_2[2:0]), .mul(out_3[5:0]));

  assign out_3[7:6] = 2'b00;
endmodule
