// Digital circuit non_Restoring_Divide.dig as structural Verilog
module non_Restoring_Divide (
  input  [7:0] in_1,
  input  [7:0] in_2,
  output [7:0] out_3,
  output [7:0] out_4,
  output [7:0] out_5,
  output [7:0] out_6
);

  wire bitselector_1_out, q0, q1, q2, q3, q4, q5, q6, q7;
  wire [7:0] add_1_s, add_2_s, add_3_s, add_4_s, add_5_s, add_6_s, add_7_s, add_8_s, add_9_s,
       multiplexer_1_out, multiplexer_2_out, multiplexer_3_out, multiplexer_4_out, multiplexer_5_out,
       multiplexer_6_out, multiplexer_7_out, multiplexer_8_out, sub_1_s, sub_2_s, sub_3_s, sub_4_s, sub_5_s,
       sub_6_s, sub_7_s, sub_8_s;

  BitSelector #(.Selector_Bits(3)) bitselector_1 (.in({8{1'b0}}), .sel(3'b111), .out(bitselector_1_out));
  Div #(.Bits(8)) div_1 (.a(in_1), .b(in_2), .q(out_3), .r(out_4));
  Sub #(.Bits(8)) sub_1 (.a({{7{1'b0}}, in_1[7]}), .b(in_2), .c_i(1'b0), .s(sub_1_s));  // open: c_o
  Add #(.Bits(8)) add_1 (.a({{7{1'b0}}, in_1[7]}), .b(in_2), .c_i(1'b0), .s(add_1_s));  // open: c_o
  assign out_5 = ~{q7, q6, q5, q4, q3, q2, q1, q0};  // Not not_1, 8 bits wide
  Multiplexer #(.Bits(8)) multiplexer_1 (
    .sel(bitselector_1_out), .in_0(sub_1_s), .in_1(add_1_s), .out(multiplexer_1_out));
  BitSelector #(.Selector_Bits(3)) bitselector_2 (.in(multiplexer_1_out), .sel(3'b111), .out(q7));
  Sub #(.Bits(8)) sub_2 (.a({multiplexer_1_out[6:0], in_1[6]}), .b(in_2), .c_i(1'b0), .s(sub_2_s));  // open: c_o
  Add #(.Bits(8)) add_2 (.a({multiplexer_1_out[6:0], in_1[6]}), .b(in_2), .c_i(1'b0), .s(add_2_s));  // open: c_o
  Multiplexer #(.Bits(8)) multiplexer_2 (.sel(q7), .in_0(sub_2_s), .in_1(add_2_s), .out(multiplexer_2_out));
  BitSelector #(.Selector_Bits(3)) bitselector_3 (.in(multiplexer_2_out), .sel(3'b111), .out(q6));
  Sub #(.Bits(8)) sub_3 (.a({multiplexer_2_out[6:0], in_1[5]}), .b(in_2), .c_i(1'b0), .s(sub_3_s));  // open: c_o
  Add #(.Bits(8)) add_3 (.a({multiplexer_2_out[6:0], in_1[5]}), .b(in_2), .c_i(1'b0), .s(add_3_s));  // open: c_o
  Multiplexer #(.Bits(8)) multiplexer_3 (.sel(q6), .in_0(sub_3_s), .in_1(add_3_s), .out(multiplexer_3_out));
  BitSelector #(.Selector_Bits(3)) bitselector_4 (.in(multiplexer_3_out), .sel(3'b111), .out(q5));
  Sub #(.Bits(8)) sub_4 (.a({multiplexer_3_out[6:0], in_1[4]}), .b(in_2), .c_i(1'b0), .s(sub_4_s));  // open: c_o
  Add #(.Bits(8)) add_4 (.a({multiplexer_3_out[6:0], in_1[4]}), .b(in_2), .c_i(1'b0), .s(add_4_s));  // open: c_o
  Multiplexer #(.Bits(8)) multiplexer_4 (.sel(q5), .in_0(sub_4_s), .in_1(add_4_s), .out(multiplexer_4_out));
  BitSelector #(.Selector_Bits(3)) bitselector_5 (.in(multiplexer_4_out), .sel(3'b111), .out(q4));
  Sub #(.Bits(8)) sub_5 (.a({multiplexer_4_out[6:0], in_1[3]}), .b(in_2), .c_i(1'b0), .s(sub_5_s));  // open: c_o
  Add #(.Bits(8)) add_5 (.a({multiplexer_4_out[6:0], in_1[3]}), .b(in_2), .c_i(1'b0), .s(add_5_s));  // open: c_o
  Multiplexer #(.Bits(8)) multiplexer_5 (.sel(q4), .in_0(sub_5_s), .in_1(add_5_s), .out(multiplexer_5_out));
  BitSelector #(.Selector_Bits(3)) bitselector_6 (.in(multiplexer_5_out), .sel(3'b111), .out(q3));
  Sub #(.Bits(8)) sub_6 (.a({multiplexer_5_out[6:0], in_1[2]}), .b(in_2), .c_i(1'b0), .s(sub_6_s));  // open: c_o
  Add #(.Bits(8)) add_6 (.a({multiplexer_5_out[6:0], in_1[2]}), .b(in_2), .c_i(1'b0), .s(add_6_s));  // open: c_o
  Multiplexer #(.Bits(8)) multiplexer_6 (.sel(q3), .in_0(sub_6_s), .in_1(add_6_s), .out(multiplexer_6_out));
  BitSelector #(.Selector_Bits(3)) bitselector_7 (.in(multiplexer_6_out), .sel(3'b111), .out(q2));
  Sub #(.Bits(8)) sub_7 (.a({multiplexer_6_out[6:0], in_1[1]}), .b(in_2), .c_i(1'b0), .s(sub_7_s));  // open: c_o
  Add #(.Bits(8)) add_7 (.a({multiplexer_6_out[6:0], in_1[1]}), .b(in_2), .c_i(1'b0), .s(add_7_s));  // open: c_o
  Multiplexer #(.Bits(8)) multiplexer_7 (.sel(q2), .in_0(sub_7_s), .in_1(add_7_s), .out(multiplexer_7_out));
  BitSelector #(.Selector_Bits(3)) bitselector_8 (.in(multiplexer_7_out), .sel(3'b111), .out(q1));
  Sub #(.Bits(8)) sub_8 (.a({multiplexer_7_out[6:0], in_1[0]}), .b(in_2), .c_i(1'b0), .s(sub_8_s));  // open: c_o
  Add #(.Bits(8)) add_8 (.a({multiplexer_7_out[6:0], in_1[0]}), .b(in_2), .c_i(1'b0), .s(add_8_s));  // open: c_o
  Multiplexer #(.Bits(8)) multiplexer_8 (.sel(q1), .in_0(sub_8_s), .in_1(add_8_s), .out(multiplexer_8_out));
  BitSelector #(.Selector_Bits(3)) bitselector_9 (.in(multiplexer_8_out), .sel(3'b111), .out(q0));
  Add #(.Bits(8)) add_9 (.a(multiplexer_8_out), .b(in_2), .c_i(1'b0), .s(add_9_s));  // open: c_o
  Multiplexer #(.Bits(8)) multiplexer_9 (.sel(q0), .in_0(multiplexer_8_out), .in_1(add_9_s), .out(out_6));

  // Other names for the same wires on the sheet: M[7:0] = in_2; Q[7:0] = in_1; sign0 = in_1[0]; sign1 = in_1[1];
  //   sign2 = in_1[2]; sign3 = in_1[3]; sign4 = in_1[4]; sign5 = in_1[5]; sign6 = in_1[6]; sign7 = in_1[7];
  //   remainder[7:0] = out_6
endmodule
