// Digital circuit power.dig as structural Verilog
module power (
  input  [2:0] A,
  input  [2:0] B,
  input  clk,
  input  reset,
  input  start,
  output [7:0] out_4
);

  wire and_1_out, Cal, eq__eq__B, load___ans, multiplexer_2_out, multiplexer_3_out, not_1_out, not_2_out,
       not_3_out, Q1, Q2, resetWait, Wait;
  wire [2:0] counter_1_out;
  wire [7:0] multiplexer_1_out;
  wire [15:0] mul_1_mul;

  Mul #(.Bits(8)) mul_1 (.a(out_4), .b({{5{1'b0}}, A}), .mul(mul_1_mul));
  not not_1 (not_1_out, reset);
  not not_2 (not_2_out, eq__eq__B);
  Multiplexer #(.Bits(8)) multiplexer_1 (.sel(Cal), .in_0(8'h1), .in_1(mul_1_mul[7:0]), .out(multiplexer_1_out));
  Decoder #(.Selector_Bits(2)) decoder_1 (.sel({Q1, Q2}), .out_0(Wait), .out_1(Cal), .out_2(resetWait));  // open: out_3
  Multiplexer #(.Selector_Bits(2)) multiplexer_2 (
    .sel({Q1, Q2}), .in_0(1'b0), .in_1(eq__eq__B), .in_2(not_1_out), .in_3(1'b0), .out(multiplexer_2_out));
  Multiplexer #(.Selector_Bits(2)) multiplexer_3 (
    .sel({Q1, Q2}), .in_0(start), .in_1(not_2_out), .in_2(1'b0), .in_3(1'b0), .out(multiplexer_3_out));
  D_FF d_ff_1 (.D(multiplexer_2_out), .C(clk), .Q(Q1));  // open: nQ
  D_FF d_ff_2 (.D(multiplexer_3_out), .C(clk), .Q(Q2));  // open: nQ
  and and_1 (and_1_out, load___ans, not_3_out);
  not not_3 (not_3_out, eq__eq__B);
  Register #(.Bits(8)) register_1 (.D(multiplexer_1_out), .C(clk), .en(and_1_out), .Q(out_4));
  Counter #(.Bits(3)) counter_1 (.en(Cal), .C(clk), .clr(Wait), .out(counter_1_out));  // open: ovf
  or or_1 (load___ans, Wait, Cal);
  Comparator #(.Bits(3)) comparator_1 (.a(counter_1_out), .b(B), .eq(eq__eq__B));  // open: gt, lt

  // Other names for the same wires on the sheet: ans[7:0] = out_4

  // Notes on the sheet:
  //   clk: Hz: 10
endmodule
