// Digital circuit q.dig as structural Verilog
module q (
  input  [15:0] A,
  input  clk,
  input  \input ,
  input  reset,
  output [15:0] mean,
  output busy
);

  wire CalState, load___sum, q1, resetState;
  wire [31:0] add_1_s, multiplexer_1_out, n, sum;
  wire [31:16] div_1_q;

  D_FF_AS d_ff_as_1 (.Set(1'b0), .D(1'b1), .C(clk), .Clr(reset), .Q(q1));  // open: nQ
  Decoder decoder_1 (.sel(q1), .out_0(resetState), .out_1(CalState));
  Div #(.Bits(32)) div_1 (.a(sum), .b(n), .q({div_1_q, mean}));  // open: r
  Add #(.Bits(32)) add_1 (.a(sum), .b({{16{1'b0}}, A}), .c_i(1'b0), .s(add_1_s));  // open: c_o
  or or_1 (load___sum, \input , resetState);
  Multiplexer #(.Bits(32)) multiplexer_1 (.sel(resetState), .in_0(add_1_s), .in_1({32{1'b0}}), .out(multiplexer_1_out));
  Register #(.Bits(32)) u_sum (.D(multiplexer_1_out), .C(clk), .en(load___sum), .Q(sum));
  Counter #(.Bits(32)) u_n (.en(\input ), .C(clk), .clr(resetState), .out(n));  // open: ovf

  assign busy = 1'b0;

  // Other names for the same wires on the sheet: A_t[15:0] = A
endmodule
