// Digital circuit Full_Adder.dig as structural Verilog
module Full_Adder (
  input  A,
  input  B,
  input  Cin,
  output Cout,
  output Sum
);

  wire _7400_1_pin3, _7400_1_pin6, _7400_1_pin8, _7400_1_pin10, _7400_2_pin1, _7400_2_pin3, _7400_2_pin5;

  _7400 _7400_1 (
    .pin1(A), .pin2(B), .pin3(_7400_1_pin3), .pin4(A), .pin5(_7400_1_pin3), .pin6(_7400_1_pin6), .pin7(1'b0),
    .pin8(_7400_1_pin8), .pin9(_7400_1_pin6), .pin10(_7400_1_pin10), .pin11(_7400_1_pin10), .pin12(B),
    .pin13(_7400_1_pin3), .pin14(1'b1));
  _7400 _7400_2 (
    .pin1(_7400_2_pin1), .pin2(Cin), .pin3(_7400_2_pin3), .pin4(_7400_2_pin3), .pin5(_7400_2_pin5),
    .pin6(Sum), .pin7(1'b0), .pin8(_7400_2_pin5), .pin9(_7400_1_pin8), .pin10(_7400_2_pin1),
    .pin11(_7400_2_pin1), .pin12(Cin), .pin13(_7400_1_pin8), .pin14(1'b1));
  _7400 _7400_3 (
    .pin1(_7400_2_pin1), .pin2(_7400_1_pin3), .pin3(Cout), .pin4(1'b0), .pin5(1'b0), .pin7(1'b0),
    .pin9(1'b0), .pin10(1'b0), .pin12(1'b0), .pin13(1'b0), .pin14(1'b1));  // open: pin6, pin8, pin11

  // Other names for the same wires on the sheet: c = Cin
endmodule

/* Test case Test1:
A B Cin Sum Cout
0 0 0 0 0
0 0 1 1 0
0 1 0 1 0
0 1 1 0 1
1 0 0 1 0
1 0 1 0 1
1 1 0 0 1
1 1 1 1 1
*/
