// Digital circuit Half_Adder.dig as structural Verilog
module Half_Adder (
  input  in_1,
  input  in_2,
  output Sum,
  output Cout
);

  wire _7400_1_pin3, _7400_1_pin6, _7400_1_pin10;

  _7400 _7400_1 (
    .pin1(in_1), .pin2(in_2), .pin3(_7400_1_pin3), .pin4(in_1), .pin5(_7400_1_pin3), .pin6(_7400_1_pin6),
    .pin7(1'b0), .pin8(Sum), .pin9(_7400_1_pin6), .pin10(_7400_1_pin10), .pin11(_7400_1_pin10), .pin12(in_2),
    .pin13(_7400_1_pin3), .pin14(1'b1));
  _7400 _7400_2 (
    .pin1(_7400_1_pin3), .pin2(_7400_1_pin3), .pin3(Cout), .pin4(1'b0), .pin5(1'b0), .pin7(1'b0),
    .pin9(1'b0), .pin10(1'b0), .pin12(1'b0), .pin13(1'b0), .pin14(1'b1));  // open: pin6, pin8, pin11

  // Other names for the same wires on the sheet: a = in_1; b = in_2
endmodule
