// Digital circuit Template.dig as structural Verilog
module Template (
  input  X0,
  input  X1,
  input  Selector,
  output Z
);

  wire and_1_out, and_2_out, not_1_out;

  not not_1 (not_1_out, Selector);
  and and_1 (and_1_out, not_1_out, X0);
  and and_2 (and_2_out, X1, Selector);
  or or_1 (Z, and_1_out, and_2_out);
endmodule
