// Digital circuit New_Template-01.dig as structural Verilog
module New_Template_01 (
  input  [3:0] In,
  output A,
  output B,
  output C,
  output D,
  output E,
  output F,
  output G
);

  Multiplexer #(.Bits(7), .Selector_Bits(4)) multiplexer_1 (
    .sel(In), .in_0(7'b1111110), .in_1(7'b0110000), .in_2(7'b1101101), .in_3(7'b1111001), .in_4(7'b0110011),
    .in_5(7'b1011011), .in_6(7'b1011111), .in_7(7'b1110010), .in_8({7{1'b1}}), .in_9(7'b1111011),
    .in_10(7'b1111110), .in_11(7'b1111110), .in_12(7'b1111110), .in_13(7'b1111110), .in_14(7'b1111110),
    .in_15(7'b1111110), .out({A, B, C, D, E, F, G}));
  Seven_Seg seven_seg_1 (.a(A), .b(B), .c(C), .d(D), .e(E), .f(F), .g(G), .dp(1'b0));
endmodule
