// Digital circuit New_Template-02.dig as structural Verilog
module New_Template_02 (
  input  [2:0] In,
  input  clk,
  output [7:0] Z
);

  wire [6:6] a;

  Multiplexer #(.Bits(8), .Selector_Bits(3)) multiplexer_1 (
    .sel(In), .in_0({1'b0, a[6], 3'b000, a[6], 2'b00}), .in_1({1'b0, {2{a[6]}}, 1'b0, a[6], 2'b00, a[6]}),
    .in_2({1'b0, {2{a[6]}}, 2'b00, {3{a[6]}}}), .in_3({1'b0, a[6], 2'b00, {2{a[6]}}, 2'b00}),
    .in_4({1'b0, {2{a[6]}}, 1'b0, {4{a[6]}}}), .in_5({1'b0, a[6], 2'b00, {2{a[6]}}, 2'b00}),
    .in_6({1'b0, {2{a[6]}}, 4'b0000, a[6]}), .in_7({1'b0, {2{a[6]}}, 3'b000, a[6], 1'b0}), .out(Z));
  not not_1 (a[6], 1'b0);
  Terminal terminal_1 (.D(Z), .C(clk), .en(1'b1));

  // Other names for the same wires on the sheet: a (some bits) = {2{a[6]}}; b (some bits) = {3{a[6]}};
  //   D (some bits) = {2{a[6]}}; g (some bits) = {5{a[6]}}; i (some bits) = {4{a[6]}}; L (some bits) = {3{a[6]}};
  //   o (some bits) = {6{a[6]}}
endmodule
