// Digital circuit New_Template-03.dig as structural Verilog
module New_Template_03 (
  input  [1:0] Selector,
  input  [3:0] In,
  output [3:0] Output
);

  wire [3:0] _2_4_2_1_code_out, _6_4_2__3_code_out, cyclic_out, excess_3_out;

  LookUpTable #(.Bits(4)) excess_3 (.in0(In[0]), .in1(In[1]), .in2(In[2]), .in3(In[3]), .out(excess_3_out));
  LookUpTable #(.Bits(4)) cyclic (.in0(In[0]), .in1(In[1]), .in2(In[2]), .in3(In[3]), .out(cyclic_out));
  LookUpTable #(.Bits(4)) _2_4_2_1_code (.in0(In[0]), .in1(In[1]), .in2(In[2]), .in3(In[3]), .out(_2_4_2_1_code_out));
  LookUpTable #(.Bits(4)) _6_4_2__3_code (.in0(In[0]), .in1(In[1]), .in2(In[2]), .in3(In[3]), .out(_6_4_2__3_code_out));
  Multiplexer #(.Selector_Bits(2), .Bits(4)) multiplexer_1 (
    .sel(Selector), .in_0(excess_3_out), .in_1(cyclic_out), .in_2(_2_4_2_1_code_out),
    .in_3(_6_4_2__3_code_out), .out(Output));

  // Other names for the same wires on the sheet: input[3:0] = In; o1[3:0] = Output; slt[1:0] = Selector

  // Notes on the sheet:
  //   contents of excess_3 (hex, n*v repeats v):
  //   3,4,5,6,7,8,9,a,b,c
  //   contents of cyclic (hex, n*v repeats v):
  //   0,1,3,2,6,7,5,4,c,d
  //   contents of _2_4_2_1_code (hex, n*v repeats v):
  //   0,1,2,3,4,b,c,d,e,f
  //   contents of _6_4_2__3_code (hex, n*v repeats v):
  //   0,5,2,9,4,b,6,d,a,f
endmodule
