// Digital circuit New_Template-04.dig as structural Verilog
module New_Template_04 (
  input  [6:0] In,
  output [6:0] Output
);

  wire C1, C2, C3;
  wire [0:0] _000_0001;
  wire [1:1] _000_0010;
  wire [2:2] _000_0100;
  wire [3:3] _000_1000;
  wire [4:4] _001_0000;
  wire [5:5] _010_0000;
  wire [6:6] _100_0000;

  xor xor_1 (C1, In[0], In[1], In[2], In[3]);
  xor xor_2 (C2, In[0], In[1], In[4], In[5]);
  xor xor_3 (C3, In[0], In[2], In[4], In[6]);
  not not_1 (_100_0000[6], In[6]);
  not not_2 (_010_0000[5], In[5]);
  not not_3 (_001_0000[4], In[4]);
  not not_4 (_000_1000[3], In[3]);
  not not_5 (_000_0100[2], In[2]);
  not not_6 (_000_0010[1], In[1]);
  not not_7 (_000_0001[0], In[0]);
  Multiplexer #(.Bits(7), .Selector_Bits(3)) multiplexer_1 (
    .sel({C1, C2, C3}), .in_0(In), .in_1({_100_0000[6], In[5:0]}), .in_2({In[6], _010_0000[5], In[4:0]}),
    .in_3({In[6:5], _001_0000[4], In[3:0]}), .in_4({In[6:4], _000_1000[3], In[2:0]}),
    .in_5({In[6:3], _000_0100[2], In[1:0]}), .in_6({In[6:2], _000_0010[1], In[0]}),
    .in_7({In[6:1], _000_0001[0]}), .out(Output));

  // Other names for the same wires on the sheet: _000_0000[6:0] = In; _000_0010 (some bits) = {In[6:2], In[0]};
  //   _000_0100 (some bits) = {In[6:3], In[1:0]}; _000_1000 (some bits) = {In[6:4], In[2:0]};
  //   _001_0000 (some bits) = {In[6:5], In[3:0]}; _010_0000 (some bits) = {In[6], In[4:0]}; _100_0000[5:0] = In[5:0];
  //   m4 = In[0]; _000_0001[6:1] = In[6:1]; m3 = In[1]; m2 = In[2]; p3 = In[3]; m1 = In[4]; p2 = In[5]; p1 = In[6];
  //   out[6:0] = Output
endmodule
