// Digital circuit Template-03.dig as structural Verilog
module Template_03 (
  input  [1:0] Selector,
  input  [3:0] In,
  output [3:0] Output
);

  wire not_2_out, not_3_out, not_4_out, not_5_out, not_6_out, not_7_out, not_8_out;
  wire [0:0] _0001;
  wire [3:0] and_15_out, and_16_out, and_17_out, and_18_out, and_19_out, and_20_out, and_21_out, and_22_out,
       and_23_out, and_24_out, and_25_out, and_26_out, and_27_out, and_28_out, and_29_out, and_30_out,
       and_31_out, and_32_out, and_33_out, and_34_out, and_35_out, and_36_out, and_37_out, and_38_out,
       and_39_out, and_40_out, and_41_out, and_42_out, and_43_out, and_44_out, and_45_out, and_46_out,
       and_47_out, and_48_out, and_49_out, and_50_out, and_51_out, and_52_out, and_53_out, and_54_out,
       and_55_out, and_56_out, or_1_out, or_2_out, or_3_out, or_4_out, or_5_out, or_6_out, or_7_out,
       or_8_out, or_9_out, or_10_out, or_11_out, or_12_out, or_13_out, or_14_out, or_15_out, or_16_out,
       or_17_out, or_18_out, or_19_out;
  wire [3:3] _642_3, _2421c, and_1_out, and_2_out, and_3_out, and_4_out, and_5_out, and_6_out, and_7_out,
       and_8_out, and_9_out, and_10_out, cyclic, exc_3;

  not not_1 (_0001[0], 1'b0);
  not not_2 (not_2_out, In[3]);
  not not_3 (not_3_out, In[2]);
  not not_4 (not_4_out, In[1]);
  not not_5 (not_5_out, In[0]);
  and and_1 (and_1_out[3], not_5_out, not_4_out, not_3_out, not_2_out);
  and and_2 (and_2_out[3], In[0], not_4_out, not_3_out, not_2_out);
  and and_3 (and_3_out[3], not_5_out, In[1], not_3_out, not_2_out);
  and and_4 (and_4_out[3], In[0], In[1], not_3_out, not_2_out);
  and and_5 (and_5_out[3], not_5_out, not_4_out, In[2], not_2_out);
  and and_6 (and_6_out[3], In[0], not_4_out, In[2], not_2_out);
  and and_7 (and_7_out[3], not_5_out, In[1], In[2], not_2_out);
  and and_8 (and_8_out[3], In[0], In[1], In[2], not_2_out);
  and and_9 (and_9_out[3], In[3], not_3_out, not_4_out, not_5_out);
  and and_10 (and_10_out[3], In[0], not_4_out, not_3_out, In[3]);
  not not_6 (not_6_out, Selector[0]);
  not not_7 (not_7_out, and_2_out[3]);
  not not_8 (not_8_out, Selector[1]);
  and and_11 (exc_3[3], not_6_out, not_8_out);
  and and_12 (cyclic[3], Selector[0], not_8_out);
  and and_13 (_2421c[3], not_6_out, Selector[1]);
  and and_14 (_642_3[3], Selector[0], Selector[1]);
  assign or_1_out = {4{cyclic[3]}} | {4{_2421c[3]}} | {4{_642_3[3]}};  // Or or_1, 4 bits wide
  assign or_2_out = {4{cyclic[3]}} | {4{_2421c[3]}};  // Or or_2, 4 bits wide
  assign or_3_out = {4{_2421c[3]}} | {4{_642_3[3]}};  // Or or_3, 4 bits wide
  assign or_4_out = {4{_2421c[3]}} | {4{_642_3[3]}};  // Or or_4, 4 bits wide
  assign or_5_out = {4{_2421c[3]}} | {4{_642_3[3]}};  // Or or_5, 4 bits wide
  assign or_6_out = {4{_2421c[3]}} | {4{_642_3[3]}};  // Or or_6, 4 bits wide
  assign or_7_out = {4{_2421c[3]}} | {4{_642_3[3]}};  // Or or_7, 4 bits wide
  assign and_15_out = 4'b0000 & or_1_out;  // And and_15, 4 bits wide
  assign and_16_out = {2'b00, {2{_0001[0]}}} & {4{exc_3[3]}};  // And and_16, 4 bits wide
  assign and_17_out = {1'b0, _0001[0], 2'b00} & {4{exc_3[3]}};  // And and_17, 4 bits wide
  assign and_18_out = {3'b000, _0001[0]} & or_2_out;  // And and_18, 4 bits wide
  assign and_19_out = {1'b0, _0001[0], 1'b0, _0001[0]} & {4{_642_3[3]}};  // And and_19, 4 bits wide
  assign and_20_out = {1'b0, _0001[0], 1'b0, _0001[0]} & {4{exc_3[3]}};  // And and_20, 4 bits wide
  assign and_21_out = {2'b00, {2{_0001[0]}}} & {4{cyclic[3]}};  // And and_21, 4 bits wide
  assign and_22_out = {2'b00, _0001[0], 1'b0} & or_3_out;  // And and_22, 4 bits wide
  assign and_23_out = {1'b0, {2{_0001[0]}}, 1'b0} & {4{exc_3[3]}};  // And and_23, 4 bits wide
  assign and_24_out = {2'b00, _0001[0], 1'b0} & {4{cyclic[3]}};  // And and_24, 4 bits wide
  assign and_25_out = {2'b00, {2{_0001[0]}}} & {4{_2421c[3]}};  // And and_25, 4 bits wide
  assign and_26_out = {_0001[0], 2'b00, _0001[0]} & {4{_642_3[3]}};  // And and_26, 4 bits wide
  assign and_27_out = {1'b0, {3{_0001[0]}}} & {4{exc_3[3]}};  // And and_27, 4 bits wide
  assign and_28_out = {1'b0, {2{_0001[0]}}, 1'b0} & {4{cyclic[3]}};  // And and_28, 4 bits wide
  assign and_29_out = {1'b0, _0001[0], 2'b00} & or_4_out;  // And and_29, 4 bits wide
  assign and_30_out = {_0001[0], 3'b000} & {4{exc_3[3]}};  // And and_30, 4 bits wide
  assign and_31_out = {1'b0, {3{_0001[0]}}} & {4{cyclic[3]}};  // And and_31, 4 bits wide
  assign and_32_out = {_0001[0], 1'b0, {2{_0001[0]}}} & or_5_out;  // And and_32, 4 bits wide
  assign and_33_out = {_0001[0], 2'b00, _0001[0]} & {4{exc_3[3]}};  // And and_33, 4 bits wide
  assign and_34_out = {1'b0, _0001[0], 1'b0, _0001[0]} & {4{cyclic[3]}};  // And and_34, 4 bits wide
  assign and_35_out = {{2{_0001[0]}}, 2'b00} & {4{_2421c[3]}};  // And and_35, 4 bits wide
  assign and_36_out = {1'b0, {2{_0001[0]}}, 1'b0} & {4{_642_3[3]}};  // And and_36, 4 bits wide
  assign and_37_out = {_0001[0], 1'b0, _0001[0], 1'b0} & {4{exc_3[3]}};  // And and_37, 4 bits wide
  assign and_38_out = {1'b0, _0001[0], 2'b00} & {4{cyclic[3]}};  // And and_38, 4 bits wide
  assign and_39_out = {{2{_0001[0]}}, 1'b0, _0001[0]} & or_6_out;  // And and_39, 4 bits wide
  assign and_40_out = {_0001[0], 1'b0, {2{_0001[0]}}} & {4{exc_3[3]}};  // And and_40, 4 bits wide
  assign and_41_out = {{2{_0001[0]}}, 2'b00} & {4{cyclic[3]}};  // And and_41, 4 bits wide
  assign and_42_out = {{3{_0001[0]}}, 1'b0} & {4{_2421c[3]}};  // And and_42, 4 bits wide
  assign and_43_out = {_0001[0], 1'b0, _0001[0], 1'b0} & {4{_642_3[3]}};  // And and_43, 4 bits wide
  assign and_44_out = {{2{_0001[0]}}, 2'b00} & {4{exc_3[3]}};  // And and_44, 4 bits wide
  assign and_45_out = {{2{_0001[0]}}, 1'b0, _0001[0]} & {4{cyclic[3]}};  // And and_45, 4 bits wide
  assign and_46_out = {4{_0001[0]}} & or_7_out;  // And and_46, 4 bits wide
  assign or_8_out = and_15_out | and_16_out;  // Or or_8, 4 bits wide
  assign or_9_out = and_17_out | and_18_out | and_19_out;  // Or or_9, 4 bits wide
  assign or_10_out = and_20_out | and_21_out | and_22_out;  // Or or_10, 4 bits wide
  assign or_11_out = and_23_out | and_24_out | and_25_out | and_26_out;  // Or or_11, 4 bits wide
  assign or_12_out = and_27_out | and_28_out | and_29_out;  // Or or_12, 4 bits wide
  assign or_13_out = and_30_out | and_31_out | and_32_out;  // Or or_13, 4 bits wide
  assign or_14_out = and_33_out | and_34_out | and_35_out | and_36_out;  // Or or_14, 4 bits wide
  assign or_15_out = and_37_out | and_38_out | and_39_out;  // Or or_15, 4 bits wide
  assign or_16_out = and_40_out | and_41_out | and_42_out | and_43_out;  // Or or_16, 4 bits wide
  assign or_17_out = and_44_out | and_45_out | and_46_out;  // Or or_17, 4 bits wide
  assign and_47_out = or_8_out & {4{and_1_out[3]}};  // And and_47, 4 bits wide
  assign and_48_out = or_9_out & {4{and_2_out[3]}};  // And and_48, 4 bits wide
  assign and_49_out = or_10_out & {4{and_3_out[3]}};  // And and_49, 4 bits wide
  assign and_50_out = or_11_out & {4{and_4_out[3]}};  // And and_50, 4 bits wide
  assign and_51_out = or_12_out & {4{and_5_out[3]}};  // And and_51, 4 bits wide
  assign and_52_out = or_13_out & {4{and_6_out[3]}};  // And and_52, 4 bits wide
  assign and_53_out = or_14_out & {4{and_7_out[3]}};  // And and_53, 4 bits wide
  assign and_54_out = or_15_out & {4{and_8_out[3]}};  // And and_54, 4 bits wide
  assign and_55_out = or_16_out & {4{and_9_out[3]}};  // And and_55, 4 bits wide
  assign and_56_out = or_17_out & {4{and_10_out[3]}};  // And and_56, 4 bits wide
  assign or_18_out = and_47_out | and_48_out | and_49_out | and_50_out | and_51_out;  // Or or_18, 4 bits wide
  assign or_19_out = and_52_out | and_53_out | and_54_out | and_55_out | and_56_out;  // Or or_19, 4 bits wide
  assign Output = or_18_out | or_19_out;  // Or or_20, 4 bits wide

  // Other names for the same wires on the sheet: exc_3[2:0] = {3{exc_3[3]}}; cyclic[2:0] = {3{cyclic[3]}};
  //   _2421c[2:0] = {3{_2421c[3]}}; _642_3[2:0] = {3{_642_3[3]}}; _0010[1] = _0001[0]; _0011[1:0] = {2{_0001[0]}};
  //   _0100[2] = _0001[0]; _0101 (some bits) = {2{_0001[0]}}; _0110[2:1] = {2{_0001[0]}}; _0111[2:0] = {3{_0001[0]}};
  //   _1000[3] = _0001[0]; _1001 (some bits) = {2{_0001[0]}}; _1010 (some bits) = {2{_0001[0]}};
  //   _1011 (some bits) = {3{_0001[0]}}; _1100[3:2] = {2{_0001[0]}}; _1101 (some bits) = {3{_0001[0]}};
  //   _1110[3:1] = {3{_0001[0]}}; _1111[3:0] = {4{_0001[0]}}; input[3:0] = In; o1[3:0] = Output; slt[1:0] = Selector
endmodule
