// Digital circuit Template-04.dig as structural Verilog
module Template_04 (
  input  [6:0] In,
  output [6:0] Output,
  output [6:0] out_3
);

  wire bit0, bit1, bit2, not_2_out, not_3_out, not_4_out;
  wire [6:0] and_9_out, and_10_out, and_11_out, and_12_out, and_13_out, and_14_out, and_15_out, and_16_out,
       and_17_out, and_18_out, and_19_out, and_20_out, and_21_out, and_22_out, and_23_out, and_24_out,
       and_25_out, and_26_out, and_27_out, and_28_out, and_29_out, and_30_out, and_31_out, and_32_out,
       and_33_out, and_34_out, and_35_out, and_36_out, and_37_out, not_5_out, not_6_out, not_7_out,
       not_8_out, not_9_out, not_10_out, not_11_out, or_1_out, or_2_out, or_3_out, or_4_out, or_5_out,
       or_6_out, or_7_out, or_22_out, or_23_out, or_24_out, or_25_out, or_26_out, or_27_out, or_28_out,
       xor_4_out, xor_5_out, xor_6_out, xor_7_out, xor_8_out, xor_9_out, xor_10_out, xor_11_out, xor_12_out,
       xor_13_out, xor_14_out, xor_15_out, xor_16_out, xor_17_out;
  wire [6:6] and_1_out, and_2_out, and_3_out, and_4_out, and_5_out, and_6_out, and_7_out, and_8_out,
       or_8_out, or_9_out, or_10_out, or_11_out, or_12_out, or_13_out, or_14_out, or_15_out, or_16_out,
       or_17_out, or_18_out, or_19_out, or_20_out, or_21_out;

  not not_1 (out_3[6], 1'b0);
  xor xor_1 (bit2, In[0], In[1], In[2], In[3]);
  not not_2 (not_2_out, bit2);
  xor xor_2 (bit1, In[0], In[1], In[4], In[5]);
  not not_3 (not_3_out, bit1);
  not not_4 (not_4_out, bit0);
  xor xor_3 (bit0, In[0], In[2], In[4], In[6]);
  and and_1 (and_1_out[6], not_4_out, not_3_out, not_2_out);
  and and_2 (and_2_out[6], bit0, not_3_out, not_2_out);
  and and_3 (and_3_out[6], not_4_out, bit1, not_2_out);
  and and_4 (and_4_out[6], bit0, bit1, not_2_out);
  and and_5 (and_5_out[6], not_4_out, not_3_out, bit2);
  and and_6 (and_6_out[6], bit0, not_3_out, bit2);
  and and_7 (and_7_out[6], not_4_out, bit1, bit2);
  and and_8 (and_8_out[6], bit0, bit1, bit2);
  assign not_5_out = ~{out_3[6], {6{1'b0}}};  // Not not_5, 7 bits wide
  assign not_6_out = ~{1'b0, out_3[6], {5{1'b0}}};  // Not not_6, 7 bits wide
  assign not_7_out = ~{2'b00, out_3[6], 4'b0000};  // Not not_7, 7 bits wide
  assign not_8_out = ~{3'b000, out_3[6], 3'b000};  // Not not_8, 7 bits wide
  assign not_9_out = ~{4'b0000, out_3[6], 2'b00};  // Not not_9, 7 bits wide
  assign not_10_out = ~{{5{1'b0}}, out_3[6], 1'b0};  // Not not_10, 7 bits wide
  assign not_11_out = ~{{6{1'b0}}, out_3[6]};  // Not not_11, 7 bits wide
  assign and_9_out = In & not_5_out;  // And and_9, 7 bits wide
  assign or_1_out = {out_3[6], {6{1'b0}}} | In;  // Or or_1, 7 bits wide
  assign and_10_out = In & not_6_out;  // And and_10, 7 bits wide
  assign or_2_out = {1'b0, out_3[6], {5{1'b0}}} | In;  // Or or_2, 7 bits wide
  assign and_11_out = In & not_7_out;  // And and_11, 7 bits wide
  assign or_3_out = {2'b00, out_3[6], 4'b0000} | In;  // Or or_3, 7 bits wide
  assign and_12_out = In & not_8_out;  // And and_12, 7 bits wide
  assign or_4_out = {3'b000, out_3[6], 3'b000} | In;  // Or or_4, 7 bits wide
  assign and_13_out = In & not_9_out;  // And and_13, 7 bits wide
  assign or_5_out = {4'b0000, out_3[6], 2'b00} | In;  // Or or_5, 7 bits wide
  assign and_14_out = In & not_10_out;  // And and_14, 7 bits wide
  assign or_6_out = {{5{1'b0}}, out_3[6], 1'b0} | In;  // Or or_6, 7 bits wide
  assign and_15_out = In & not_11_out;  // And and_15, 7 bits wide
  assign or_7_out = {{6{1'b0}}, out_3[6]} | In;  // Or or_7, 7 bits wide
  assign xor_4_out = In ^ and_9_out;  // XOr xor_4, 7 bits wide
  assign xor_5_out = In ^ or_1_out;  // XOr xor_5, 7 bits wide
  assign xor_6_out = In ^ and_10_out;  // XOr xor_6, 7 bits wide
  assign xor_7_out = In ^ or_2_out;  // XOr xor_7, 7 bits wide
  assign xor_8_out = In ^ and_11_out;  // XOr xor_8, 7 bits wide
  assign xor_9_out = In ^ or_3_out;  // XOr xor_9, 7 bits wide
  assign xor_10_out = In ^ and_12_out;  // XOr xor_10, 7 bits wide
  assign xor_11_out = In ^ or_4_out;  // XOr xor_11, 7 bits wide
  assign xor_12_out = In ^ and_13_out;  // XOr xor_12, 7 bits wide
  assign xor_13_out = In ^ or_5_out;  // XOr xor_13, 7 bits wide
  assign xor_14_out = In ^ and_14_out;  // XOr xor_14, 7 bits wide
  assign xor_15_out = In ^ or_6_out;  // XOr xor_15, 7 bits wide
  assign xor_16_out = In ^ and_15_out;  // XOr xor_16, 7 bits wide
  assign xor_17_out = In ^ or_7_out;  // XOr xor_17, 7 bits wide
  assign and_16_out = In & {7{and_1_out[6]}};  // And and_16, 7 bits wide
  or or_8 (or_8_out[6], xor_4_out[0], xor_4_out[1], xor_4_out[2], xor_4_out[3], xor_4_out[4], xor_4_out[5], xor_4_out[6]);
  or or_9 (or_9_out[6], xor_5_out[0], xor_5_out[1], xor_5_out[2], xor_5_out[3], xor_5_out[4], xor_5_out[5], xor_5_out[6]);
  or or_10 (or_10_out[6], xor_6_out[0], xor_6_out[1], xor_6_out[2], xor_6_out[3], xor_6_out[4], xor_6_out[5], xor_6_out[6]);
  or or_11 (or_11_out[6], xor_7_out[0], xor_7_out[1], xor_7_out[2], xor_7_out[3], xor_7_out[4], xor_7_out[5], xor_7_out[6]);
  or or_12 (or_12_out[6], xor_8_out[0], xor_8_out[1], xor_8_out[2], xor_8_out[3], xor_8_out[4], xor_8_out[5], xor_8_out[6]);
  or or_13 (or_13_out[6], xor_9_out[0], xor_9_out[1], xor_9_out[2], xor_9_out[3], xor_9_out[4], xor_9_out[5], xor_9_out[6]);
  or or_14 (or_14_out[6], xor_10_out[0], xor_10_out[1], xor_10_out[2], xor_10_out[3], xor_10_out[4], xor_10_out[5], xor_10_out[6]);
  or or_15 (or_15_out[6], xor_11_out[0], xor_11_out[1], xor_11_out[2], xor_11_out[3], xor_11_out[4], xor_11_out[5], xor_11_out[6]);
  or or_16 (or_16_out[6], xor_12_out[0], xor_12_out[1], xor_12_out[2], xor_12_out[3], xor_12_out[4], xor_12_out[5], xor_12_out[6]);
  or or_17 (or_17_out[6], xor_13_out[0], xor_13_out[1], xor_13_out[2], xor_13_out[3], xor_13_out[4], xor_13_out[5], xor_13_out[6]);
  or or_18 (or_18_out[6], xor_14_out[0], xor_14_out[1], xor_14_out[2], xor_14_out[3], xor_14_out[4], xor_14_out[5], xor_14_out[6]);
  or or_19 (or_19_out[6], xor_15_out[0], xor_15_out[1], xor_15_out[2], xor_15_out[3], xor_15_out[4], xor_15_out[5], xor_15_out[6]);
  or or_20 (or_20_out[6], xor_16_out[0], xor_16_out[1], xor_16_out[2], xor_16_out[3], xor_16_out[4], xor_16_out[5], xor_16_out[6]);
  or or_21 (or_21_out[6], xor_17_out[0], xor_17_out[1], xor_17_out[2], xor_17_out[3], xor_17_out[4], xor_17_out[5], xor_17_out[6]);
  assign and_17_out = {7{or_8_out[6]}} & and_9_out;  // And and_17, 7 bits wide
  assign and_18_out = {7{or_9_out[6]}} & or_1_out;  // And and_18, 7 bits wide
  assign and_19_out = {7{or_10_out[6]}} & and_10_out;  // And and_19, 7 bits wide
  assign and_20_out = {7{or_11_out[6]}} & or_2_out;  // And and_20, 7 bits wide
  assign and_21_out = {7{or_12_out[6]}} & and_11_out;  // And and_21, 7 bits wide
  assign and_22_out = {7{or_13_out[6]}} & or_3_out;  // And and_22, 7 bits wide
  assign and_23_out = {7{or_14_out[6]}} & and_12_out;  // And and_23, 7 bits wide
  assign and_24_out = {7{or_15_out[6]}} & or_4_out;  // And and_24, 7 bits wide
  assign and_25_out = {7{or_16_out[6]}} & and_13_out;  // And and_25, 7 bits wide
  assign and_26_out = {7{or_17_out[6]}} & or_5_out;  // And and_26, 7 bits wide
  assign and_27_out = {7{or_18_out[6]}} & and_14_out;  // And and_27, 7 bits wide
  assign and_28_out = {7{or_19_out[6]}} & or_6_out;  // And and_28, 7 bits wide
  assign and_29_out = {7{or_20_out[6]}} & and_15_out;  // And and_29, 7 bits wide
  assign and_30_out = {7{or_21_out[6]}} & or_7_out;  // And and_30, 7 bits wide
  assign or_22_out = and_17_out | and_18_out;  // Or or_22, 7 bits wide
  assign or_23_out = and_19_out | and_20_out;  // Or or_23, 7 bits wide
  assign or_24_out = and_21_out | and_22_out;  // Or or_24, 7 bits wide
  assign and_31_out = or_22_out & {7{and_2_out[6]}};  // And and_31, 7 bits wide
  assign and_32_out = or_23_out & {7{and_3_out[6]}};  // And and_32, 7 bits wide
  assign and_33_out = or_24_out & {7{and_4_out[6]}};  // And and_33, 7 bits wide
  assign or_25_out = and_23_out | and_24_out;  // Or or_25, 7 bits wide
  assign or_26_out = and_25_out | and_26_out;  // Or or_26, 7 bits wide
  assign and_34_out = or_25_out & {7{and_5_out[6]}};  // And and_34, 7 bits wide
  assign and_35_out = or_26_out & {7{and_6_out[6]}};  // And and_35, 7 bits wide
  assign or_27_out = and_27_out | and_28_out;  // Or or_27, 7 bits wide
  assign or_28_out = and_29_out | and_30_out;  // Or or_28, 7 bits wide
  assign and_36_out = or_27_out & {7{and_7_out[6]}};  // And and_36, 7 bits wide
  assign and_37_out = or_28_out & {7{and_8_out[6]}};  // And and_37, 7 bits wide
  assign Output = and_16_out | and_31_out | and_32_out | and_33_out | and_34_out | and_35_out | and_36_out | and_37_out;  // Or or_29, 7 bits wide

  assign out_3[5:0] = {6{1'b0}};

  // Other names for the same wires on the sheet: _0000_001[0] = out_3[6]; _0000_010[1] = out_3[6];
  //   _0000_100[2] = out_3[6]; _0001_000[3] = out_3[6]; _0010_000[4] = out_3[6]; _0100_000[5] = out_3[6];
  //   _1000_000[6] = out_3[6]; input[6:0] = In; m4 = In[0]; m3 = In[1]; m2 = In[2]; p3 = In[3]; m1 = In[4];
  //   p2 = In[5]; p1 = In[6]; out[6:0] = Output
endmodule
