// Digital circuit Template.dig as structural Verilog
module Template (
  input  T,
  input  Clear,
  input  Clock,
  output Q,
  output Q_2
);

  wire and_2_out, and_3_out, and_4_out, and_5_out, clear_t, nor_1_out, nor_2_out, nor_3_out, nor_4_out,
       nor_5_out, nor_6_out, not_1_out;

  and and_1 (clear_t, Clock, Clear);
  nor nor_1 (nor_1_out, nor_4_out, nor_2_out);
  nor nor_2 (nor_2_out, nor_1_out, Clock);
  nor nor_3 (nor_3_out, nor_2_out, Clock, nor_4_out);
  nor nor_4 (nor_4_out, nor_3_out, T);
  and and_2 (and_2_out, Q_2, nor_3_out);
  and and_3 (and_3_out, nor_3_out, Q);
  not not_1 (not_1_out, nor_3_out);
  nor nor_5 (nor_5_out, and_2_out, nor_6_out);
  nor nor_6 (nor_6_out, nor_5_out, clear_t, and_3_out);
  and and_4 (and_4_out, not_1_out, nor_5_out);
  and and_5 (and_5_out, nor_6_out, not_1_out);
  nor nor_7 (Q, and_4_out, Q_2);
  nor nor_8 (Q_2, Q, and_5_out);
endmodule
