// Digital circuit gcd_template.dig as structural Verilog
module gcd_template (
  input  [7:0] A,
  input  [7:0] B,
  input  start,
  input  clear,
  input  clk,
  output busy,
  output [7:0] \output 
);

  wire and_1_out, and_3_out, d_ff_1_nq, driverinvsel_1_out, not_1_out, or_1_out, or_2_out, or_3_out, t_ff_1_q;
  wire [7:0] div_1_r, multiplexer_1_out, multiplexer_2_out, register_1_q, register_2_q;

  and and_1 (and_1_out, start, not_1_out);
  or or_1 (or_1_out, driverinvsel_1_out, and_1_out);
  T_FF t_ff_1 (.T(1'b1), .C(or_1_out), .Q(t_ff_1_q));  // open: nQ
  not not_1 (not_1_out, busy);
  assign driverinvsel_1_out = ~busy ? t_ff_1_q : 1'bz;  // DriverInvSel driverinvsel_1
  Multiplexer #(.Bits(8)) multiplexer_1 (.sel(busy), .in_0(A), .in_1(register_2_q), .out(multiplexer_1_out));
  Multiplexer #(.Bits(8)) multiplexer_2 (.sel(busy), .in_0(B), .in_1(div_1_r), .out(multiplexer_2_out));
  or or_2 (or_2_out, or_3_out, d_ff_1_nq);
  Register #(.Bits(8)) register_1 (.D(multiplexer_1_out), .C(clk), .en(1'b1), .Q(register_1_q));
  Register #(.Bits(8)) register_2 (.D(multiplexer_2_out), .C(clk), .en(1'b1), .Q(register_2_q));
  and and_2 (busy, driverinvsel_1_out, or_2_out);
  Div #(.Bits(8)) div_1 (.a(register_1_q), .b(register_2_q), .r(div_1_r));  // open: q
  D_FF d_ff_1 (.D(busy), .C(clk), .nQ(d_ff_1_nq));  // open: Q
  or or_3 (or_3_out, div_1_r[0], div_1_r[1], div_1_r[2], div_1_r[3], div_1_r[4], div_1_r[5], div_1_r[6], div_1_r[7]);
  and and_3 (and_3_out, ~or_3_out, ~busy);  // And
  Register #(.Bits(8)) register_3 (.D(register_2_q), .C(clk), .en(and_3_out), .Q(\output ));
  Seven_Seg_Hex seven_seg_hex_1 (.d(\output [7:4]), .dp(1'b0));
  Seven_Seg_Hex seven_seg_hex_2 (.d(\output [3:0]), .dp(1'b0));
endmodule
