// Digital circuit gcd_template2.dig as structural Verilog
module gcd_template2 (
  input  [7:0] A,
  input  [7:0] B,
  input  start,
  input  clear,
  input  clk,
  output busy,
  output [7:0] \output 
);

  wire and_1_out, and_2_out, and_3_out, and_4_out, comparator_1_eq, d_ff_1_nq, d_ff_2_nq, d_ff_2_q,
       driverinvsel_1_out;
  wire [7:0] a_t, and_5_out, and_6_out, and_7_out, and_8_out, b_t, multiplexer_1_out, multiplexer_2_out,
       register_1_q, register_2_q, sub_1_s, sub_2_s;
  wire [7:7] comparator_1_gt, comparator_1_lt;

  Multiplexer #(.Bits(8)) multiplexer_1 (.sel(busy), .in_0(A), .in_1(a_t), .out(multiplexer_1_out));
  Multiplexer #(.Bits(8)) multiplexer_2 (.sel(busy), .in_0(B), .in_1(b_t), .out(multiplexer_2_out));
  D_FF d_ff_1 (.D(start), .C(clk), .nQ(d_ff_1_nq));  // open: Q
  Register #(.Bits(8)) register_1 (.D(multiplexer_1_out), .C(clk), .en(1'b1), .Q(register_1_q));
  Register #(.Bits(8)) register_2 (.D(multiplexer_2_out), .C(clk), .en(1'b1), .Q(register_2_q));
  and and_1 (and_1_out, d_ff_1_nq, start);
  Comparator #(.Bits(8)) comparator_1 (
    .a(register_1_q), .b(register_2_q), .gt(comparator_1_gt[7]), .eq(comparator_1_eq), .lt(comparator_1_lt[7]));
  assign driverinvsel_1_out = ~busy ? and_1_out : 1'bz;  // DriverInvSel driverinvsel_1
  and and_2 (and_2_out, d_ff_2_q, ~clear, ~comparator_1_eq);  // And
  and and_3 (and_3_out, ~clear, driverinvsel_1_out, ~comparator_1_eq);  // And
  and and_4 (and_4_out, driverinvsel_1_out, ~clear, d_ff_2_nq);  // And
  or or_1 (busy, and_2_out, and_3_out, and_4_out);
  Sub #(.Bits(8)) sub_1 (.a(register_1_q), .b(register_2_q), .c_i(1'b0), .s(sub_1_s));  // open: c_o
  Sub #(.Bits(8)) sub_2 (.a(register_2_q), .b(register_1_q), .c_i(1'b0), .s(sub_2_s));  // open: c_o
  assign b_t = and_5_out | and_6_out;  // Or or_2, 8 bits wide
  assign and_5_out = register_2_q & {8{comparator_1_gt[7]}};  // And and_5, 8 bits wide
  D_FF d_ff_2 (.D(busy), .C(clk), .Q(d_ff_2_q), .nQ(d_ff_2_nq));
  assign and_6_out = {8{comparator_1_lt[7]}} & register_1_q;  // And and_6, 8 bits wide
  assign and_7_out = sub_1_s & {8{comparator_1_gt[7]}};  // And and_7, 8 bits wide
  assign and_8_out = {8{comparator_1_lt[7]}} & sub_2_s;  // And and_8, 8 bits wide
  assign a_t = and_7_out | and_8_out;  // Or or_3, 8 bits wide
  Register #(.Bits(8)) register_3 (.D(register_2_q), .C(clk), .en(comparator_1_eq), .Q(\output ));
endmodule
