// Digital circuit template.dig as structural Verilog
module template (
  input  reset,
  input  clk,
  output A,
  output B,
  output C
);

  wire and_1_out, and_2_out, and_3_out, and_4_out, d_ff_1_nq, d_ff_2_nq, d_ff_3_nq, not_1_out, or_1_out;

  not not_1 (not_1_out, reset);
  and and_1 (and_1_out, C, not_1_out);
  D_FF d_ff_1 (.D(and_1_out), .C(clk), .Q(A), .nQ(d_ff_1_nq));
  and and_2 (and_2_out, d_ff_2_nq, not_1_out);
  and and_3 (and_3_out, d_ff_1_nq, d_ff_3_nq, not_1_out);
  or or_1 (or_1_out, and_2_out, and_3_out);
  D_FF d_ff_2 (.D(or_1_out), .C(clk), .Q(B), .nQ(d_ff_2_nq));
  and and_4 (and_4_out, d_ff_1_nq, B, not_1_out);
  D_FF d_ff_3 (.D(and_4_out), .C(clk), .Q(C), .nQ(d_ff_3_nq));
endmodule
