// Digital circuit 01.dig as structural Verilog
module _01 (
  input  [3:0] in,
  output out
);

  wire demultiplexer_1_out_1, demultiplexer_1_out_3, demultiplexer_1_out_4, demultiplexer_1_out_5,
       demultiplexer_1_out_9, demultiplexer_1_out_10, demultiplexer_1_out_13, demultiplexer_1_out_14;

  Demultiplexer #(.Selector_Bits(4)) demultiplexer_1 (
    .sel(in), .in(1'b1), .out_1(demultiplexer_1_out_1), .out_3(demultiplexer_1_out_3),
    .out_4(demultiplexer_1_out_4), .out_5(demultiplexer_1_out_5), .out_9(demultiplexer_1_out_9),
    .out_10(demultiplexer_1_out_10), .out_13(demultiplexer_1_out_13), .out_14(demultiplexer_1_out_14));  // open: out_0, out_2, out_6, out_7, out_8, out_11, out_12, out_15
  or or_1 (out, demultiplexer_1_out_1, demultiplexer_1_out_3, demultiplexer_1_out_4, demultiplexer_1_out_5, demultiplexer_1_out_9, demultiplexer_1_out_10, demultiplexer_1_out_13, demultiplexer_1_out_14);
endmodule
