// Digital circuit 02.dig as structural Verilog
module _02 (
  input  [2:0] in0,
  input  [2:0] in1,
  input  addsubtract,
  output [2:0] out
);

  wire [2:0] add, multiplexer_1_out, multiplexer_2_out, multiplexer_3_out, multiplexer_4_out, sub;

  Multiplexer #(.Selector_Bits(3), .Bits(3)) multiplexer_1 (
    .sel(in0), .in_0(3'b000), .in_1(3'b001), .in_2(3'b001), .in_3(3'b010), .in_4(3'b001), .in_5(3'b010),
    .in_6(3'b010), .in_7(3'b011), .out(multiplexer_1_out));
  Multiplexer #(.Selector_Bits(3), .Bits(3)) multiplexer_2 (
    .sel(in1), .in_0(3'b000), .in_1(3'b001), .in_2(3'b001), .in_3(3'b010), .in_4(3'b001), .in_5(3'b010),
    .in_6(3'b010), .in_7(3'b011), .out(multiplexer_2_out));
  Multiplexer #(.Selector_Bits(3), .Bits(3)) multiplexer_3 (
    .sel(in0), .in_0(3'b000), .in_1(3'b001), .in_2(3'b001), .in_3(3'b010), .in_4(3'b001), .in_5(3'b010),
    .in_6(3'b010), .in_7(3'b011), .out(multiplexer_3_out));
  Multiplexer #(.Selector_Bits(3), .Bits(3)) multiplexer_4 (
    .sel(in1), .in_0(3'b000), .in_1(3'b001), .in_2(3'b001), .in_3(3'b010), .in_4(3'b001), .in_5(3'b010),
    .in_6(3'b010), .in_7(3'b011), .out(multiplexer_4_out));
  LookUpTable #(.Bits(3)) lookuptable_1 (
    .in0(multiplexer_1_out[0]), .in1(multiplexer_1_out[1]), .in2(multiplexer_1_out[2]),
    .in3(multiplexer_2_out[0]), .in4(multiplexer_2_out[1]), .in5(multiplexer_2_out[2]), .out(add));
  LookUpTable #(.Bits(3)) lookuptable_2 (
    .in0(multiplexer_3_out[0]), .in1(multiplexer_3_out[1]), .in2(multiplexer_3_out[2]),
    .in3(multiplexer_4_out[0]), .in4(multiplexer_4_out[1]), .in5(multiplexer_4_out[2]), .out(sub));
  Multiplexer #(.Bits(3)) multiplexer_5 (.sel(addsubtract), .in_0(add), .in_1(sub), .out(out));

  // Other names for the same wires on the sheet: input0[2:0] = in0; input1[2:0] = in1

  // Notes on the sheet:
  //   contents of lookuptable_1 (hex, n*v repeats v):
  //   0,1,2,3,4*0,1,2,3,4,4*0,2,3,4,5,4*0,3,4,5,6
  //   contents of lookuptable_2 (hex, n*v repeats v):
  //   0,1,2,3,6*0,1,2,7*0,1
endmodule
