// Digital circuit 1.dig as structural Verilog
module _1 (
  input  reset,
  input  clk,
  output C,
  output B,
  output A
);

  wire multiplexer_1_out, multiplexer_2_out, multiplexer_3_out;

  Multiplexer #(.Selector_Bits(3)) multiplexer_1 (
    .sel({C, B, A}), .in_0(1'b0), .in_1(1'b0), .in_2(1'b1), .in_3(1'b0), .in_4(1'b0), .in_5(1'b1),
    .in_6(1'b1), .in_7(1'b1), .out(multiplexer_1_out));
  Multiplexer #(.Selector_Bits(3)) multiplexer_2 (
    .sel({C, B, A}), .in_0(1'b0), .in_1(1'b1), .in_2(1'b1), .in_3(1'b1), .in_4(1'b0), .in_5(1'b0),
    .in_6(1'b1), .in_7(1'b0), .out(multiplexer_2_out));
  Multiplexer #(.Selector_Bits(3)) multiplexer_3 (
    .sel({C, B, A}), .in_0(1'b1), .in_1(1'b1), .in_2(1'b0), .in_3(1'b0), .in_4(1'b0), .in_5(1'b0),
    .in_6(1'b1), .in_7(1'b1), .out(multiplexer_3_out));
  D_FF_AS d_ff_as_1 (.Set(1'b0), .D(multiplexer_1_out), .C(clk), .Clr(reset), .Q(C));  // open: nQ
  D_FF_AS d_ff_as_2 (.Set(1'b0), .D(multiplexer_2_out), .C(clk), .Clr(reset), .Q(B));  // open: nQ
  D_FF_AS d_ff_as_3 (.Set(1'b0), .D(multiplexer_3_out), .C(clk), .Clr(reset), .Q(A));  // open: nQ
  // Probe state on {A, B, C}
endmodule
