// Digital circuit 2.dig as structural Verilog
module _2 (
  input  [15:0] A,
  input  clk,
  input  \input ,
  output [7:0] sqrt,
  output busy
);

  wire i___i__gt__A, multiplexer_1_out, not_1_out, not_2_out, Q1, s1;
  wire [15:0] i;
  wire [15:8] register_1_q;
  wire [31:0] mul_1_mul;

  Decoder decoder_1 (.sel(Q1), .out_0(s1), .out_1(busy));
  Multiplexer multiplexer_1 (.sel(Q1), .in_0(\input ), .in_1(not_1_out), .out(multiplexer_1_out));
  not not_1 (not_1_out, i___i__gt__A);
  D_FF d_ff_1 (.D(multiplexer_1_out), .C(clk), .Q(Q1));  // open: nQ
  Counter #(.Bits(16)) counter_1 (.en(busy), .C(clk), .clr(\input ), .out(i));  // open: ovf
  Mul #(.Bits(16)) mul_1 (.a(i), .b(i), .mul(mul_1_mul));
  Register #(.Bits(16)) register_1 (.D(i), .C(clk), .en(not_2_out), .Q({register_1_q, sqrt}));
  not not_2 (not_2_out, i___i__gt__A);
  Comparator #(.Bits(32)) comparator_1 (.a(mul_1_mul), .b({{16{1'b0}}, A}), .gt(i___i__gt__A));  // open: eq, lt

  // Other names for the same wires on the sheet: s2 = busy
endmodule
