// Digital circuit 3.dig as structural Verilog
module _3 (
  input  [15:0] A,
  input  reset,
  input  clk,
  input  \input ,
  output [15:0] mean,
  output busy
);

  wire CalSum, clearCounter, \initial , load___sum, multiplexer_1_out, Q1;
  wire [15:0] a_t;
  wire [31:0] add_1_s, multiplexer_2_out, n, sum;
  wire [31:16] div_1_q;

  Decoder decoder_1 (.sel(Q1), .out_0(\initial ), .out_1(CalSum));
  Add #(.Bits(32)) add_1 (.a(sum), .b({{16{1'b0}}, a_t}), .c_i(1'b0), .s(add_1_s));  // open: c_o
  Counter #(.Bits(32)) counter_1 (.en(\input ), .C(clk), .clr(clearCounter), .out(n));  // open: ovf
  Register #(.Bits(16)) register_1 (.D(A), .C(\input ), .en(1'b1), .Q(a_t));
  Multiplexer multiplexer_1 (.sel(Q1), .in_0(1'b1), .in_1(1'b1), .out(multiplexer_1_out));
  Multiplexer #(.Bits(32)) multiplexer_2 (.sel(\initial ), .in_0(add_1_s), .in_1({32{1'b0}}), .out(multiplexer_2_out));
  Div #(.Bits(32)) div_1 (.a(sum), .b(n), .q({div_1_q, mean}));  // open: r
  D_FF_AS d_ff_as_1 (.Set(1'b0), .D(multiplexer_1_out), .C(clk), .Clr(reset), .Q(Q1));  // open: nQ
  or or_1 (load___sum, \initial , \input );
  Register #(.Bits(32)) u_sum (.D(multiplexer_2_out), .C(clk), .en(load___sum), .Q(sum));
  or or_2 (clearCounter, \initial , reset);

  assign busy = 1'b0;
endmodule
